// Logisim project project_1.circ as structural Verilog: 16 circuits, main circuit main
module main (
  input  in_1,
  input  in_2,
  input  in_3,
  input  in_4,
  input  in_5,
  input  in_6,
  input  in_7,
  input  in_8,
  input  in_9,
  input  in_10,
  input  in_11,
  input  in_12,
  input  Address,
  input  in_14,
  input  in_15,
  input  in_16,
  input  in_17,
  input  in_18,
  input  in_19,
  input  in_20,
  input  in_21,
  input  in_22,
  input  in_23,
  input  in_24,
  input  in_25,
  input  in_26,
  input  in_27,
  input  in_28,
  input  in_29,
  input  in_30,
  input  in_31,
  input  in_32,
  input  in_33,
  output out_34,
  output out_35,
  output out_36,
  output out_37,
  output out_38,
  output out_39,
  output out_40,
  output out_41,
  output out_42,
  output out_43,
  output out_44,
  output out_45,
  output out_46,
  output out_47,
  output out_48,
  output out_49
);

  wire and_1_out, and_2_out, and_3_out, and_7_out, and_9_out, and_10_out, bcd_to_seven_segment_display_1_a,
       bcd_to_seven_segment_display_1_b, bcd_to_seven_segment_display_1_c, bcd_to_seven_segment_display_1_d,
       bcd_to_seven_segment_display_1_e, bcd_to_seven_segment_display_1_f, bcd_to_seven_segment_display_1_g,
       bcd_to_seven_segment_display_2_a, bcd_to_seven_segment_display_2_b, bcd_to_seven_segment_display_2_c,
       bcd_to_seven_segment_display_2_d, bcd_to_seven_segment_display_2_e, bcd_to_seven_segment_display_2_f,
       bcd_to_seven_segment_display_2_g, bcd_to_seven_segment_display_3_a, bcd_to_seven_segment_display_3_b,
       bcd_to_seven_segment_display_3_c, bcd_to_seven_segment_display_3_d, bcd_to_seven_segment_display_3_e,
       bcd_to_seven_segment_display_3_f, bcd_to_seven_segment_display_3_g, bcd_to_seven_segment_display_4_a,
       bcd_to_seven_segment_display_4_b, bcd_to_seven_segment_display_4_c, bcd_to_seven_segment_display_4_d,
       bcd_to_seven_segment_display_4_e, bcd_to_seven_segment_display_4_f, bcd_to_seven_segment_display_4_g,
       bcd_to_seven_segment_display_5_a, bcd_to_seven_segment_display_5_b, bcd_to_seven_segment_display_5_c,
       bcd_to_seven_segment_display_5_d, bcd_to_seven_segment_display_5_e, bcd_to_seven_segment_display_5_f,
       bcd_to_seven_segment_display_5_g, bcd_to_seven_segment_display_6_a, bcd_to_seven_segment_display_6_b,
       bcd_to_seven_segment_display_6_c, bcd_to_seven_segment_display_6_d, bcd_to_seven_segment_display_6_e,
       bcd_to_seven_segment_display_6_f, bcd_to_seven_segment_display_6_g, buffer_1_out, buffer_2_out,
       button_1_out, clock_1_out, controlled_buffer_1_out, controlled_buffer_2_out, controlled_buffer_3_out,
       controlled_buffer_4_out, controlled_buffer_5_out, controlled_buffer_6_out, controlled_buffer_7_out,
       controlled_buffer_8_out, eight_bit_to_bcd_1_h0, eight_bit_to_bcd_1_h1, eight_bit_to_bcd_1_o0,
       eight_bit_to_bcd_1_o1, eight_bit_to_bcd_1_o2, eight_bit_to_bcd_1_o3, eight_bit_to_bcd_1_t0,
       eight_bit_to_bcd_1_t1, eight_bit_to_bcd_1_t2, eight_bit_to_bcd_1_t3, eight_bit_to_bcd_2_h0,
       eight_bit_to_bcd_2_h1, eight_bit_to_bcd_2_o0, eight_bit_to_bcd_2_o1, eight_bit_to_bcd_2_o2,
       eight_bit_to_bcd_2_o3, eight_bit_to_bcd_2_t0, eight_bit_to_bcd_2_t1, eight_bit_to_bcd_2_t2,
       eight_bit_to_bcd_2_t3, nor_1_out, nor_2_out, nor_3_out, nor_4_out, not_1_out, not_2_out, not_3_out,
       not_4_out, not_5_out, undriven, undriven_2, undriven_3, undriven_4, undriven_5, undriven_6,
       undriven_7, undriven_8;

  Eight_Bit_to_BCD eight_bit_to_bcd_1 (
    .B7(in_1), .B6(in_2), .B5(in_3), .B4(in_4), .B3(in_5), .B2(in_6), .B1(in_7), .B0(in_8),
    .H1(eight_bit_to_bcd_1_h1), .H0(eight_bit_to_bcd_1_h0), .T3(eight_bit_to_bcd_1_t3),
    .T2(eight_bit_to_bcd_1_t2), .T1(eight_bit_to_bcd_1_t1), .T0(eight_bit_to_bcd_1_t0),
    .O3(eight_bit_to_bcd_1_o3), .O2(eight_bit_to_bcd_1_o2), .O1(eight_bit_to_bcd_1_o1),
    .O0(eight_bit_to_bcd_1_o0));
  BCD_To_Seven_Segment_Display bcd_to_seven_segment_display_1 (
    .B3_A(1'b0), .B2_B(1'b0), .B1_C(eight_bit_to_bcd_1_h1), .B0_D(eight_bit_to_bcd_1_h0),
    .g(bcd_to_seven_segment_display_1_g), .f(bcd_to_seven_segment_display_1_f),
    .e(bcd_to_seven_segment_display_1_e), .d(bcd_to_seven_segment_display_1_d),
    .c(bcd_to_seven_segment_display_1_c), .b(bcd_to_seven_segment_display_1_b),
    .a(bcd_to_seven_segment_display_1_a));
  BCD_To_Seven_Segment_Display bcd_to_seven_segment_display_2 (
    .B3_A(eight_bit_to_bcd_1_t3), .B2_B(eight_bit_to_bcd_1_t2), .B1_C(eight_bit_to_bcd_1_t1),
    .B0_D(eight_bit_to_bcd_1_t0), .g(bcd_to_seven_segment_display_2_g), .f(bcd_to_seven_segment_display_2_f),
    .e(bcd_to_seven_segment_display_2_e), .d(bcd_to_seven_segment_display_2_d),
    .c(bcd_to_seven_segment_display_2_c), .b(bcd_to_seven_segment_display_2_b),
    .a(bcd_to_seven_segment_display_2_a));
  BCD_To_Seven_Segment_Display bcd_to_seven_segment_display_3 (
    .B3_A(eight_bit_to_bcd_1_o3), .B2_B(eight_bit_to_bcd_1_o2), .B1_C(eight_bit_to_bcd_1_o1),
    .B0_D(eight_bit_to_bcd_1_o0), .g(bcd_to_seven_segment_display_3_g), .f(bcd_to_seven_segment_display_3_f),
    .e(bcd_to_seven_segment_display_3_e), .d(bcd_to_seven_segment_display_3_d),
    .c(bcd_to_seven_segment_display_3_c), .b(bcd_to_seven_segment_display_3_b),
    .a(bcd_to_seven_segment_display_3_a));
  _7_Segment_Display u_7_segment_display_1 (
    .g(bcd_to_seven_segment_display_1_g), .f(bcd_to_seven_segment_display_1_f),
    .a(bcd_to_seven_segment_display_1_a), .b(bcd_to_seven_segment_display_1_b),
    .e(bcd_to_seven_segment_display_1_e), .d(bcd_to_seven_segment_display_1_d),
    .c(bcd_to_seven_segment_display_1_c), .dp(1'b0));
  _7_Segment_Display u_7_segment_display_2 (
    .g(bcd_to_seven_segment_display_2_g), .f(bcd_to_seven_segment_display_2_f),
    .a(bcd_to_seven_segment_display_2_a), .b(bcd_to_seven_segment_display_2_b),
    .e(bcd_to_seven_segment_display_2_e), .d(bcd_to_seven_segment_display_2_d),
    .c(bcd_to_seven_segment_display_2_c), .dp(1'b0));
  _7_Segment_Display u_7_segment_display_3 (
    .g(bcd_to_seven_segment_display_3_g), .f(bcd_to_seven_segment_display_3_f),
    .a(bcd_to_seven_segment_display_3_a), .b(bcd_to_seven_segment_display_3_b),
    .e(bcd_to_seven_segment_display_3_e), .d(bcd_to_seven_segment_display_3_d),
    .c(bcd_to_seven_segment_display_3_c), .dp(1'b0));
  Clock clock_1 (.out(clock_1_out));
  not not_1 (not_1_out, clock_1_out);
  and and_1 (and_1_out, clock_1_out, buffer_1_out);
  buf buffer_1 (buffer_1_out, not_1_out);
  not not_2 (not_2_out, nor_1_out);
  and and_2 (and_2_out, nor_1_out, 1'b1, and_1_out);
  and and_3 (and_3_out, and_1_out, 1'b1, nor_2_out);
  // AND_Gate and_4 has open pins: in0=not_2_out, in1=not_4_out, out=open
  nor nor_1 (nor_1_out, and_2_out, nor_2_out);
  nor nor_2 (nor_2_out, nor_1_out, and_3_out);
  // AND_Gate and_5 has open pins: in0=nor_1_out, in1=not_4_out, out=open
  not not_3 (not_3_out, nor_2_out);
  // AND_Gate and_6 has open pins: in0=nor_3_out, in1=not_2_out, out=open
  and and_7 (and_7_out, nor_2_out, buffer_2_out);
  buf buffer_2 (buffer_2_out, not_3_out);
  // AND_Gate and_8 has open pins: in0=nor_1_out, in1=nor_3_out, out=open
  not not_4 (not_4_out, nor_3_out);
  and and_9 (and_9_out, nor_3_out, 1'b1, and_7_out);
  and and_10 (and_10_out, and_7_out, 1'b1, nor_4_out);
  nor nor_3 (nor_3_out, and_9_out, nor_4_out);
  nor nor_4 (nor_4_out, nor_3_out, and_10_out);
  assign controlled_buffer_1_out = in_9 ? undriven : 1'bz;  // Controlled_Buffer controlled_buffer_1
  assign controlled_buffer_2_out = in_9 ? undriven_2 : 1'bz;  // Controlled_Buffer controlled_buffer_2
  assign controlled_buffer_3_out = in_9 ? undriven_3 : 1'bz;  // Controlled_Buffer controlled_buffer_3
  assign controlled_buffer_4_out = in_9 ? undriven_4 : 1'bz;  // Controlled_Buffer controlled_buffer_4
  assign controlled_buffer_5_out = in_9 ? undriven_5 : 1'bz;  // Controlled_Buffer controlled_buffer_5
  assign controlled_buffer_6_out = in_9 ? undriven_6 : 1'bz;  // Controlled_Buffer controlled_buffer_6
  assign controlled_buffer_7_out = in_9 ? undriven_7 : 1'bz;  // Controlled_Buffer controlled_buffer_7
  assign controlled_buffer_8_out = in_9 ? undriven_8 : 1'bz;  // Controlled_Buffer controlled_buffer_8
  assign controlled_buffer_6_out = not_5_out ? in_12 : 1'bz;  // Controlled_Buffer controlled_buffer_9
  assign controlled_buffer_7_out = not_5_out ? in_11 : 1'bz;  // Controlled_Buffer controlled_buffer_10
  assign controlled_buffer_8_out = not_5_out ? in_10 : 1'bz;  // Controlled_Buffer controlled_buffer_11
  assign controlled_buffer_2_out = not_5_out ? in_16 : 1'bz;  // Controlled_Buffer controlled_buffer_12
  assign controlled_buffer_3_out = not_5_out ? in_15 : 1'bz;  // Controlled_Buffer controlled_buffer_13
  assign controlled_buffer_4_out = not_5_out ? in_14 : 1'bz;  // Controlled_Buffer controlled_buffer_14
  assign controlled_buffer_5_out = not_5_out ? Address : 1'bz;  // Controlled_Buffer controlled_buffer_15
  not not_5 (not_5_out, in_9);
  assign controlled_buffer_1_out = not_5_out ? in_17 : 1'bz;  // Controlled_Buffer controlled_buffer_16
  Memory_256_Bit memory_256_bit_1 (
    .A2(controlled_buffer_3_out), .A1(controlled_buffer_2_out), .A0(controlled_buffer_1_out),
    .Data_In(in_18), .A7(controlled_buffer_8_out), .Write_Enable(button_1_out), .A6(controlled_buffer_7_out),
    .A5(controlled_buffer_6_out), .A4(controlled_buffer_5_out), .Read_Enable(1'b1),
    .A3(controlled_buffer_4_out), .Data_Out(out_34));
  Memory_256_Bit memory_256_bit_2 (
    .A2(controlled_buffer_3_out), .A1(controlled_buffer_2_out), .A0(controlled_buffer_1_out),
    .Data_In(in_19), .A7(controlled_buffer_8_out), .Write_Enable(button_1_out), .A6(controlled_buffer_7_out),
    .A5(controlled_buffer_6_out), .A4(controlled_buffer_5_out), .Read_Enable(1'b1),
    .A3(controlled_buffer_4_out), .Data_Out(out_35));
  Memory_256_Bit memory_256_bit_3 (
    .A2(controlled_buffer_3_out), .A1(controlled_buffer_2_out), .A0(controlled_buffer_1_out),
    .Data_In(in_20), .A7(controlled_buffer_8_out), .Write_Enable(button_1_out), .A6(controlled_buffer_7_out),
    .A5(controlled_buffer_6_out), .A4(controlled_buffer_5_out), .Read_Enable(1'b1),
    .A3(controlled_buffer_4_out), .Data_Out(out_36));
  Memory_256_Bit memory_256_bit_4 (
    .A2(controlled_buffer_3_out), .A1(controlled_buffer_2_out), .A0(controlled_buffer_1_out),
    .Data_In(in_21), .A7(controlled_buffer_8_out), .Write_Enable(button_1_out), .A6(controlled_buffer_7_out),
    .A5(controlled_buffer_6_out), .A4(controlled_buffer_5_out), .Read_Enable(1'b1),
    .A3(controlled_buffer_4_out), .Data_Out(out_37));
  Memory_256_Bit memory_256_bit_5 (
    .A2(controlled_buffer_3_out), .A1(controlled_buffer_2_out), .A0(controlled_buffer_1_out),
    .Data_In(in_22), .A7(controlled_buffer_8_out), .Write_Enable(button_1_out), .A6(controlled_buffer_7_out),
    .A5(controlled_buffer_6_out), .A4(controlled_buffer_5_out), .Read_Enable(1'b1),
    .A3(controlled_buffer_4_out), .Data_Out(out_38));
  Memory_256_Bit memory_256_bit_6 (
    .A2(controlled_buffer_3_out), .A1(controlled_buffer_2_out), .A0(controlled_buffer_1_out),
    .Data_In(in_23), .A7(controlled_buffer_8_out), .Write_Enable(button_1_out), .A6(controlled_buffer_7_out),
    .A5(controlled_buffer_6_out), .A4(controlled_buffer_5_out), .Read_Enable(1'b1),
    .A3(controlled_buffer_4_out), .Data_Out(out_39));
  Memory_256_Bit memory_256_bit_7 (
    .A2(controlled_buffer_3_out), .A1(controlled_buffer_2_out), .A0(controlled_buffer_1_out),
    .Data_In(in_24), .A7(controlled_buffer_8_out), .Write_Enable(button_1_out), .A6(controlled_buffer_7_out),
    .A5(controlled_buffer_6_out), .A4(controlled_buffer_5_out), .Read_Enable(1'b1),
    .A3(controlled_buffer_4_out), .Data_Out(out_40));
  Memory_256_Bit memory_256_bit_8 (
    .A2(controlled_buffer_3_out), .A1(controlled_buffer_2_out), .A0(controlled_buffer_1_out),
    .Data_In(in_25), .A7(controlled_buffer_8_out), .Write_Enable(button_1_out), .A6(controlled_buffer_7_out),
    .A5(controlled_buffer_6_out), .A4(controlled_buffer_5_out), .Read_Enable(1'b1),
    .A3(controlled_buffer_4_out), .Data_Out(out_41));
  Memory_256_Bit memory_256_bit_9 (
    .A2(controlled_buffer_3_out), .A1(controlled_buffer_2_out), .A0(controlled_buffer_1_out),
    .Data_In(in_26), .A7(controlled_buffer_8_out), .Write_Enable(button_1_out), .A6(controlled_buffer_7_out),
    .A5(controlled_buffer_6_out), .A4(controlled_buffer_5_out), .Read_Enable(1'b1),
    .A3(controlled_buffer_4_out), .Data_Out(out_42));
  Memory_256_Bit memory_256_bit_10 (
    .A2(controlled_buffer_3_out), .A1(controlled_buffer_2_out), .A0(controlled_buffer_1_out),
    .Data_In(in_27), .A7(controlled_buffer_8_out), .Write_Enable(button_1_out), .A6(controlled_buffer_7_out),
    .A5(controlled_buffer_6_out), .A4(controlled_buffer_5_out), .Read_Enable(1'b1),
    .A3(controlled_buffer_4_out), .Data_Out(out_43));
  Memory_256_Bit memory_256_bit_11 (
    .A2(controlled_buffer_3_out), .A1(controlled_buffer_2_out), .A0(controlled_buffer_1_out),
    .Data_In(in_28), .A7(controlled_buffer_8_out), .Write_Enable(button_1_out), .A6(controlled_buffer_7_out),
    .A5(controlled_buffer_6_out), .A4(controlled_buffer_5_out), .Read_Enable(1'b1),
    .A3(controlled_buffer_4_out), .Data_Out(out_44));
  Memory_256_Bit memory_256_bit_12 (
    .A2(controlled_buffer_3_out), .A1(controlled_buffer_2_out), .A0(controlled_buffer_1_out),
    .Data_In(in_29), .A7(controlled_buffer_8_out), .Write_Enable(button_1_out), .A6(controlled_buffer_7_out),
    .A5(controlled_buffer_6_out), .A4(controlled_buffer_5_out), .Read_Enable(1'b1),
    .A3(controlled_buffer_4_out), .Data_Out(out_45));
  Memory_256_Bit memory_256_bit_13 (
    .A2(controlled_buffer_3_out), .A1(controlled_buffer_2_out), .A0(controlled_buffer_1_out),
    .Data_In(in_30), .A7(controlled_buffer_8_out), .Write_Enable(button_1_out), .A6(controlled_buffer_7_out),
    .A5(controlled_buffer_6_out), .A4(controlled_buffer_5_out), .Read_Enable(1'b1),
    .A3(controlled_buffer_4_out), .Data_Out(out_46));
  Memory_256_Bit memory_256_bit_14 (
    .A2(controlled_buffer_3_out), .A1(controlled_buffer_2_out), .A0(controlled_buffer_1_out),
    .Data_In(in_31), .A7(controlled_buffer_8_out), .Write_Enable(button_1_out), .A6(controlled_buffer_7_out),
    .A5(controlled_buffer_6_out), .A4(controlled_buffer_5_out), .Read_Enable(1'b1),
    .A3(controlled_buffer_4_out), .Data_Out(out_47));
  Memory_256_Bit memory_256_bit_15 (
    .A2(controlled_buffer_3_out), .A1(controlled_buffer_2_out), .A0(controlled_buffer_1_out),
    .Data_In(in_32), .A7(controlled_buffer_8_out), .Write_Enable(button_1_out), .A6(controlled_buffer_7_out),
    .A5(controlled_buffer_6_out), .A4(controlled_buffer_5_out), .Read_Enable(1'b1),
    .A3(controlled_buffer_4_out), .Data_Out(out_48));
  Memory_256_Bit memory_256_bit_16 (
    .A2(controlled_buffer_3_out), .A1(controlled_buffer_2_out), .A0(controlled_buffer_1_out),
    .Data_In(in_33), .A7(controlled_buffer_8_out), .Write_Enable(button_1_out), .A6(controlled_buffer_7_out),
    .A5(controlled_buffer_6_out), .A4(controlled_buffer_5_out), .Read_Enable(1'b1),
    .A3(controlled_buffer_4_out), .Data_Out(out_49));
  Button button_1 (.out(button_1_out));
  BCD_To_Seven_Segment_Display bcd_to_seven_segment_display_4 (
    .B3_A(1'b0), .B2_B(1'b0), .B1_C(eight_bit_to_bcd_2_h1), .B0_D(eight_bit_to_bcd_2_h0),
    .g(bcd_to_seven_segment_display_4_g), .f(bcd_to_seven_segment_display_4_f),
    .e(bcd_to_seven_segment_display_4_e), .d(bcd_to_seven_segment_display_4_d),
    .c(bcd_to_seven_segment_display_4_c), .b(bcd_to_seven_segment_display_4_b),
    .a(bcd_to_seven_segment_display_4_a));
  _7_Segment_Display u_7_segment_display_4 (
    .g(bcd_to_seven_segment_display_4_g), .f(bcd_to_seven_segment_display_4_f),
    .a(bcd_to_seven_segment_display_4_a), .b(bcd_to_seven_segment_display_4_b),
    .e(bcd_to_seven_segment_display_4_e), .d(bcd_to_seven_segment_display_4_d),
    .c(bcd_to_seven_segment_display_4_c), .dp(1'b0));
  _7_Segment_Display u_7_segment_display_5 (
    .g(bcd_to_seven_segment_display_5_g), .f(bcd_to_seven_segment_display_5_f),
    .a(bcd_to_seven_segment_display_5_a), .b(bcd_to_seven_segment_display_5_b),
    .e(bcd_to_seven_segment_display_5_e), .d(bcd_to_seven_segment_display_5_d),
    .c(bcd_to_seven_segment_display_5_c), .dp(1'b0));
  BCD_To_Seven_Segment_Display bcd_to_seven_segment_display_5 (
    .B3_A(eight_bit_to_bcd_2_t3), .B2_B(eight_bit_to_bcd_2_t2), .B1_C(eight_bit_to_bcd_2_t1),
    .B0_D(eight_bit_to_bcd_2_t0), .g(bcd_to_seven_segment_display_5_g), .f(bcd_to_seven_segment_display_5_f),
    .e(bcd_to_seven_segment_display_5_e), .d(bcd_to_seven_segment_display_5_d),
    .c(bcd_to_seven_segment_display_5_c), .b(bcd_to_seven_segment_display_5_b),
    .a(bcd_to_seven_segment_display_5_a));
  _7_Segment_Display u_7_segment_display_6 (
    .g(bcd_to_seven_segment_display_6_g), .f(bcd_to_seven_segment_display_6_f),
    .a(bcd_to_seven_segment_display_6_a), .b(bcd_to_seven_segment_display_6_b),
    .e(bcd_to_seven_segment_display_6_e), .d(bcd_to_seven_segment_display_6_d),
    .c(bcd_to_seven_segment_display_6_c), .dp(1'b0));
  BCD_To_Seven_Segment_Display bcd_to_seven_segment_display_6 (
    .B3_A(eight_bit_to_bcd_2_o3), .B2_B(eight_bit_to_bcd_2_o2), .B1_C(eight_bit_to_bcd_2_o1),
    .B0_D(eight_bit_to_bcd_2_o0), .g(bcd_to_seven_segment_display_6_g), .f(bcd_to_seven_segment_display_6_f),
    .e(bcd_to_seven_segment_display_6_e), .d(bcd_to_seven_segment_display_6_d),
    .c(bcd_to_seven_segment_display_6_c), .b(bcd_to_seven_segment_display_6_b),
    .a(bcd_to_seven_segment_display_6_a));
  Eight_Bit_to_BCD eight_bit_to_bcd_2 (
    .B7(in_10), .B6(in_11), .B5(in_12), .B4(Address), .B3(in_14), .B2(in_15), .B1(in_16), .B0(in_17),
    .H1(eight_bit_to_bcd_2_h1), .H0(eight_bit_to_bcd_2_h0), .T3(eight_bit_to_bcd_2_t3),
    .T2(eight_bit_to_bcd_2_t2), .T1(eight_bit_to_bcd_2_t1), .T0(eight_bit_to_bcd_2_t0),
    .O3(eight_bit_to_bcd_2_o3), .O2(eight_bit_to_bcd_2_o2), .O1(eight_bit_to_bcd_2_o1),
    .O0(eight_bit_to_bcd_2_o0));

  // Notes on the sheet:
  //   0 - Editting Instructions
  //   1 - Running program
  //   Instruction Writing
  //   Instruction Reading
  //   Write Instruction To Memory
  //   Instruction Index
endmodule

module Gated_Latch (
  input  Data_In,
  input  Write_Enable,
  output Data_Out
);

  wire and_1_out, and_2_out, not_1_out, not_2_out, or_1_out;

  not not_1 (not_1_out, Data_In);
  and and_1 (and_1_out, Write_Enable, Data_In);
  and and_2 (and_2_out, not_1_out, Write_Enable);
  or or_1 (or_1_out, Data_Out, and_1_out);
  not not_2 (not_2_out, and_2_out);
  and and_3 (Data_Out, or_1_out, not_2_out);
endmodule

module Binary_Decoder_4_to_16 (
  input  in_1,
  input  in_2,
  input  in_3,
  input  in_4,
  output out_5,
  output out_6,
  output out_7,
  output out_8,
  output out_9,
  output out_10,
  output out_11,
  output out_12,
  output out_13,
  output out_14,
  output out_15,
  output out_16,
  output out_17,
  output out_18,
  output out_19,
  output out_20
);

  wire not_1_out, not_2_out, not_3_out, not_4_out;

  not not_1 (not_1_out, in_1);
  not not_2 (not_2_out, in_2);
  not not_3 (not_3_out, in_3);
  not not_4 (not_4_out, in_4);
  and and_1 (out_5, not_1_out, not_2_out, not_3_out, not_4_out);
  and and_2 (out_6, not_1_out, not_2_out, not_3_out, in_4);
  and and_3 (out_7, not_1_out, not_2_out, in_3, not_4_out);
  and and_4 (out_8, not_1_out, not_2_out, in_3, in_4);
  and and_5 (out_9, not_1_out, in_2, not_3_out, not_4_out);
  and and_6 (out_10, not_1_out, in_2, not_3_out, in_4);
  and and_7 (out_11, not_1_out, in_2, in_3, not_4_out);
  and and_8 (out_12, not_1_out, in_2, in_3, in_4);
  and and_9 (out_13, in_1, not_2_out, not_3_out, not_4_out);
  and and_10 (out_14, in_1, not_2_out, not_3_out, in_4);
  and and_11 (out_15, in_1, not_2_out, in_3, not_4_out);
  and and_12 (out_16, in_1, not_2_out, in_3, in_4);
  and and_13 (out_17, in_1, in_2, not_3_out, not_4_out);
  and and_14 (out_18, in_1, in_2, not_3_out, in_4);
  and and_15 (out_19, in_1, in_2, in_3, not_4_out);
  and and_16 (out_20, in_1, in_2, in_3, in_4);
endmodule
module Memory_256_Bit (
  input  A3,
  input  A2,
  input  A1,
  input  A0,
  input  A7,
  input  A6,
  input  A5,
  input  A4,
  input  Data_In,
  input  Write_Enable,
  input  Read_Enable,
  output Data_Out
);

  wire and_1_out, and_2_out, and_3_out, and_4_out, and_5_out, and_6_out, and_7_out, and_8_out, and_9_out,
       and_10_out, and_11_out, and_12_out, and_13_out, and_14_out, and_15_out, and_16_out, and_17_out,
       and_18_out, and_19_out, and_20_out, and_21_out, and_22_out, and_23_out, and_24_out, and_25_out,
       and_26_out, and_27_out, and_28_out, and_29_out, and_30_out, and_31_out, and_32_out, and_33_out,
       and_34_out, and_35_out, and_36_out, and_37_out, and_38_out, and_39_out, and_40_out, and_41_out,
       and_42_out, and_43_out, and_44_out, and_45_out, and_46_out, and_47_out, and_48_out, and_49_out,
       and_50_out, and_51_out, and_52_out, and_53_out, and_54_out, and_55_out, and_56_out, and_57_out,
       and_58_out, and_59_out, and_60_out, and_61_out, and_62_out, and_63_out, and_64_out, and_65_out,
       and_66_out, and_67_out, and_68_out, and_69_out, and_70_out, and_71_out, and_72_out, and_73_out,
       and_74_out, and_75_out, and_76_out, and_77_out, and_78_out, and_79_out, and_80_out, and_81_out,
       and_82_out, and_83_out, and_84_out, and_85_out, and_86_out, and_87_out, and_88_out, and_89_out,
       and_90_out, and_91_out, and_92_out, and_93_out, and_94_out, and_95_out, and_96_out, and_97_out,
       and_98_out, and_99_out, and_100_out, and_101_out, and_102_out, and_103_out, and_104_out, and_105_out,
       and_106_out, and_107_out, and_108_out, and_109_out, and_110_out, and_111_out, and_112_out,
       and_113_out, and_114_out, and_115_out, and_116_out, and_117_out, and_118_out, and_119_out,
       and_120_out, and_121_out, and_122_out, and_123_out, and_124_out, and_125_out, and_126_out,
       and_127_out, and_128_out, and_129_out, and_130_out, and_131_out, and_132_out, and_133_out,
       and_134_out, and_135_out, and_136_out, and_137_out, and_138_out, and_139_out, and_140_out,
       and_141_out, and_142_out, and_143_out, and_144_out, and_145_out, and_146_out, and_147_out,
       and_148_out, and_149_out, and_150_out, and_151_out, and_152_out, and_153_out, and_154_out,
       and_155_out, and_156_out, and_157_out, and_158_out, and_159_out, and_160_out, and_161_out,
       and_162_out, and_163_out, and_164_out, and_165_out, and_166_out, and_167_out, and_168_out,
       and_169_out, and_170_out, and_171_out, and_172_out, and_173_out, and_174_out, and_175_out,
       and_176_out, and_177_out, and_178_out, and_179_out, and_180_out, and_181_out, and_182_out,
       and_183_out, and_184_out, and_185_out, and_186_out, and_187_out, and_188_out, and_189_out,
       and_190_out, and_191_out, and_192_out, and_193_out, and_194_out, and_195_out, and_196_out,
       and_197_out, and_198_out, and_199_out, and_200_out, and_201_out, and_202_out, and_203_out,
       and_204_out, and_205_out, and_206_out, and_207_out, and_208_out, and_209_out, and_210_out,
       and_211_out, and_212_out, and_213_out, and_214_out, and_215_out, and_216_out, and_217_out,
       and_218_out, and_219_out, and_220_out, and_221_out, and_222_out, and_223_out, and_224_out,
       and_225_out, and_226_out, and_227_out, and_228_out, and_229_out, and_230_out, and_231_out,
       and_232_out, and_233_out, and_234_out, and_235_out, and_236_out, and_237_out, and_238_out,
       and_239_out, and_240_out, and_241_out, and_242_out, and_243_out, and_244_out, and_245_out,
       and_246_out, and_247_out, and_248_out, and_249_out, and_250_out, and_251_out, and_252_out,
       and_253_out, and_254_out, and_255_out, and_256_out, and_257_out, and_258_out, and_259_out,
       and_260_out, and_261_out, and_262_out, and_263_out, and_264_out, and_265_out, and_266_out,
       and_267_out, and_268_out, and_269_out, and_270_out, and_271_out, and_272_out, and_273_out,
       and_274_out, and_275_out, and_276_out, and_277_out, and_278_out, and_279_out, and_280_out,
       and_281_out, and_282_out, and_283_out, and_284_out, and_285_out, and_286_out, and_287_out,
       and_288_out, and_289_out, and_290_out, and_291_out, and_292_out, and_293_out, and_294_out,
       and_295_out, and_296_out, and_297_out, and_298_out, and_299_out, and_300_out, and_301_out,
       and_302_out, and_303_out, and_304_out, and_305_out, and_306_out, and_307_out, and_308_out,
       and_309_out, and_310_out, and_311_out, and_312_out, and_313_out, and_314_out, and_315_out,
       and_316_out, and_317_out, and_318_out, and_319_out, and_320_out, and_321_out, and_322_out,
       and_323_out, and_324_out, and_325_out, and_326_out, and_327_out, and_328_out, and_329_out,
       and_330_out, and_331_out, and_332_out, and_333_out, and_334_out, and_335_out, and_336_out,
       and_337_out, and_338_out, and_339_out, and_340_out, and_341_out, and_342_out, and_343_out,
       and_344_out, and_345_out, and_346_out, and_347_out, and_348_out, and_349_out, and_350_out,
       and_351_out, and_352_out, and_353_out, and_354_out, and_355_out, and_356_out, and_357_out,
       and_358_out, and_359_out, and_360_out, and_361_out, and_362_out, and_363_out, and_364_out,
       and_365_out, and_366_out, and_367_out, and_368_out, and_369_out, and_370_out, and_371_out,
       and_372_out, and_373_out, and_374_out, and_375_out, and_376_out, and_377_out, and_378_out,
       and_379_out, and_380_out, and_381_out, and_382_out, and_383_out, and_384_out, and_385_out,
       and_386_out, and_387_out, and_388_out, and_389_out, and_390_out, and_391_out, and_392_out,
       and_393_out, and_394_out, and_395_out, and_396_out, and_397_out, and_398_out, and_399_out,
       and_400_out, and_401_out, and_402_out, and_403_out, and_404_out, and_405_out, and_406_out,
       and_407_out, and_408_out, and_409_out, and_410_out, and_411_out, and_412_out, and_413_out,
       and_414_out, and_415_out, and_416_out, and_417_out, and_418_out, and_419_out, and_420_out,
       and_421_out, and_422_out, and_423_out, and_424_out, and_425_out, and_426_out, and_427_out,
       and_428_out, and_429_out, and_430_out, and_431_out, and_432_out, and_433_out, and_434_out,
       and_435_out, and_436_out, and_437_out, and_438_out, and_439_out, and_440_out, and_441_out,
       and_442_out, and_443_out, and_444_out, and_445_out, and_446_out, and_447_out, and_448_out,
       and_449_out, and_450_out, and_451_out, and_452_out, and_453_out, and_454_out, and_455_out,
       and_456_out, and_457_out, and_458_out, and_459_out, and_460_out, and_461_out, and_462_out,
       and_463_out, and_464_out, and_465_out, and_466_out, and_467_out, and_468_out, and_469_out,
       and_470_out, and_471_out, and_472_out, and_473_out, and_474_out, and_475_out, and_476_out,
       and_477_out, and_478_out, and_479_out, and_480_out, and_481_out, and_482_out, and_483_out,
       and_484_out, and_485_out, and_486_out, and_487_out, and_488_out, and_489_out, and_490_out,
       and_491_out, and_492_out, and_493_out, and_494_out, and_495_out, and_496_out, and_497_out,
       and_498_out, and_499_out, and_500_out, and_501_out, and_502_out, and_503_out, and_504_out,
       and_505_out, and_506_out, and_507_out, and_508_out, and_509_out, and_510_out, and_511_out,
       and_512_out, and_513_out, and_514_out, and_515_out, and_516_out, and_517_out, and_518_out,
       and_519_out, and_520_out, and_521_out, and_522_out, and_523_out, and_524_out, and_525_out,
       and_526_out, and_527_out, and_528_out, and_529_out, and_530_out, and_531_out, and_532_out,
       and_533_out, and_534_out, and_535_out, and_536_out, and_537_out, and_538_out, and_539_out,
       and_540_out, and_541_out, and_542_out, and_543_out, and_544_out, and_545_out, and_546_out,
       and_547_out, and_548_out, and_549_out, and_550_out, and_551_out, and_552_out, and_553_out,
       and_554_out, and_555_out, and_556_out, and_557_out, and_558_out, and_559_out, and_560_out,
       and_561_out, and_562_out, and_563_out, and_564_out, and_565_out, and_566_out, and_567_out,
       and_568_out, and_569_out, and_570_out, and_571_out, and_572_out, and_573_out, and_574_out,
       and_575_out, and_576_out, and_577_out, and_578_out, and_579_out, and_580_out, and_581_out,
       and_582_out, and_583_out, and_584_out, and_585_out, and_586_out, and_587_out, and_588_out,
       and_589_out, and_590_out, and_591_out, and_592_out, and_593_out, and_594_out, and_595_out,
       and_596_out, and_597_out, and_598_out, and_599_out, and_600_out, and_601_out, and_602_out,
       and_603_out, and_604_out, and_605_out, and_606_out, and_607_out, and_608_out, and_609_out,
       and_610_out, and_611_out, and_612_out, and_613_out, and_614_out, and_615_out, and_616_out,
       and_617_out, and_618_out, and_619_out, and_620_out, and_621_out, and_622_out, and_623_out,
       and_624_out, and_625_out, and_626_out, and_627_out, and_628_out, and_629_out, and_630_out,
       and_631_out, and_632_out, and_633_out, and_634_out, and_635_out, and_636_out, and_637_out,
       and_638_out, and_639_out, and_640_out, and_641_out, and_642_out, and_643_out, and_644_out,
       and_645_out, and_646_out, and_647_out, and_648_out, and_649_out, and_650_out, and_651_out,
       and_652_out, and_653_out, and_654_out, and_655_out, and_656_out, and_657_out, and_658_out,
       and_659_out, and_660_out, and_661_out, and_662_out, and_663_out, and_664_out, and_665_out,
       and_666_out, and_667_out, and_668_out, and_669_out, and_670_out, and_671_out, and_672_out,
       and_673_out, and_674_out, and_675_out, and_676_out, and_677_out, and_678_out, and_679_out,
       and_680_out, and_681_out, and_682_out, and_683_out, and_684_out, and_685_out, and_686_out,
       and_687_out, and_688_out, and_689_out, and_690_out, and_691_out, and_692_out, and_693_out,
       and_694_out, and_695_out, and_696_out, and_697_out, and_698_out, and_699_out, and_700_out,
       and_701_out, and_702_out, and_703_out, and_704_out, and_705_out, and_706_out, and_707_out,
       and_708_out, and_709_out, and_710_out, and_711_out, and_712_out, and_713_out, and_714_out,
       and_715_out, and_716_out, and_717_out, and_718_out, and_719_out, and_720_out, and_721_out,
       and_722_out, and_723_out, and_724_out, and_725_out, and_726_out, and_727_out, and_728_out,
       and_729_out, and_730_out, and_731_out, and_732_out, and_733_out, and_734_out, and_735_out,
       and_736_out, and_737_out, and_738_out, and_739_out, and_740_out, and_741_out, and_742_out,
       and_743_out, and_744_out, and_745_out, and_746_out, and_747_out, and_748_out, and_749_out,
       and_750_out, and_751_out, and_752_out, and_753_out, and_754_out, and_755_out, and_756_out,
       and_757_out, and_758_out, and_759_out, and_760_out, and_761_out, and_762_out, and_763_out,
       and_764_out, and_765_out, and_766_out, and_767_out, and_768_out, binary_decoder_4_to_16_1_out_5,
       binary_decoder_4_to_16_1_out_6, binary_decoder_4_to_16_1_out_7, binary_decoder_4_to_16_1_out_8,
       binary_decoder_4_to_16_1_out_9, binary_decoder_4_to_16_1_out_10, binary_decoder_4_to_16_1_out_11,
       binary_decoder_4_to_16_1_out_12, binary_decoder_4_to_16_1_out_13, binary_decoder_4_to_16_1_out_14,
       binary_decoder_4_to_16_1_out_15, binary_decoder_4_to_16_1_out_16, binary_decoder_4_to_16_1_out_17,
       binary_decoder_4_to_16_1_out_18, binary_decoder_4_to_16_1_out_19, binary_decoder_4_to_16_1_out_20,
       binary_decoder_4_to_16_2_1_out_5, binary_decoder_4_to_16_2_1_out_6, binary_decoder_4_to_16_2_1_out_7,
       binary_decoder_4_to_16_2_1_out_8, binary_decoder_4_to_16_2_1_out_9, binary_decoder_4_to_16_2_1_out_10,
       binary_decoder_4_to_16_2_1_out_11, binary_decoder_4_to_16_2_1_out_12,
       binary_decoder_4_to_16_2_1_out_13, binary_decoder_4_to_16_2_1_out_14,
       binary_decoder_4_to_16_2_1_out_15, binary_decoder_4_to_16_2_1_out_16,
       binary_decoder_4_to_16_2_1_out_17, binary_decoder_4_to_16_2_1_out_18,
       binary_decoder_4_to_16_2_1_out_19, binary_decoder_4_to_16_2_1_out_20, gated_latch_1_data_out,
       gated_latch_2_data_out, gated_latch_3_data_out, gated_latch_4_data_out, gated_latch_5_data_out,
       gated_latch_6_data_out, gated_latch_7_data_out, gated_latch_8_data_out, gated_latch_9_data_out,
       gated_latch_10_data_out, gated_latch_11_data_out, gated_latch_12_data_out, gated_latch_13_data_out,
       gated_latch_14_data_out, gated_latch_15_data_out, gated_latch_16_data_out, gated_latch_17_data_out,
       gated_latch_18_data_out, gated_latch_19_data_out, gated_latch_20_data_out, gated_latch_21_data_out,
       gated_latch_22_data_out, gated_latch_23_data_out, gated_latch_24_data_out, gated_latch_25_data_out,
       gated_latch_26_data_out, gated_latch_27_data_out, gated_latch_28_data_out, gated_latch_29_data_out,
       gated_latch_30_data_out, gated_latch_31_data_out, gated_latch_32_data_out, gated_latch_33_data_out,
       gated_latch_34_data_out, gated_latch_35_data_out, gated_latch_36_data_out, gated_latch_37_data_out,
       gated_latch_38_data_out, gated_latch_39_data_out, gated_latch_40_data_out, gated_latch_41_data_out,
       gated_latch_42_data_out, gated_latch_43_data_out, gated_latch_44_data_out, gated_latch_45_data_out,
       gated_latch_46_data_out, gated_latch_47_data_out, gated_latch_48_data_out, gated_latch_49_data_out,
       gated_latch_50_data_out, gated_latch_51_data_out, gated_latch_52_data_out, gated_latch_53_data_out,
       gated_latch_54_data_out, gated_latch_55_data_out, gated_latch_56_data_out, gated_latch_57_data_out,
       gated_latch_58_data_out, gated_latch_59_data_out, gated_latch_60_data_out, gated_latch_61_data_out,
       gated_latch_62_data_out, gated_latch_63_data_out, gated_latch_64_data_out, gated_latch_65_data_out,
       gated_latch_66_data_out, gated_latch_67_data_out, gated_latch_68_data_out, gated_latch_69_data_out,
       gated_latch_70_data_out, gated_latch_71_data_out, gated_latch_72_data_out, gated_latch_73_data_out,
       gated_latch_74_data_out, gated_latch_75_data_out, gated_latch_76_data_out, gated_latch_77_data_out,
       gated_latch_78_data_out, gated_latch_79_data_out, gated_latch_80_data_out, gated_latch_81_data_out,
       gated_latch_82_data_out, gated_latch_83_data_out, gated_latch_84_data_out, gated_latch_85_data_out,
       gated_latch_86_data_out, gated_latch_87_data_out, gated_latch_88_data_out, gated_latch_89_data_out,
       gated_latch_90_data_out, gated_latch_91_data_out, gated_latch_92_data_out, gated_latch_93_data_out,
       gated_latch_94_data_out, gated_latch_95_data_out, gated_latch_96_data_out, gated_latch_97_data_out,
       gated_latch_98_data_out, gated_latch_99_data_out, gated_latch_100_data_out, gated_latch_101_data_out,
       gated_latch_102_data_out, gated_latch_103_data_out, gated_latch_104_data_out,
       gated_latch_105_data_out, gated_latch_106_data_out, gated_latch_107_data_out,
       gated_latch_108_data_out, gated_latch_109_data_out, gated_latch_110_data_out,
       gated_latch_111_data_out, gated_latch_112_data_out, gated_latch_113_data_out,
       gated_latch_114_data_out, gated_latch_115_data_out, gated_latch_116_data_out,
       gated_latch_117_data_out, gated_latch_118_data_out, gated_latch_119_data_out,
       gated_latch_120_data_out, gated_latch_121_data_out, gated_latch_122_data_out,
       gated_latch_123_data_out, gated_latch_124_data_out, gated_latch_125_data_out,
       gated_latch_126_data_out, gated_latch_127_data_out, gated_latch_128_data_out,
       gated_latch_129_data_out, gated_latch_130_data_out, gated_latch_131_data_out,
       gated_latch_132_data_out, gated_latch_133_data_out, gated_latch_134_data_out,
       gated_latch_135_data_out, gated_latch_136_data_out, gated_latch_137_data_out,
       gated_latch_138_data_out, gated_latch_139_data_out, gated_latch_140_data_out,
       gated_latch_141_data_out, gated_latch_142_data_out, gated_latch_143_data_out,
       gated_latch_144_data_out, gated_latch_145_data_out, gated_latch_146_data_out,
       gated_latch_147_data_out, gated_latch_148_data_out, gated_latch_149_data_out,
       gated_latch_150_data_out, gated_latch_151_data_out, gated_latch_152_data_out,
       gated_latch_153_data_out, gated_latch_154_data_out, gated_latch_155_data_out,
       gated_latch_156_data_out, gated_latch_157_data_out, gated_latch_158_data_out,
       gated_latch_159_data_out, gated_latch_160_data_out, gated_latch_161_data_out,
       gated_latch_162_data_out, gated_latch_163_data_out, gated_latch_164_data_out,
       gated_latch_165_data_out, gated_latch_166_data_out, gated_latch_167_data_out,
       gated_latch_168_data_out, gated_latch_169_data_out, gated_latch_170_data_out,
       gated_latch_171_data_out, gated_latch_172_data_out, gated_latch_173_data_out,
       gated_latch_174_data_out, gated_latch_175_data_out, gated_latch_176_data_out,
       gated_latch_177_data_out, gated_latch_178_data_out, gated_latch_179_data_out,
       gated_latch_180_data_out, gated_latch_181_data_out, gated_latch_182_data_out,
       gated_latch_183_data_out, gated_latch_184_data_out, gated_latch_185_data_out,
       gated_latch_186_data_out, gated_latch_187_data_out, gated_latch_188_data_out,
       gated_latch_189_data_out, gated_latch_190_data_out, gated_latch_191_data_out,
       gated_latch_192_data_out, gated_latch_193_data_out, gated_latch_194_data_out,
       gated_latch_195_data_out, gated_latch_196_data_out, gated_latch_197_data_out,
       gated_latch_198_data_out, gated_latch_199_data_out, gated_latch_200_data_out,
       gated_latch_201_data_out, gated_latch_202_data_out, gated_latch_203_data_out,
       gated_latch_204_data_out, gated_latch_205_data_out, gated_latch_206_data_out,
       gated_latch_207_data_out, gated_latch_208_data_out, gated_latch_209_data_out,
       gated_latch_210_data_out, gated_latch_211_data_out, gated_latch_212_data_out,
       gated_latch_213_data_out, gated_latch_214_data_out, gated_latch_215_data_out,
       gated_latch_216_data_out, gated_latch_217_data_out, gated_latch_218_data_out,
       gated_latch_219_data_out, gated_latch_220_data_out, gated_latch_221_data_out,
       gated_latch_222_data_out, gated_latch_223_data_out, gated_latch_224_data_out,
       gated_latch_225_data_out, gated_latch_226_data_out, gated_latch_227_data_out,
       gated_latch_228_data_out, gated_latch_229_data_out, gated_latch_230_data_out,
       gated_latch_231_data_out, gated_latch_232_data_out, gated_latch_233_data_out,
       gated_latch_234_data_out, gated_latch_235_data_out, gated_latch_236_data_out,
       gated_latch_237_data_out, gated_latch_238_data_out, gated_latch_239_data_out,
       gated_latch_240_data_out, gated_latch_241_data_out, gated_latch_242_data_out,
       gated_latch_243_data_out, gated_latch_244_data_out, gated_latch_245_data_out,
       gated_latch_246_data_out, gated_latch_247_data_out, gated_latch_248_data_out,
       gated_latch_249_data_out, gated_latch_250_data_out, gated_latch_251_data_out,
       gated_latch_252_data_out, gated_latch_253_data_out, gated_latch_254_data_out,
       gated_latch_255_data_out, gated_latch_256_data_out;

  Binary_Decoder_4_to_16 binary_decoder_4_to_16_1 (
    .in_1(A7), .in_2(A6), .in_3(A5), .in_4(A4), .out_5(binary_decoder_4_to_16_1_out_5),
    .out_6(binary_decoder_4_to_16_1_out_6), .out_7(binary_decoder_4_to_16_1_out_7),
    .out_8(binary_decoder_4_to_16_1_out_8), .out_9(binary_decoder_4_to_16_1_out_9),
    .out_10(binary_decoder_4_to_16_1_out_10), .out_11(binary_decoder_4_to_16_1_out_11),
    .out_12(binary_decoder_4_to_16_1_out_12), .out_13(binary_decoder_4_to_16_1_out_13),
    .out_14(binary_decoder_4_to_16_1_out_14), .out_15(binary_decoder_4_to_16_1_out_15),
    .out_16(binary_decoder_4_to_16_1_out_16), .out_17(binary_decoder_4_to_16_1_out_17),
    .out_18(binary_decoder_4_to_16_1_out_18), .out_19(binary_decoder_4_to_16_1_out_19),
    .out_20(binary_decoder_4_to_16_1_out_20));
  and and_1 (and_1_out, binary_decoder_4_to_16_2_1_out_20, binary_decoder_4_to_16_1_out_5);
  and and_2 (and_2_out, binary_decoder_4_to_16_2_1_out_20, binary_decoder_4_to_16_1_out_6);
  and and_3 (and_3_out, binary_decoder_4_to_16_2_1_out_20, binary_decoder_4_to_16_1_out_7);
  and and_4 (and_4_out, binary_decoder_4_to_16_2_1_out_20, binary_decoder_4_to_16_1_out_8);
  and and_5 (and_5_out, binary_decoder_4_to_16_2_1_out_20, binary_decoder_4_to_16_1_out_9);
  and and_6 (and_6_out, binary_decoder_4_to_16_2_1_out_20, binary_decoder_4_to_16_1_out_10);
  and and_7 (and_7_out, binary_decoder_4_to_16_2_1_out_20, binary_decoder_4_to_16_1_out_11);
  and and_8 (and_8_out, binary_decoder_4_to_16_2_1_out_20, binary_decoder_4_to_16_1_out_12);
  and and_9 (and_9_out, binary_decoder_4_to_16_2_1_out_20, binary_decoder_4_to_16_1_out_13);
  and and_10 (and_10_out, binary_decoder_4_to_16_2_1_out_20, binary_decoder_4_to_16_1_out_14);
  and and_11 (and_11_out, binary_decoder_4_to_16_2_1_out_20, binary_decoder_4_to_16_1_out_15);
  and and_12 (and_12_out, binary_decoder_4_to_16_2_1_out_20, binary_decoder_4_to_16_1_out_16);
  and and_13 (and_13_out, binary_decoder_4_to_16_2_1_out_20, binary_decoder_4_to_16_1_out_17);
  and and_14 (and_14_out, binary_decoder_4_to_16_2_1_out_20, binary_decoder_4_to_16_1_out_18);
  and and_15 (and_15_out, binary_decoder_4_to_16_2_1_out_20, binary_decoder_4_to_16_1_out_19);
  and and_16 (and_16_out, binary_decoder_4_to_16_2_1_out_20, binary_decoder_4_to_16_1_out_20);
  and and_17 (and_17_out, Write_Enable, and_1_out);
  and and_18 (and_18_out, Write_Enable, and_2_out);
  and and_19 (and_19_out, Write_Enable, and_3_out);
  and and_20 (and_20_out, Write_Enable, and_4_out);
  and and_21 (and_21_out, Write_Enable, and_5_out);
  and and_22 (and_22_out, Write_Enable, and_6_out);
  and and_23 (and_23_out, Write_Enable, and_7_out);
  and and_24 (and_24_out, Write_Enable, and_8_out);
  and and_25 (and_25_out, Write_Enable, and_9_out);
  and and_26 (and_26_out, Write_Enable, and_10_out);
  and and_27 (and_27_out, Write_Enable, and_11_out);
  and and_28 (and_28_out, Write_Enable, and_12_out);
  and and_29 (and_29_out, Write_Enable, and_13_out);
  and and_30 (and_30_out, Write_Enable, and_14_out);
  and and_31 (and_31_out, Write_Enable, and_15_out);
  and and_32 (and_32_out, Write_Enable, and_16_out);
  Gated_Latch gated_latch_1 (.Data_In(Data_In), .Write_Enable(and_17_out), .Data_Out(gated_latch_1_data_out));
  and and_33 (and_33_out, and_1_out, Read_Enable);
  Gated_Latch gated_latch_2 (.Data_In(Data_In), .Write_Enable(and_18_out), .Data_Out(gated_latch_2_data_out));
  and and_34 (and_34_out, and_2_out, Read_Enable);
  Gated_Latch gated_latch_3 (.Data_In(Data_In), .Write_Enable(and_19_out), .Data_Out(gated_latch_3_data_out));
  and and_35 (and_35_out, and_3_out, Read_Enable);
  Gated_Latch gated_latch_4 (.Data_In(Data_In), .Write_Enable(and_20_out), .Data_Out(gated_latch_4_data_out));
  and and_36 (and_36_out, and_4_out, Read_Enable);
  Gated_Latch gated_latch_5 (.Data_In(Data_In), .Write_Enable(and_21_out), .Data_Out(gated_latch_5_data_out));
  and and_37 (and_37_out, and_5_out, Read_Enable);
  Gated_Latch gated_latch_6 (.Data_In(Data_In), .Write_Enable(and_22_out), .Data_Out(gated_latch_6_data_out));
  and and_38 (and_38_out, and_6_out, Read_Enable);
  Gated_Latch gated_latch_7 (.Data_In(Data_In), .Write_Enable(and_23_out), .Data_Out(gated_latch_7_data_out));
  and and_39 (and_39_out, and_7_out, Read_Enable);
  Gated_Latch gated_latch_8 (.Data_In(Data_In), .Write_Enable(and_24_out), .Data_Out(gated_latch_8_data_out));
  and and_40 (and_40_out, and_8_out, Read_Enable);
  Gated_Latch gated_latch_9 (.Data_In(Data_In), .Write_Enable(and_25_out), .Data_Out(gated_latch_9_data_out));
  and and_41 (and_41_out, and_9_out, Read_Enable);
  Gated_Latch gated_latch_10 (.Data_In(Data_In), .Write_Enable(and_26_out), .Data_Out(gated_latch_10_data_out));
  and and_42 (and_42_out, and_10_out, Read_Enable);
  Gated_Latch gated_latch_11 (.Data_In(Data_In), .Write_Enable(and_27_out), .Data_Out(gated_latch_11_data_out));
  and and_43 (and_43_out, and_11_out, Read_Enable);
  Gated_Latch gated_latch_12 (.Data_In(Data_In), .Write_Enable(and_28_out), .Data_Out(gated_latch_12_data_out));
  and and_44 (and_44_out, and_12_out, Read_Enable);
  Gated_Latch gated_latch_13 (.Data_In(Data_In), .Write_Enable(and_29_out), .Data_Out(gated_latch_13_data_out));
  and and_45 (and_45_out, and_13_out, Read_Enable);
  Gated_Latch gated_latch_14 (.Data_In(Data_In), .Write_Enable(and_30_out), .Data_Out(gated_latch_14_data_out));
  and and_46 (and_46_out, and_14_out, Read_Enable);
  Gated_Latch gated_latch_15 (.Data_In(Data_In), .Write_Enable(and_31_out), .Data_Out(gated_latch_15_data_out));
  and and_47 (and_47_out, and_15_out, Read_Enable);
  Gated_Latch gated_latch_16 (.Data_In(Data_In), .Write_Enable(and_32_out), .Data_Out(gated_latch_16_data_out));
  and and_48 (and_48_out, and_16_out, Read_Enable);
  Binary_Decoder_4_to_16_2 binary_decoder_4_to_16_2_1 (
    .in_1(A0), .in_2(A1), .in_3(A2), .in_4(A3), .out_16(binary_decoder_4_to_16_2_1_out_16),
    .out_17(binary_decoder_4_to_16_2_1_out_17), .out_18(binary_decoder_4_to_16_2_1_out_18),
    .out_19(binary_decoder_4_to_16_2_1_out_19), .out_20(binary_decoder_4_to_16_2_1_out_20),
    .out_5(binary_decoder_4_to_16_2_1_out_5), .out_6(binary_decoder_4_to_16_2_1_out_6),
    .out_7(binary_decoder_4_to_16_2_1_out_7), .out_8(binary_decoder_4_to_16_2_1_out_8),
    .out_9(binary_decoder_4_to_16_2_1_out_9), .out_10(binary_decoder_4_to_16_2_1_out_10),
    .out_11(binary_decoder_4_to_16_2_1_out_11), .out_12(binary_decoder_4_to_16_2_1_out_12),
    .out_13(binary_decoder_4_to_16_2_1_out_13), .out_14(binary_decoder_4_to_16_2_1_out_14),
    .out_15(binary_decoder_4_to_16_2_1_out_15));
  assign Data_Out = and_33_out ? gated_latch_1_data_out : 1'bz;  // Controlled_Buffer controlled_buffer_1
  assign Data_Out = and_34_out ? gated_latch_2_data_out : 1'bz;  // Controlled_Buffer controlled_buffer_2
  assign Data_Out = and_35_out ? gated_latch_3_data_out : 1'bz;  // Controlled_Buffer controlled_buffer_3
  assign Data_Out = and_36_out ? gated_latch_4_data_out : 1'bz;  // Controlled_Buffer controlled_buffer_4
  assign Data_Out = and_37_out ? gated_latch_5_data_out : 1'bz;  // Controlled_Buffer controlled_buffer_5
  assign Data_Out = and_38_out ? gated_latch_6_data_out : 1'bz;  // Controlled_Buffer controlled_buffer_6
  assign Data_Out = and_39_out ? gated_latch_7_data_out : 1'bz;  // Controlled_Buffer controlled_buffer_7
  assign Data_Out = and_40_out ? gated_latch_8_data_out : 1'bz;  // Controlled_Buffer controlled_buffer_8
  assign Data_Out = and_41_out ? gated_latch_9_data_out : 1'bz;  // Controlled_Buffer controlled_buffer_9
  assign Data_Out = and_42_out ? gated_latch_10_data_out : 1'bz;  // Controlled_Buffer controlled_buffer_10
  assign Data_Out = and_43_out ? gated_latch_11_data_out : 1'bz;  // Controlled_Buffer controlled_buffer_11
  assign Data_Out = and_44_out ? gated_latch_12_data_out : 1'bz;  // Controlled_Buffer controlled_buffer_12
  assign Data_Out = and_45_out ? gated_latch_13_data_out : 1'bz;  // Controlled_Buffer controlled_buffer_13
  assign Data_Out = and_46_out ? gated_latch_14_data_out : 1'bz;  // Controlled_Buffer controlled_buffer_14
  assign Data_Out = and_47_out ? gated_latch_15_data_out : 1'bz;  // Controlled_Buffer controlled_buffer_15
  assign Data_Out = and_48_out ? gated_latch_16_data_out : 1'bz;  // Controlled_Buffer controlled_buffer_16
  and and_49 (and_49_out, binary_decoder_4_to_16_2_1_out_19, binary_decoder_4_to_16_1_out_5);
  and and_50 (and_50_out, binary_decoder_4_to_16_2_1_out_19, binary_decoder_4_to_16_1_out_6);
  and and_51 (and_51_out, binary_decoder_4_to_16_2_1_out_19, binary_decoder_4_to_16_1_out_7);
  and and_52 (and_52_out, binary_decoder_4_to_16_2_1_out_19, binary_decoder_4_to_16_1_out_8);
  and and_53 (and_53_out, binary_decoder_4_to_16_2_1_out_19, binary_decoder_4_to_16_1_out_9);
  and and_54 (and_54_out, binary_decoder_4_to_16_2_1_out_19, binary_decoder_4_to_16_1_out_10);
  and and_55 (and_55_out, binary_decoder_4_to_16_2_1_out_19, binary_decoder_4_to_16_1_out_11);
  and and_56 (and_56_out, binary_decoder_4_to_16_2_1_out_19, binary_decoder_4_to_16_1_out_12);
  and and_57 (and_57_out, binary_decoder_4_to_16_2_1_out_19, binary_decoder_4_to_16_1_out_13);
  and and_58 (and_58_out, binary_decoder_4_to_16_2_1_out_19, binary_decoder_4_to_16_1_out_14);
  and and_59 (and_59_out, binary_decoder_4_to_16_2_1_out_19, binary_decoder_4_to_16_1_out_15);
  and and_60 (and_60_out, binary_decoder_4_to_16_2_1_out_19, binary_decoder_4_to_16_1_out_16);
  and and_61 (and_61_out, binary_decoder_4_to_16_2_1_out_19, binary_decoder_4_to_16_1_out_17);
  and and_62 (and_62_out, binary_decoder_4_to_16_2_1_out_19, binary_decoder_4_to_16_1_out_18);
  and and_63 (and_63_out, binary_decoder_4_to_16_2_1_out_19, binary_decoder_4_to_16_1_out_19);
  and and_64 (and_64_out, binary_decoder_4_to_16_2_1_out_19, binary_decoder_4_to_16_1_out_20);
  and and_65 (and_65_out, Write_Enable, and_49_out);
  and and_66 (and_66_out, Write_Enable, and_50_out);
  and and_67 (and_67_out, Write_Enable, and_51_out);
  and and_68 (and_68_out, Write_Enable, and_52_out);
  and and_69 (and_69_out, Write_Enable, and_53_out);
  and and_70 (and_70_out, Write_Enable, and_54_out);
  and and_71 (and_71_out, Write_Enable, and_55_out);
  and and_72 (and_72_out, Write_Enable, and_56_out);
  and and_73 (and_73_out, Write_Enable, and_57_out);
  and and_74 (and_74_out, Write_Enable, and_58_out);
  and and_75 (and_75_out, Write_Enable, and_59_out);
  and and_76 (and_76_out, Write_Enable, and_60_out);
  and and_77 (and_77_out, Write_Enable, and_61_out);
  and and_78 (and_78_out, Write_Enable, and_62_out);
  and and_79 (and_79_out, Write_Enable, and_63_out);
  and and_80 (and_80_out, Write_Enable, and_64_out);
  Gated_Latch gated_latch_17 (.Data_In(Data_In), .Write_Enable(and_65_out), .Data_Out(gated_latch_17_data_out));
  Gated_Latch gated_latch_18 (.Data_In(Data_In), .Write_Enable(and_66_out), .Data_Out(gated_latch_18_data_out));
  Gated_Latch gated_latch_19 (.Data_In(Data_In), .Write_Enable(and_67_out), .Data_Out(gated_latch_19_data_out));
  Gated_Latch gated_latch_20 (.Data_In(Data_In), .Write_Enable(and_68_out), .Data_Out(gated_latch_20_data_out));
  Gated_Latch gated_latch_21 (.Data_In(Data_In), .Write_Enable(and_69_out), .Data_Out(gated_latch_21_data_out));
  Gated_Latch gated_latch_22 (.Data_In(Data_In), .Write_Enable(and_70_out), .Data_Out(gated_latch_22_data_out));
  Gated_Latch gated_latch_23 (.Data_In(Data_In), .Write_Enable(and_71_out), .Data_Out(gated_latch_23_data_out));
  Gated_Latch gated_latch_24 (.Data_In(Data_In), .Write_Enable(and_72_out), .Data_Out(gated_latch_24_data_out));
  Gated_Latch gated_latch_25 (.Data_In(Data_In), .Write_Enable(and_73_out), .Data_Out(gated_latch_25_data_out));
  Gated_Latch gated_latch_26 (.Data_In(Data_In), .Write_Enable(and_74_out), .Data_Out(gated_latch_26_data_out));
  Gated_Latch gated_latch_27 (.Data_In(Data_In), .Write_Enable(and_75_out), .Data_Out(gated_latch_27_data_out));
  Gated_Latch gated_latch_28 (.Data_In(Data_In), .Write_Enable(and_76_out), .Data_Out(gated_latch_28_data_out));
  Gated_Latch gated_latch_29 (.Data_In(Data_In), .Write_Enable(and_77_out), .Data_Out(gated_latch_29_data_out));
  Gated_Latch gated_latch_30 (.Data_In(Data_In), .Write_Enable(and_78_out), .Data_Out(gated_latch_30_data_out));
  Gated_Latch gated_latch_31 (.Data_In(Data_In), .Write_Enable(and_79_out), .Data_Out(gated_latch_31_data_out));
  Gated_Latch gated_latch_32 (.Data_In(Data_In), .Write_Enable(and_80_out), .Data_Out(gated_latch_32_data_out));
  assign Data_Out = and_81_out ? gated_latch_17_data_out : 1'bz;  // Controlled_Buffer controlled_buffer_17
  and and_81 (and_81_out, and_49_out, Read_Enable);
  assign Data_Out = and_82_out ? gated_latch_18_data_out : 1'bz;  // Controlled_Buffer controlled_buffer_18
  and and_82 (and_82_out, and_50_out, Read_Enable);
  assign Data_Out = and_83_out ? gated_latch_19_data_out : 1'bz;  // Controlled_Buffer controlled_buffer_19
  and and_83 (and_83_out, and_51_out, Read_Enable);
  assign Data_Out = and_84_out ? gated_latch_20_data_out : 1'bz;  // Controlled_Buffer controlled_buffer_20
  and and_84 (and_84_out, and_52_out, Read_Enable);
  assign Data_Out = and_85_out ? gated_latch_21_data_out : 1'bz;  // Controlled_Buffer controlled_buffer_21
  and and_85 (and_85_out, and_53_out, Read_Enable);
  assign Data_Out = and_86_out ? gated_latch_22_data_out : 1'bz;  // Controlled_Buffer controlled_buffer_22
  and and_86 (and_86_out, and_54_out, Read_Enable);
  assign Data_Out = and_87_out ? gated_latch_23_data_out : 1'bz;  // Controlled_Buffer controlled_buffer_23
  and and_87 (and_87_out, and_55_out, Read_Enable);
  assign Data_Out = and_88_out ? gated_latch_24_data_out : 1'bz;  // Controlled_Buffer controlled_buffer_24
  and and_88 (and_88_out, and_56_out, Read_Enable);
  assign Data_Out = and_89_out ? gated_latch_25_data_out : 1'bz;  // Controlled_Buffer controlled_buffer_25
  and and_89 (and_89_out, and_57_out, Read_Enable);
  assign Data_Out = and_90_out ? gated_latch_26_data_out : 1'bz;  // Controlled_Buffer controlled_buffer_26
  and and_90 (and_90_out, and_58_out, Read_Enable);
  assign Data_Out = and_91_out ? gated_latch_27_data_out : 1'bz;  // Controlled_Buffer controlled_buffer_27
  and and_91 (and_91_out, and_59_out, Read_Enable);
  assign Data_Out = and_92_out ? gated_latch_28_data_out : 1'bz;  // Controlled_Buffer controlled_buffer_28
  and and_92 (and_92_out, and_60_out, Read_Enable);
  assign Data_Out = and_93_out ? gated_latch_29_data_out : 1'bz;  // Controlled_Buffer controlled_buffer_29
  and and_93 (and_93_out, and_61_out, Read_Enable);
  assign Data_Out = and_94_out ? gated_latch_30_data_out : 1'bz;  // Controlled_Buffer controlled_buffer_30
  and and_94 (and_94_out, and_62_out, Read_Enable);
  assign Data_Out = and_95_out ? gated_latch_31_data_out : 1'bz;  // Controlled_Buffer controlled_buffer_31
  and and_95 (and_95_out, and_63_out, Read_Enable);
  assign Data_Out = and_96_out ? gated_latch_32_data_out : 1'bz;  // Controlled_Buffer controlled_buffer_32
  and and_96 (and_96_out, and_64_out, Read_Enable);
  and and_97 (and_97_out, binary_decoder_4_to_16_2_1_out_18, binary_decoder_4_to_16_1_out_5);
  and and_98 (and_98_out, binary_decoder_4_to_16_2_1_out_18, binary_decoder_4_to_16_1_out_6);
  and and_99 (and_99_out, binary_decoder_4_to_16_2_1_out_18, binary_decoder_4_to_16_1_out_7);
  and and_100 (and_100_out, binary_decoder_4_to_16_2_1_out_18, binary_decoder_4_to_16_1_out_8);
  and and_101 (and_101_out, binary_decoder_4_to_16_2_1_out_18, binary_decoder_4_to_16_1_out_9);
  and and_102 (and_102_out, binary_decoder_4_to_16_2_1_out_18, binary_decoder_4_to_16_1_out_10);
  and and_103 (and_103_out, binary_decoder_4_to_16_2_1_out_18, binary_decoder_4_to_16_1_out_11);
  and and_104 (and_104_out, binary_decoder_4_to_16_2_1_out_18, binary_decoder_4_to_16_1_out_12);
  and and_105 (and_105_out, binary_decoder_4_to_16_2_1_out_18, binary_decoder_4_to_16_1_out_13);
  and and_106 (and_106_out, binary_decoder_4_to_16_2_1_out_18, binary_decoder_4_to_16_1_out_14);
  and and_107 (and_107_out, binary_decoder_4_to_16_2_1_out_18, binary_decoder_4_to_16_1_out_15);
  and and_108 (and_108_out, binary_decoder_4_to_16_2_1_out_18, binary_decoder_4_to_16_1_out_16);
  and and_109 (and_109_out, binary_decoder_4_to_16_2_1_out_18, binary_decoder_4_to_16_1_out_17);
  and and_110 (and_110_out, binary_decoder_4_to_16_2_1_out_18, binary_decoder_4_to_16_1_out_18);
  and and_111 (and_111_out, binary_decoder_4_to_16_2_1_out_18, binary_decoder_4_to_16_1_out_19);
  and and_112 (and_112_out, binary_decoder_4_to_16_2_1_out_18, binary_decoder_4_to_16_1_out_20);
  and and_113 (and_113_out, Write_Enable, and_97_out);
  and and_114 (and_114_out, Write_Enable, and_98_out);
  and and_115 (and_115_out, Write_Enable, and_99_out);
  and and_116 (and_116_out, Write_Enable, and_100_out);
  and and_117 (and_117_out, Write_Enable, and_101_out);
  and and_118 (and_118_out, Write_Enable, and_102_out);
  and and_119 (and_119_out, Write_Enable, and_103_out);
  and and_120 (and_120_out, Write_Enable, and_104_out);
  and and_121 (and_121_out, Write_Enable, and_105_out);
  and and_122 (and_122_out, Write_Enable, and_106_out);
  and and_123 (and_123_out, Write_Enable, and_107_out);
  and and_124 (and_124_out, Write_Enable, and_108_out);
  and and_125 (and_125_out, Write_Enable, and_109_out);
  and and_126 (and_126_out, Write_Enable, and_110_out);
  and and_127 (and_127_out, Write_Enable, and_111_out);
  and and_128 (and_128_out, Write_Enable, and_112_out);
  Gated_Latch gated_latch_33 (.Data_In(Data_In), .Write_Enable(and_113_out), .Data_Out(gated_latch_33_data_out));
  Gated_Latch gated_latch_34 (.Data_In(Data_In), .Write_Enable(and_114_out), .Data_Out(gated_latch_34_data_out));
  Gated_Latch gated_latch_35 (.Data_In(Data_In), .Write_Enable(and_115_out), .Data_Out(gated_latch_35_data_out));
  Gated_Latch gated_latch_36 (.Data_In(Data_In), .Write_Enable(and_116_out), .Data_Out(gated_latch_36_data_out));
  Gated_Latch gated_latch_37 (.Data_In(Data_In), .Write_Enable(and_117_out), .Data_Out(gated_latch_37_data_out));
  Gated_Latch gated_latch_38 (.Data_In(Data_In), .Write_Enable(and_118_out), .Data_Out(gated_latch_38_data_out));
  Gated_Latch gated_latch_39 (.Data_In(Data_In), .Write_Enable(and_119_out), .Data_Out(gated_latch_39_data_out));
  Gated_Latch gated_latch_40 (.Data_In(Data_In), .Write_Enable(and_120_out), .Data_Out(gated_latch_40_data_out));
  Gated_Latch gated_latch_41 (.Data_In(Data_In), .Write_Enable(and_121_out), .Data_Out(gated_latch_41_data_out));
  Gated_Latch gated_latch_42 (.Data_In(Data_In), .Write_Enable(and_122_out), .Data_Out(gated_latch_42_data_out));
  Gated_Latch gated_latch_43 (.Data_In(Data_In), .Write_Enable(and_123_out), .Data_Out(gated_latch_43_data_out));
  Gated_Latch gated_latch_44 (.Data_In(Data_In), .Write_Enable(and_124_out), .Data_Out(gated_latch_44_data_out));
  Gated_Latch gated_latch_45 (.Data_In(Data_In), .Write_Enable(and_125_out), .Data_Out(gated_latch_45_data_out));
  Gated_Latch gated_latch_46 (.Data_In(Data_In), .Write_Enable(and_126_out), .Data_Out(gated_latch_46_data_out));
  Gated_Latch gated_latch_47 (.Data_In(Data_In), .Write_Enable(and_127_out), .Data_Out(gated_latch_47_data_out));
  Gated_Latch gated_latch_48 (.Data_In(Data_In), .Write_Enable(and_128_out), .Data_Out(gated_latch_48_data_out));
  assign Data_Out = and_129_out ? gated_latch_33_data_out : 1'bz;  // Controlled_Buffer controlled_buffer_33
  and and_129 (and_129_out, and_97_out, Read_Enable);
  assign Data_Out = and_130_out ? gated_latch_34_data_out : 1'bz;  // Controlled_Buffer controlled_buffer_34
  and and_130 (and_130_out, and_98_out, Read_Enable);
  assign Data_Out = and_131_out ? gated_latch_35_data_out : 1'bz;  // Controlled_Buffer controlled_buffer_35
  and and_131 (and_131_out, and_99_out, Read_Enable);
  assign Data_Out = and_132_out ? gated_latch_36_data_out : 1'bz;  // Controlled_Buffer controlled_buffer_36
  and and_132 (and_132_out, and_100_out, Read_Enable);
  assign Data_Out = and_133_out ? gated_latch_37_data_out : 1'bz;  // Controlled_Buffer controlled_buffer_37
  and and_133 (and_133_out, and_101_out, Read_Enable);
  assign Data_Out = and_134_out ? gated_latch_38_data_out : 1'bz;  // Controlled_Buffer controlled_buffer_38
  and and_134 (and_134_out, and_102_out, Read_Enable);
  assign Data_Out = and_135_out ? gated_latch_39_data_out : 1'bz;  // Controlled_Buffer controlled_buffer_39
  and and_135 (and_135_out, and_103_out, Read_Enable);
  assign Data_Out = and_136_out ? gated_latch_40_data_out : 1'bz;  // Controlled_Buffer controlled_buffer_40
  and and_136 (and_136_out, and_104_out, Read_Enable);
  assign Data_Out = and_137_out ? gated_latch_41_data_out : 1'bz;  // Controlled_Buffer controlled_buffer_41
  and and_137 (and_137_out, and_105_out, Read_Enable);
  assign Data_Out = and_138_out ? gated_latch_42_data_out : 1'bz;  // Controlled_Buffer controlled_buffer_42
  and and_138 (and_138_out, and_106_out, Read_Enable);
  assign Data_Out = and_139_out ? gated_latch_43_data_out : 1'bz;  // Controlled_Buffer controlled_buffer_43
  and and_139 (and_139_out, and_107_out, Read_Enable);
  assign Data_Out = and_140_out ? gated_latch_44_data_out : 1'bz;  // Controlled_Buffer controlled_buffer_44
  and and_140 (and_140_out, and_108_out, Read_Enable);
  assign Data_Out = and_141_out ? gated_latch_45_data_out : 1'bz;  // Controlled_Buffer controlled_buffer_45
  and and_141 (and_141_out, and_109_out, Read_Enable);
  assign Data_Out = and_142_out ? gated_latch_46_data_out : 1'bz;  // Controlled_Buffer controlled_buffer_46
  and and_142 (and_142_out, and_110_out, Read_Enable);
  assign Data_Out = and_143_out ? gated_latch_47_data_out : 1'bz;  // Controlled_Buffer controlled_buffer_47
  and and_143 (and_143_out, and_111_out, Read_Enable);
  assign Data_Out = and_144_out ? gated_latch_48_data_out : 1'bz;  // Controlled_Buffer controlled_buffer_48
  and and_144 (and_144_out, and_112_out, Read_Enable);
  and and_145 (and_145_out, binary_decoder_4_to_16_2_1_out_17, binary_decoder_4_to_16_1_out_5);
  and and_146 (and_146_out, binary_decoder_4_to_16_2_1_out_17, binary_decoder_4_to_16_1_out_6);
  and and_147 (and_147_out, binary_decoder_4_to_16_2_1_out_17, binary_decoder_4_to_16_1_out_7);
  and and_148 (and_148_out, binary_decoder_4_to_16_2_1_out_17, binary_decoder_4_to_16_1_out_8);
  and and_149 (and_149_out, binary_decoder_4_to_16_2_1_out_17, binary_decoder_4_to_16_1_out_9);
  and and_150 (and_150_out, binary_decoder_4_to_16_2_1_out_17, binary_decoder_4_to_16_1_out_10);
  and and_151 (and_151_out, binary_decoder_4_to_16_2_1_out_17, binary_decoder_4_to_16_1_out_11);
  and and_152 (and_152_out, binary_decoder_4_to_16_2_1_out_17, binary_decoder_4_to_16_1_out_12);
  and and_153 (and_153_out, binary_decoder_4_to_16_2_1_out_17, binary_decoder_4_to_16_1_out_13);
  and and_154 (and_154_out, binary_decoder_4_to_16_2_1_out_17, binary_decoder_4_to_16_1_out_14);
  and and_155 (and_155_out, binary_decoder_4_to_16_2_1_out_17, binary_decoder_4_to_16_1_out_15);
  and and_156 (and_156_out, binary_decoder_4_to_16_2_1_out_17, binary_decoder_4_to_16_1_out_16);
  and and_157 (and_157_out, binary_decoder_4_to_16_2_1_out_17, binary_decoder_4_to_16_1_out_17);
  and and_158 (and_158_out, binary_decoder_4_to_16_2_1_out_17, binary_decoder_4_to_16_1_out_18);
  and and_159 (and_159_out, binary_decoder_4_to_16_2_1_out_17, binary_decoder_4_to_16_1_out_19);
  and and_160 (and_160_out, binary_decoder_4_to_16_2_1_out_17, binary_decoder_4_to_16_1_out_20);
  and and_161 (and_161_out, Write_Enable, and_145_out);
  and and_162 (and_162_out, Write_Enable, and_146_out);
  and and_163 (and_163_out, Write_Enable, and_147_out);
  and and_164 (and_164_out, Write_Enable, and_148_out);
  and and_165 (and_165_out, Write_Enable, and_149_out);
  and and_166 (and_166_out, Write_Enable, and_150_out);
  and and_167 (and_167_out, Write_Enable, and_151_out);
  and and_168 (and_168_out, Write_Enable, and_152_out);
  and and_169 (and_169_out, Write_Enable, and_153_out);
  and and_170 (and_170_out, Write_Enable, and_154_out);
  and and_171 (and_171_out, Write_Enable, and_155_out);
  and and_172 (and_172_out, Write_Enable, and_156_out);
  and and_173 (and_173_out, Write_Enable, and_157_out);
  and and_174 (and_174_out, Write_Enable, and_158_out);
  and and_175 (and_175_out, Write_Enable, and_159_out);
  and and_176 (and_176_out, Write_Enable, and_160_out);
  assign Data_Out = and_177_out ? gated_latch_49_data_out : 1'bz;  // Controlled_Buffer controlled_buffer_49
  Gated_Latch gated_latch_49 (.Data_In(Data_In), .Write_Enable(and_161_out), .Data_Out(gated_latch_49_data_out));
  and and_177 (and_177_out, and_145_out, Read_Enable);
  assign Data_Out = and_178_out ? gated_latch_50_data_out : 1'bz;  // Controlled_Buffer controlled_buffer_50
  Gated_Latch gated_latch_50 (.Data_In(Data_In), .Write_Enable(and_162_out), .Data_Out(gated_latch_50_data_out));
  and and_178 (and_178_out, and_146_out, Read_Enable);
  assign Data_Out = and_179_out ? gated_latch_51_data_out : 1'bz;  // Controlled_Buffer controlled_buffer_51
  Gated_Latch gated_latch_51 (.Data_In(Data_In), .Write_Enable(and_163_out), .Data_Out(gated_latch_51_data_out));
  and and_179 (and_179_out, and_147_out, Read_Enable);
  assign Data_Out = and_180_out ? gated_latch_52_data_out : 1'bz;  // Controlled_Buffer controlled_buffer_52
  Gated_Latch gated_latch_52 (.Data_In(Data_In), .Write_Enable(and_164_out), .Data_Out(gated_latch_52_data_out));
  and and_180 (and_180_out, and_148_out, Read_Enable);
  assign Data_Out = and_181_out ? gated_latch_53_data_out : 1'bz;  // Controlled_Buffer controlled_buffer_53
  Gated_Latch gated_latch_53 (.Data_In(Data_In), .Write_Enable(and_165_out), .Data_Out(gated_latch_53_data_out));
  and and_181 (and_181_out, and_149_out, Read_Enable);
  assign Data_Out = and_182_out ? gated_latch_54_data_out : 1'bz;  // Controlled_Buffer controlled_buffer_54
  Gated_Latch gated_latch_54 (.Data_In(Data_In), .Write_Enable(and_166_out), .Data_Out(gated_latch_54_data_out));
  and and_182 (and_182_out, and_150_out, Read_Enable);
  assign Data_Out = and_183_out ? gated_latch_55_data_out : 1'bz;  // Controlled_Buffer controlled_buffer_55
  Gated_Latch gated_latch_55 (.Data_In(Data_In), .Write_Enable(and_167_out), .Data_Out(gated_latch_55_data_out));
  and and_183 (and_183_out, and_151_out, Read_Enable);
  assign Data_Out = and_184_out ? gated_latch_56_data_out : 1'bz;  // Controlled_Buffer controlled_buffer_56
  Gated_Latch gated_latch_56 (.Data_In(Data_In), .Write_Enable(and_168_out), .Data_Out(gated_latch_56_data_out));
  and and_184 (and_184_out, and_152_out, Read_Enable);
  assign Data_Out = and_185_out ? gated_latch_57_data_out : 1'bz;  // Controlled_Buffer controlled_buffer_57
  Gated_Latch gated_latch_57 (.Data_In(Data_In), .Write_Enable(and_169_out), .Data_Out(gated_latch_57_data_out));
  and and_185 (and_185_out, and_153_out, Read_Enable);
  assign Data_Out = and_186_out ? gated_latch_58_data_out : 1'bz;  // Controlled_Buffer controlled_buffer_58
  Gated_Latch gated_latch_58 (.Data_In(Data_In), .Write_Enable(and_170_out), .Data_Out(gated_latch_58_data_out));
  and and_186 (and_186_out, and_154_out, Read_Enable);
  assign Data_Out = and_187_out ? gated_latch_59_data_out : 1'bz;  // Controlled_Buffer controlled_buffer_59
  Gated_Latch gated_latch_59 (.Data_In(Data_In), .Write_Enable(and_171_out), .Data_Out(gated_latch_59_data_out));
  and and_187 (and_187_out, and_155_out, Read_Enable);
  assign Data_Out = and_188_out ? gated_latch_60_data_out : 1'bz;  // Controlled_Buffer controlled_buffer_60
  Gated_Latch gated_latch_60 (.Data_In(Data_In), .Write_Enable(and_172_out), .Data_Out(gated_latch_60_data_out));
  and and_188 (and_188_out, and_156_out, Read_Enable);
  assign Data_Out = and_189_out ? gated_latch_61_data_out : 1'bz;  // Controlled_Buffer controlled_buffer_61
  Gated_Latch gated_latch_61 (.Data_In(Data_In), .Write_Enable(and_173_out), .Data_Out(gated_latch_61_data_out));
  and and_189 (and_189_out, and_157_out, Read_Enable);
  assign Data_Out = and_190_out ? gated_latch_62_data_out : 1'bz;  // Controlled_Buffer controlled_buffer_62
  Gated_Latch gated_latch_62 (.Data_In(Data_In), .Write_Enable(and_174_out), .Data_Out(gated_latch_62_data_out));
  and and_190 (and_190_out, and_158_out, Read_Enable);
  assign Data_Out = and_191_out ? gated_latch_63_data_out : 1'bz;  // Controlled_Buffer controlled_buffer_63
  Gated_Latch gated_latch_63 (.Data_In(Data_In), .Write_Enable(and_175_out), .Data_Out(gated_latch_63_data_out));
  and and_191 (and_191_out, and_159_out, Read_Enable);
  assign Data_Out = and_192_out ? gated_latch_64_data_out : 1'bz;  // Controlled_Buffer controlled_buffer_64
  Gated_Latch gated_latch_64 (.Data_In(Data_In), .Write_Enable(and_176_out), .Data_Out(gated_latch_64_data_out));
  and and_192 (and_192_out, and_160_out, Read_Enable);
  and and_193 (and_193_out, binary_decoder_4_to_16_2_1_out_16, binary_decoder_4_to_16_1_out_5);
  and and_194 (and_194_out, binary_decoder_4_to_16_2_1_out_16, binary_decoder_4_to_16_1_out_6);
  and and_195 (and_195_out, binary_decoder_4_to_16_2_1_out_16, binary_decoder_4_to_16_1_out_7);
  and and_196 (and_196_out, binary_decoder_4_to_16_2_1_out_16, binary_decoder_4_to_16_1_out_8);
  and and_197 (and_197_out, binary_decoder_4_to_16_2_1_out_16, binary_decoder_4_to_16_1_out_9);
  and and_198 (and_198_out, binary_decoder_4_to_16_2_1_out_16, binary_decoder_4_to_16_1_out_10);
  and and_199 (and_199_out, binary_decoder_4_to_16_2_1_out_16, binary_decoder_4_to_16_1_out_11);
  and and_200 (and_200_out, binary_decoder_4_to_16_2_1_out_16, binary_decoder_4_to_16_1_out_12);
  and and_201 (and_201_out, binary_decoder_4_to_16_2_1_out_16, binary_decoder_4_to_16_1_out_13);
  and and_202 (and_202_out, binary_decoder_4_to_16_2_1_out_16, binary_decoder_4_to_16_1_out_14);
  and and_203 (and_203_out, binary_decoder_4_to_16_2_1_out_16, binary_decoder_4_to_16_1_out_15);
  and and_204 (and_204_out, binary_decoder_4_to_16_2_1_out_16, binary_decoder_4_to_16_1_out_16);
  and and_205 (and_205_out, binary_decoder_4_to_16_2_1_out_16, binary_decoder_4_to_16_1_out_17);
  and and_206 (and_206_out, binary_decoder_4_to_16_2_1_out_16, binary_decoder_4_to_16_1_out_18);
  and and_207 (and_207_out, binary_decoder_4_to_16_2_1_out_16, binary_decoder_4_to_16_1_out_19);
  and and_208 (and_208_out, binary_decoder_4_to_16_2_1_out_16, binary_decoder_4_to_16_1_out_20);
  and and_209 (and_209_out, Write_Enable, and_193_out);
  and and_210 (and_210_out, Write_Enable, and_194_out);
  and and_211 (and_211_out, Write_Enable, and_195_out);
  and and_212 (and_212_out, Write_Enable, and_196_out);
  and and_213 (and_213_out, Write_Enable, and_197_out);
  and and_214 (and_214_out, Write_Enable, and_198_out);
  and and_215 (and_215_out, Write_Enable, and_199_out);
  and and_216 (and_216_out, Write_Enable, and_200_out);
  and and_217 (and_217_out, Write_Enable, and_201_out);
  and and_218 (and_218_out, Write_Enable, and_202_out);
  and and_219 (and_219_out, Write_Enable, and_203_out);
  and and_220 (and_220_out, Write_Enable, and_204_out);
  and and_221 (and_221_out, Write_Enable, and_205_out);
  and and_222 (and_222_out, Write_Enable, and_206_out);
  and and_223 (and_223_out, Write_Enable, and_207_out);
  and and_224 (and_224_out, Write_Enable, and_208_out);
  assign Data_Out = and_225_out ? gated_latch_65_data_out : 1'bz;  // Controlled_Buffer controlled_buffer_65
  Gated_Latch gated_latch_65 (.Data_In(Data_In), .Write_Enable(and_209_out), .Data_Out(gated_latch_65_data_out));
  and and_225 (and_225_out, and_193_out, Read_Enable);
  assign Data_Out = and_226_out ? gated_latch_66_data_out : 1'bz;  // Controlled_Buffer controlled_buffer_66
  Gated_Latch gated_latch_66 (.Data_In(Data_In), .Write_Enable(and_210_out), .Data_Out(gated_latch_66_data_out));
  and and_226 (and_226_out, and_194_out, Read_Enable);
  assign Data_Out = and_227_out ? gated_latch_67_data_out : 1'bz;  // Controlled_Buffer controlled_buffer_67
  Gated_Latch gated_latch_67 (.Data_In(Data_In), .Write_Enable(and_211_out), .Data_Out(gated_latch_67_data_out));
  and and_227 (and_227_out, and_195_out, Read_Enable);
  assign Data_Out = and_228_out ? gated_latch_68_data_out : 1'bz;  // Controlled_Buffer controlled_buffer_68
  Gated_Latch gated_latch_68 (.Data_In(Data_In), .Write_Enable(and_212_out), .Data_Out(gated_latch_68_data_out));
  and and_228 (and_228_out, and_196_out, Read_Enable);
  assign Data_Out = and_229_out ? gated_latch_69_data_out : 1'bz;  // Controlled_Buffer controlled_buffer_69
  Gated_Latch gated_latch_69 (.Data_In(Data_In), .Write_Enable(and_213_out), .Data_Out(gated_latch_69_data_out));
  and and_229 (and_229_out, and_197_out, Read_Enable);
  assign Data_Out = and_230_out ? gated_latch_70_data_out : 1'bz;  // Controlled_Buffer controlled_buffer_70
  Gated_Latch gated_latch_70 (.Data_In(Data_In), .Write_Enable(and_214_out), .Data_Out(gated_latch_70_data_out));
  and and_230 (and_230_out, and_198_out, Read_Enable);
  assign Data_Out = and_231_out ? gated_latch_71_data_out : 1'bz;  // Controlled_Buffer controlled_buffer_71
  Gated_Latch gated_latch_71 (.Data_In(Data_In), .Write_Enable(and_215_out), .Data_Out(gated_latch_71_data_out));
  and and_231 (and_231_out, and_199_out, Read_Enable);
  assign Data_Out = and_232_out ? gated_latch_72_data_out : 1'bz;  // Controlled_Buffer controlled_buffer_72
  Gated_Latch gated_latch_72 (.Data_In(Data_In), .Write_Enable(and_216_out), .Data_Out(gated_latch_72_data_out));
  and and_232 (and_232_out, and_200_out, Read_Enable);
  assign Data_Out = and_233_out ? gated_latch_73_data_out : 1'bz;  // Controlled_Buffer controlled_buffer_73
  Gated_Latch gated_latch_73 (.Data_In(Data_In), .Write_Enable(and_217_out), .Data_Out(gated_latch_73_data_out));
  and and_233 (and_233_out, and_201_out, Read_Enable);
  assign Data_Out = and_234_out ? gated_latch_74_data_out : 1'bz;  // Controlled_Buffer controlled_buffer_74
  Gated_Latch gated_latch_74 (.Data_In(Data_In), .Write_Enable(and_218_out), .Data_Out(gated_latch_74_data_out));
  and and_234 (and_234_out, and_202_out, Read_Enable);
  assign Data_Out = and_235_out ? gated_latch_75_data_out : 1'bz;  // Controlled_Buffer controlled_buffer_75
  Gated_Latch gated_latch_75 (.Data_In(Data_In), .Write_Enable(and_219_out), .Data_Out(gated_latch_75_data_out));
  and and_235 (and_235_out, and_203_out, Read_Enable);
  assign Data_Out = and_236_out ? gated_latch_76_data_out : 1'bz;  // Controlled_Buffer controlled_buffer_76
  Gated_Latch gated_latch_76 (.Data_In(Data_In), .Write_Enable(and_220_out), .Data_Out(gated_latch_76_data_out));
  and and_236 (and_236_out, and_204_out, Read_Enable);
  assign Data_Out = and_237_out ? gated_latch_77_data_out : 1'bz;  // Controlled_Buffer controlled_buffer_77
  Gated_Latch gated_latch_77 (.Data_In(Data_In), .Write_Enable(and_221_out), .Data_Out(gated_latch_77_data_out));
  and and_237 (and_237_out, and_205_out, Read_Enable);
  assign Data_Out = and_238_out ? gated_latch_78_data_out : 1'bz;  // Controlled_Buffer controlled_buffer_78
  Gated_Latch gated_latch_78 (.Data_In(Data_In), .Write_Enable(and_222_out), .Data_Out(gated_latch_78_data_out));
  and and_238 (and_238_out, and_206_out, Read_Enable);
  assign Data_Out = and_239_out ? gated_latch_79_data_out : 1'bz;  // Controlled_Buffer controlled_buffer_79
  Gated_Latch gated_latch_79 (.Data_In(Data_In), .Write_Enable(and_223_out), .Data_Out(gated_latch_79_data_out));
  and and_239 (and_239_out, and_207_out, Read_Enable);
  assign Data_Out = and_240_out ? gated_latch_80_data_out : 1'bz;  // Controlled_Buffer controlled_buffer_80
  Gated_Latch gated_latch_80 (.Data_In(Data_In), .Write_Enable(and_224_out), .Data_Out(gated_latch_80_data_out));
  and and_240 (and_240_out, and_208_out, Read_Enable);
  and and_241 (and_241_out, binary_decoder_4_to_16_2_1_out_15, binary_decoder_4_to_16_1_out_5);
  and and_242 (and_242_out, Write_Enable, and_241_out);
  and and_243 (and_243_out, binary_decoder_4_to_16_2_1_out_15, binary_decoder_4_to_16_1_out_6);
  and and_244 (and_244_out, Write_Enable, and_243_out);
  and and_245 (and_245_out, binary_decoder_4_to_16_2_1_out_15, binary_decoder_4_to_16_1_out_7);
  and and_246 (and_246_out, Write_Enable, and_245_out);
  and and_247 (and_247_out, binary_decoder_4_to_16_2_1_out_15, binary_decoder_4_to_16_1_out_8);
  and and_248 (and_248_out, Write_Enable, and_247_out);
  and and_249 (and_249_out, binary_decoder_4_to_16_2_1_out_15, binary_decoder_4_to_16_1_out_9);
  and and_250 (and_250_out, Write_Enable, and_249_out);
  and and_251 (and_251_out, binary_decoder_4_to_16_2_1_out_15, binary_decoder_4_to_16_1_out_10);
  and and_252 (and_252_out, Write_Enable, and_251_out);
  and and_253 (and_253_out, binary_decoder_4_to_16_2_1_out_15, binary_decoder_4_to_16_1_out_11);
  and and_254 (and_254_out, Write_Enable, and_253_out);
  and and_255 (and_255_out, binary_decoder_4_to_16_2_1_out_15, binary_decoder_4_to_16_1_out_12);
  and and_256 (and_256_out, Write_Enable, and_255_out);
  and and_257 (and_257_out, binary_decoder_4_to_16_2_1_out_15, binary_decoder_4_to_16_1_out_13);
  and and_258 (and_258_out, Write_Enable, and_257_out);
  and and_259 (and_259_out, binary_decoder_4_to_16_2_1_out_15, binary_decoder_4_to_16_1_out_14);
  and and_260 (and_260_out, Write_Enable, and_259_out);
  and and_261 (and_261_out, binary_decoder_4_to_16_2_1_out_15, binary_decoder_4_to_16_1_out_15);
  and and_262 (and_262_out, Write_Enable, and_261_out);
  and and_263 (and_263_out, binary_decoder_4_to_16_2_1_out_15, binary_decoder_4_to_16_1_out_16);
  and and_264 (and_264_out, Write_Enable, and_263_out);
  and and_265 (and_265_out, binary_decoder_4_to_16_2_1_out_15, binary_decoder_4_to_16_1_out_17);
  and and_266 (and_266_out, Write_Enable, and_265_out);
  and and_267 (and_267_out, binary_decoder_4_to_16_2_1_out_15, binary_decoder_4_to_16_1_out_18);
  and and_268 (and_268_out, Write_Enable, and_267_out);
  and and_269 (and_269_out, binary_decoder_4_to_16_2_1_out_15, binary_decoder_4_to_16_1_out_19);
  and and_270 (and_270_out, Write_Enable, and_269_out);
  and and_271 (and_271_out, binary_decoder_4_to_16_2_1_out_15, binary_decoder_4_to_16_1_out_20);
  and and_272 (and_272_out, Write_Enable, and_271_out);
  assign Data_Out = and_273_out ? gated_latch_81_data_out : 1'bz;  // Controlled_Buffer controlled_buffer_81
  Gated_Latch gated_latch_81 (.Data_In(Data_In), .Write_Enable(and_242_out), .Data_Out(gated_latch_81_data_out));
  and and_273 (and_273_out, and_241_out, Read_Enable);
  assign Data_Out = and_274_out ? gated_latch_82_data_out : 1'bz;  // Controlled_Buffer controlled_buffer_82
  Gated_Latch gated_latch_82 (.Data_In(Data_In), .Write_Enable(and_244_out), .Data_Out(gated_latch_82_data_out));
  and and_274 (and_274_out, and_243_out, Read_Enable);
  assign Data_Out = and_275_out ? gated_latch_83_data_out : 1'bz;  // Controlled_Buffer controlled_buffer_83
  Gated_Latch gated_latch_83 (.Data_In(Data_In), .Write_Enable(and_246_out), .Data_Out(gated_latch_83_data_out));
  and and_275 (and_275_out, and_245_out, Read_Enable);
  assign Data_Out = and_276_out ? gated_latch_84_data_out : 1'bz;  // Controlled_Buffer controlled_buffer_84
  Gated_Latch gated_latch_84 (.Data_In(Data_In), .Write_Enable(and_248_out), .Data_Out(gated_latch_84_data_out));
  and and_276 (and_276_out, and_247_out, Read_Enable);
  assign Data_Out = and_277_out ? gated_latch_85_data_out : 1'bz;  // Controlled_Buffer controlled_buffer_85
  Gated_Latch gated_latch_85 (.Data_In(Data_In), .Write_Enable(and_250_out), .Data_Out(gated_latch_85_data_out));
  and and_277 (and_277_out, and_249_out, Read_Enable);
  assign Data_Out = and_278_out ? gated_latch_86_data_out : 1'bz;  // Controlled_Buffer controlled_buffer_86
  Gated_Latch gated_latch_86 (.Data_In(Data_In), .Write_Enable(and_252_out), .Data_Out(gated_latch_86_data_out));
  and and_278 (and_278_out, and_251_out, Read_Enable);
  assign Data_Out = and_279_out ? gated_latch_87_data_out : 1'bz;  // Controlled_Buffer controlled_buffer_87
  Gated_Latch gated_latch_87 (.Data_In(Data_In), .Write_Enable(and_254_out), .Data_Out(gated_latch_87_data_out));
  and and_279 (and_279_out, and_253_out, Read_Enable);
  assign Data_Out = and_280_out ? gated_latch_88_data_out : 1'bz;  // Controlled_Buffer controlled_buffer_88
  Gated_Latch gated_latch_88 (.Data_In(Data_In), .Write_Enable(and_256_out), .Data_Out(gated_latch_88_data_out));
  and and_280 (and_280_out, and_255_out, Read_Enable);
  assign Data_Out = and_281_out ? gated_latch_89_data_out : 1'bz;  // Controlled_Buffer controlled_buffer_89
  Gated_Latch gated_latch_89 (.Data_In(Data_In), .Write_Enable(and_258_out), .Data_Out(gated_latch_89_data_out));
  and and_281 (and_281_out, and_257_out, Read_Enable);
  assign Data_Out = and_282_out ? gated_latch_90_data_out : 1'bz;  // Controlled_Buffer controlled_buffer_90
  Gated_Latch gated_latch_90 (.Data_In(Data_In), .Write_Enable(and_260_out), .Data_Out(gated_latch_90_data_out));
  and and_282 (and_282_out, and_259_out, Read_Enable);
  assign Data_Out = and_283_out ? gated_latch_91_data_out : 1'bz;  // Controlled_Buffer controlled_buffer_91
  Gated_Latch gated_latch_91 (.Data_In(Data_In), .Write_Enable(and_262_out), .Data_Out(gated_latch_91_data_out));
  and and_283 (and_283_out, and_261_out, Read_Enable);
  assign Data_Out = and_284_out ? gated_latch_92_data_out : 1'bz;  // Controlled_Buffer controlled_buffer_92
  Gated_Latch gated_latch_92 (.Data_In(Data_In), .Write_Enable(and_264_out), .Data_Out(gated_latch_92_data_out));
  and and_284 (and_284_out, and_263_out, Read_Enable);
  assign Data_Out = and_285_out ? gated_latch_93_data_out : 1'bz;  // Controlled_Buffer controlled_buffer_93
  Gated_Latch gated_latch_93 (.Data_In(Data_In), .Write_Enable(and_266_out), .Data_Out(gated_latch_93_data_out));
  and and_285 (and_285_out, and_265_out, Read_Enable);
  assign Data_Out = and_286_out ? gated_latch_94_data_out : 1'bz;  // Controlled_Buffer controlled_buffer_94
  Gated_Latch gated_latch_94 (.Data_In(Data_In), .Write_Enable(and_268_out), .Data_Out(gated_latch_94_data_out));
  and and_286 (and_286_out, and_267_out, Read_Enable);
  assign Data_Out = and_287_out ? gated_latch_95_data_out : 1'bz;  // Controlled_Buffer controlled_buffer_95
  Gated_Latch gated_latch_95 (.Data_In(Data_In), .Write_Enable(and_270_out), .Data_Out(gated_latch_95_data_out));
  and and_287 (and_287_out, and_269_out, Read_Enable);
  assign Data_Out = and_288_out ? gated_latch_96_data_out : 1'bz;  // Controlled_Buffer controlled_buffer_96
  Gated_Latch gated_latch_96 (.Data_In(Data_In), .Write_Enable(and_272_out), .Data_Out(gated_latch_96_data_out));
  and and_288 (and_288_out, and_271_out, Read_Enable);
  and and_289 (and_289_out, binary_decoder_4_to_16_2_1_out_14, binary_decoder_4_to_16_1_out_5);
  and and_290 (and_290_out, Write_Enable, and_289_out);
  and and_291 (and_291_out, binary_decoder_4_to_16_2_1_out_14, binary_decoder_4_to_16_1_out_6);
  and and_292 (and_292_out, Write_Enable, and_291_out);
  and and_293 (and_293_out, binary_decoder_4_to_16_2_1_out_14, binary_decoder_4_to_16_1_out_7);
  and and_294 (and_294_out, Write_Enable, and_293_out);
  and and_295 (and_295_out, binary_decoder_4_to_16_2_1_out_14, binary_decoder_4_to_16_1_out_8);
  and and_296 (and_296_out, Write_Enable, and_295_out);
  and and_297 (and_297_out, binary_decoder_4_to_16_2_1_out_14, binary_decoder_4_to_16_1_out_9);
  and and_298 (and_298_out, Write_Enable, and_297_out);
  and and_299 (and_299_out, binary_decoder_4_to_16_2_1_out_14, binary_decoder_4_to_16_1_out_10);
  and and_300 (and_300_out, Write_Enable, and_299_out);
  and and_301 (and_301_out, binary_decoder_4_to_16_2_1_out_14, binary_decoder_4_to_16_1_out_11);
  and and_302 (and_302_out, Write_Enable, and_301_out);
  and and_303 (and_303_out, binary_decoder_4_to_16_2_1_out_14, binary_decoder_4_to_16_1_out_12);
  and and_304 (and_304_out, Write_Enable, and_303_out);
  and and_305 (and_305_out, binary_decoder_4_to_16_2_1_out_14, binary_decoder_4_to_16_1_out_13);
  and and_306 (and_306_out, Write_Enable, and_305_out);
  and and_307 (and_307_out, binary_decoder_4_to_16_2_1_out_14, binary_decoder_4_to_16_1_out_14);
  and and_308 (and_308_out, Write_Enable, and_307_out);
  and and_309 (and_309_out, binary_decoder_4_to_16_2_1_out_14, binary_decoder_4_to_16_1_out_15);
  and and_310 (and_310_out, Write_Enable, and_309_out);
  and and_311 (and_311_out, binary_decoder_4_to_16_2_1_out_14, binary_decoder_4_to_16_1_out_16);
  and and_312 (and_312_out, Write_Enable, and_311_out);
  and and_313 (and_313_out, binary_decoder_4_to_16_2_1_out_14, binary_decoder_4_to_16_1_out_17);
  and and_314 (and_314_out, Write_Enable, and_313_out);
  and and_315 (and_315_out, binary_decoder_4_to_16_2_1_out_14, binary_decoder_4_to_16_1_out_18);
  and and_316 (and_316_out, Write_Enable, and_315_out);
  and and_317 (and_317_out, binary_decoder_4_to_16_2_1_out_14, binary_decoder_4_to_16_1_out_19);
  and and_318 (and_318_out, Write_Enable, and_317_out);
  and and_319 (and_319_out, binary_decoder_4_to_16_2_1_out_14, binary_decoder_4_to_16_1_out_20);
  and and_320 (and_320_out, Write_Enable, and_319_out);
  assign Data_Out = and_321_out ? gated_latch_97_data_out : 1'bz;  // Controlled_Buffer controlled_buffer_97
  Gated_Latch gated_latch_97 (.Data_In(Data_In), .Write_Enable(and_290_out), .Data_Out(gated_latch_97_data_out));
  and and_321 (and_321_out, and_289_out, Read_Enable);
  assign Data_Out = and_322_out ? gated_latch_98_data_out : 1'bz;  // Controlled_Buffer controlled_buffer_98
  Gated_Latch gated_latch_98 (.Data_In(Data_In), .Write_Enable(and_292_out), .Data_Out(gated_latch_98_data_out));
  and and_322 (and_322_out, and_291_out, Read_Enable);
  assign Data_Out = and_323_out ? gated_latch_99_data_out : 1'bz;  // Controlled_Buffer controlled_buffer_99
  Gated_Latch gated_latch_99 (.Data_In(Data_In), .Write_Enable(and_294_out), .Data_Out(gated_latch_99_data_out));
  and and_323 (and_323_out, and_293_out, Read_Enable);
  assign Data_Out = and_324_out ? gated_latch_100_data_out : 1'bz;  // Controlled_Buffer controlled_buffer_100
  Gated_Latch gated_latch_100 (.Data_In(Data_In), .Write_Enable(and_296_out), .Data_Out(gated_latch_100_data_out));
  and and_324 (and_324_out, and_295_out, Read_Enable);
  assign Data_Out = and_325_out ? gated_latch_101_data_out : 1'bz;  // Controlled_Buffer controlled_buffer_101
  Gated_Latch gated_latch_101 (.Data_In(Data_In), .Write_Enable(and_298_out), .Data_Out(gated_latch_101_data_out));
  and and_325 (and_325_out, and_297_out, Read_Enable);
  assign Data_Out = and_326_out ? gated_latch_102_data_out : 1'bz;  // Controlled_Buffer controlled_buffer_102
  Gated_Latch gated_latch_102 (.Data_In(Data_In), .Write_Enable(and_300_out), .Data_Out(gated_latch_102_data_out));
  and and_326 (and_326_out, and_299_out, Read_Enable);
  assign Data_Out = and_327_out ? gated_latch_103_data_out : 1'bz;  // Controlled_Buffer controlled_buffer_103
  Gated_Latch gated_latch_103 (.Data_In(Data_In), .Write_Enable(and_302_out), .Data_Out(gated_latch_103_data_out));
  and and_327 (and_327_out, and_301_out, Read_Enable);
  assign Data_Out = and_328_out ? gated_latch_104_data_out : 1'bz;  // Controlled_Buffer controlled_buffer_104
  Gated_Latch gated_latch_104 (.Data_In(Data_In), .Write_Enable(and_304_out), .Data_Out(gated_latch_104_data_out));
  and and_328 (and_328_out, and_303_out, Read_Enable);
  assign Data_Out = and_329_out ? gated_latch_105_data_out : 1'bz;  // Controlled_Buffer controlled_buffer_105
  Gated_Latch gated_latch_105 (.Data_In(Data_In), .Write_Enable(and_306_out), .Data_Out(gated_latch_105_data_out));
  and and_329 (and_329_out, and_305_out, Read_Enable);
  assign Data_Out = and_330_out ? gated_latch_106_data_out : 1'bz;  // Controlled_Buffer controlled_buffer_106
  Gated_Latch gated_latch_106 (.Data_In(Data_In), .Write_Enable(and_308_out), .Data_Out(gated_latch_106_data_out));
  and and_330 (and_330_out, and_307_out, Read_Enable);
  assign Data_Out = and_331_out ? gated_latch_107_data_out : 1'bz;  // Controlled_Buffer controlled_buffer_107
  Gated_Latch gated_latch_107 (.Data_In(Data_In), .Write_Enable(and_310_out), .Data_Out(gated_latch_107_data_out));
  and and_331 (and_331_out, and_309_out, Read_Enable);
  assign Data_Out = and_332_out ? gated_latch_108_data_out : 1'bz;  // Controlled_Buffer controlled_buffer_108
  Gated_Latch gated_latch_108 (.Data_In(Data_In), .Write_Enable(and_312_out), .Data_Out(gated_latch_108_data_out));
  and and_332 (and_332_out, and_311_out, Read_Enable);
  assign Data_Out = and_333_out ? gated_latch_109_data_out : 1'bz;  // Controlled_Buffer controlled_buffer_109
  Gated_Latch gated_latch_109 (.Data_In(Data_In), .Write_Enable(and_314_out), .Data_Out(gated_latch_109_data_out));
  and and_333 (and_333_out, and_313_out, Read_Enable);
  assign Data_Out = and_334_out ? gated_latch_110_data_out : 1'bz;  // Controlled_Buffer controlled_buffer_110
  Gated_Latch gated_latch_110 (.Data_In(Data_In), .Write_Enable(and_316_out), .Data_Out(gated_latch_110_data_out));
  and and_334 (and_334_out, and_315_out, Read_Enable);
  assign Data_Out = and_335_out ? gated_latch_111_data_out : 1'bz;  // Controlled_Buffer controlled_buffer_111
  Gated_Latch gated_latch_111 (.Data_In(Data_In), .Write_Enable(and_318_out), .Data_Out(gated_latch_111_data_out));
  and and_335 (and_335_out, and_317_out, Read_Enable);
  assign Data_Out = and_336_out ? gated_latch_112_data_out : 1'bz;  // Controlled_Buffer controlled_buffer_112
  Gated_Latch gated_latch_112 (.Data_In(Data_In), .Write_Enable(and_320_out), .Data_Out(gated_latch_112_data_out));
  and and_336 (and_336_out, and_319_out, Read_Enable);
  and and_337 (and_337_out, binary_decoder_4_to_16_2_1_out_13, binary_decoder_4_to_16_1_out_5);
  and and_338 (and_338_out, Write_Enable, and_337_out);
  and and_339 (and_339_out, binary_decoder_4_to_16_2_1_out_13, binary_decoder_4_to_16_1_out_6);
  and and_340 (and_340_out, Write_Enable, and_339_out);
  and and_341 (and_341_out, binary_decoder_4_to_16_2_1_out_13, binary_decoder_4_to_16_1_out_7);
  and and_342 (and_342_out, Write_Enable, and_341_out);
  and and_343 (and_343_out, binary_decoder_4_to_16_2_1_out_13, binary_decoder_4_to_16_1_out_8);
  and and_344 (and_344_out, Write_Enable, and_343_out);
  and and_345 (and_345_out, binary_decoder_4_to_16_2_1_out_13, binary_decoder_4_to_16_1_out_9);
  and and_346 (and_346_out, Write_Enable, and_345_out);
  and and_347 (and_347_out, binary_decoder_4_to_16_2_1_out_13, binary_decoder_4_to_16_1_out_10);
  and and_348 (and_348_out, Write_Enable, and_347_out);
  and and_349 (and_349_out, binary_decoder_4_to_16_2_1_out_13, binary_decoder_4_to_16_1_out_11);
  and and_350 (and_350_out, Write_Enable, and_349_out);
  and and_351 (and_351_out, binary_decoder_4_to_16_2_1_out_13, binary_decoder_4_to_16_1_out_12);
  and and_352 (and_352_out, Write_Enable, and_351_out);
  and and_353 (and_353_out, binary_decoder_4_to_16_2_1_out_13, binary_decoder_4_to_16_1_out_13);
  and and_354 (and_354_out, Write_Enable, and_353_out);
  and and_355 (and_355_out, binary_decoder_4_to_16_2_1_out_13, binary_decoder_4_to_16_1_out_14);
  and and_356 (and_356_out, Write_Enable, and_355_out);
  and and_357 (and_357_out, binary_decoder_4_to_16_2_1_out_13, binary_decoder_4_to_16_1_out_15);
  and and_358 (and_358_out, Write_Enable, and_357_out);
  and and_359 (and_359_out, binary_decoder_4_to_16_2_1_out_13, binary_decoder_4_to_16_1_out_16);
  and and_360 (and_360_out, Write_Enable, and_359_out);
  and and_361 (and_361_out, binary_decoder_4_to_16_2_1_out_13, binary_decoder_4_to_16_1_out_17);
  and and_362 (and_362_out, Write_Enable, and_361_out);
  and and_363 (and_363_out, binary_decoder_4_to_16_2_1_out_13, binary_decoder_4_to_16_1_out_18);
  and and_364 (and_364_out, Write_Enable, and_363_out);
  and and_365 (and_365_out, binary_decoder_4_to_16_2_1_out_13, binary_decoder_4_to_16_1_out_19);
  and and_366 (and_366_out, Write_Enable, and_365_out);
  and and_367 (and_367_out, binary_decoder_4_to_16_2_1_out_13, binary_decoder_4_to_16_1_out_20);
  and and_368 (and_368_out, Write_Enable, and_367_out);
  assign Data_Out = and_369_out ? gated_latch_113_data_out : 1'bz;  // Controlled_Buffer controlled_buffer_113
  Gated_Latch gated_latch_113 (.Data_In(Data_In), .Write_Enable(and_338_out), .Data_Out(gated_latch_113_data_out));
  and and_369 (and_369_out, and_337_out, Read_Enable);
  assign Data_Out = and_370_out ? gated_latch_114_data_out : 1'bz;  // Controlled_Buffer controlled_buffer_114
  Gated_Latch gated_latch_114 (.Data_In(Data_In), .Write_Enable(and_340_out), .Data_Out(gated_latch_114_data_out));
  and and_370 (and_370_out, and_339_out, Read_Enable);
  assign Data_Out = and_371_out ? gated_latch_115_data_out : 1'bz;  // Controlled_Buffer controlled_buffer_115
  Gated_Latch gated_latch_115 (.Data_In(Data_In), .Write_Enable(and_342_out), .Data_Out(gated_latch_115_data_out));
  and and_371 (and_371_out, and_341_out, Read_Enable);
  assign Data_Out = and_372_out ? gated_latch_116_data_out : 1'bz;  // Controlled_Buffer controlled_buffer_116
  Gated_Latch gated_latch_116 (.Data_In(Data_In), .Write_Enable(and_344_out), .Data_Out(gated_latch_116_data_out));
  and and_372 (and_372_out, and_343_out, Read_Enable);
  assign Data_Out = and_373_out ? gated_latch_117_data_out : 1'bz;  // Controlled_Buffer controlled_buffer_117
  Gated_Latch gated_latch_117 (.Data_In(Data_In), .Write_Enable(and_346_out), .Data_Out(gated_latch_117_data_out));
  and and_373 (and_373_out, and_345_out, Read_Enable);
  assign Data_Out = and_374_out ? gated_latch_118_data_out : 1'bz;  // Controlled_Buffer controlled_buffer_118
  Gated_Latch gated_latch_118 (.Data_In(Data_In), .Write_Enable(and_348_out), .Data_Out(gated_latch_118_data_out));
  and and_374 (and_374_out, and_347_out, Read_Enable);
  assign Data_Out = and_375_out ? gated_latch_119_data_out : 1'bz;  // Controlled_Buffer controlled_buffer_119
  Gated_Latch gated_latch_119 (.Data_In(Data_In), .Write_Enable(and_350_out), .Data_Out(gated_latch_119_data_out));
  and and_375 (and_375_out, and_349_out, Read_Enable);
  assign Data_Out = and_376_out ? gated_latch_120_data_out : 1'bz;  // Controlled_Buffer controlled_buffer_120
  Gated_Latch gated_latch_120 (.Data_In(Data_In), .Write_Enable(and_352_out), .Data_Out(gated_latch_120_data_out));
  and and_376 (and_376_out, and_351_out, Read_Enable);
  assign Data_Out = and_377_out ? gated_latch_121_data_out : 1'bz;  // Controlled_Buffer controlled_buffer_121
  Gated_Latch gated_latch_121 (.Data_In(Data_In), .Write_Enable(and_354_out), .Data_Out(gated_latch_121_data_out));
  and and_377 (and_377_out, and_353_out, Read_Enable);
  assign Data_Out = and_378_out ? gated_latch_122_data_out : 1'bz;  // Controlled_Buffer controlled_buffer_122
  Gated_Latch gated_latch_122 (.Data_In(Data_In), .Write_Enable(and_356_out), .Data_Out(gated_latch_122_data_out));
  and and_378 (and_378_out, and_355_out, Read_Enable);
  assign Data_Out = and_379_out ? gated_latch_123_data_out : 1'bz;  // Controlled_Buffer controlled_buffer_123
  Gated_Latch gated_latch_123 (.Data_In(Data_In), .Write_Enable(and_358_out), .Data_Out(gated_latch_123_data_out));
  and and_379 (and_379_out, and_357_out, Read_Enable);
  assign Data_Out = and_380_out ? gated_latch_124_data_out : 1'bz;  // Controlled_Buffer controlled_buffer_124
  Gated_Latch gated_latch_124 (.Data_In(Data_In), .Write_Enable(and_360_out), .Data_Out(gated_latch_124_data_out));
  and and_380 (and_380_out, and_359_out, Read_Enable);
  assign Data_Out = and_381_out ? gated_latch_125_data_out : 1'bz;  // Controlled_Buffer controlled_buffer_125
  Gated_Latch gated_latch_125 (.Data_In(Data_In), .Write_Enable(and_362_out), .Data_Out(gated_latch_125_data_out));
  and and_381 (and_381_out, and_361_out, Read_Enable);
  assign Data_Out = and_382_out ? gated_latch_126_data_out : 1'bz;  // Controlled_Buffer controlled_buffer_126
  Gated_Latch gated_latch_126 (.Data_In(Data_In), .Write_Enable(and_364_out), .Data_Out(gated_latch_126_data_out));
  and and_382 (and_382_out, and_363_out, Read_Enable);
  assign Data_Out = and_383_out ? gated_latch_127_data_out : 1'bz;  // Controlled_Buffer controlled_buffer_127
  Gated_Latch gated_latch_127 (.Data_In(Data_In), .Write_Enable(and_366_out), .Data_Out(gated_latch_127_data_out));
  and and_383 (and_383_out, and_365_out, Read_Enable);
  assign Data_Out = and_384_out ? gated_latch_128_data_out : 1'bz;  // Controlled_Buffer controlled_buffer_128
  Gated_Latch gated_latch_128 (.Data_In(Data_In), .Write_Enable(and_368_out), .Data_Out(gated_latch_128_data_out));
  and and_384 (and_384_out, and_367_out, Read_Enable);
  and and_385 (and_385_out, binary_decoder_4_to_16_2_1_out_12, binary_decoder_4_to_16_1_out_5);
  and and_386 (and_386_out, binary_decoder_4_to_16_2_1_out_12, binary_decoder_4_to_16_1_out_6);
  and and_387 (and_387_out, binary_decoder_4_to_16_2_1_out_12, binary_decoder_4_to_16_1_out_7);
  and and_388 (and_388_out, binary_decoder_4_to_16_2_1_out_12, binary_decoder_4_to_16_1_out_8);
  and and_389 (and_389_out, binary_decoder_4_to_16_2_1_out_12, binary_decoder_4_to_16_1_out_9);
  and and_390 (and_390_out, binary_decoder_4_to_16_2_1_out_12, binary_decoder_4_to_16_1_out_10);
  and and_391 (and_391_out, binary_decoder_4_to_16_2_1_out_12, binary_decoder_4_to_16_1_out_11);
  and and_392 (and_392_out, binary_decoder_4_to_16_2_1_out_12, binary_decoder_4_to_16_1_out_12);
  and and_393 (and_393_out, binary_decoder_4_to_16_2_1_out_12, binary_decoder_4_to_16_1_out_13);
  and and_394 (and_394_out, binary_decoder_4_to_16_2_1_out_12, binary_decoder_4_to_16_1_out_14);
  and and_395 (and_395_out, binary_decoder_4_to_16_2_1_out_12, binary_decoder_4_to_16_1_out_15);
  and and_396 (and_396_out, binary_decoder_4_to_16_2_1_out_12, binary_decoder_4_to_16_1_out_16);
  and and_397 (and_397_out, binary_decoder_4_to_16_2_1_out_12, binary_decoder_4_to_16_1_out_17);
  and and_398 (and_398_out, binary_decoder_4_to_16_2_1_out_12, binary_decoder_4_to_16_1_out_18);
  and and_399 (and_399_out, binary_decoder_4_to_16_2_1_out_12, binary_decoder_4_to_16_1_out_19);
  and and_400 (and_400_out, binary_decoder_4_to_16_2_1_out_12, binary_decoder_4_to_16_1_out_20);
  and and_401 (and_401_out, Write_Enable, and_385_out);
  and and_402 (and_402_out, Write_Enable, and_386_out);
  and and_403 (and_403_out, Write_Enable, and_387_out);
  and and_404 (and_404_out, Write_Enable, and_388_out);
  and and_405 (and_405_out, Write_Enable, and_389_out);
  and and_406 (and_406_out, Write_Enable, and_390_out);
  and and_407 (and_407_out, Write_Enable, and_391_out);
  and and_408 (and_408_out, Write_Enable, and_392_out);
  and and_409 (and_409_out, Write_Enable, and_393_out);
  and and_410 (and_410_out, Write_Enable, and_394_out);
  and and_411 (and_411_out, Write_Enable, and_395_out);
  and and_412 (and_412_out, Write_Enable, and_396_out);
  and and_413 (and_413_out, Write_Enable, and_397_out);
  and and_414 (and_414_out, Write_Enable, and_398_out);
  and and_415 (and_415_out, Write_Enable, and_399_out);
  and and_416 (and_416_out, Write_Enable, and_400_out);
  Gated_Latch gated_latch_129 (.Data_In(Data_In), .Write_Enable(and_401_out), .Data_Out(gated_latch_129_data_out));
  and and_417 (and_417_out, and_385_out, Read_Enable);
  Gated_Latch gated_latch_130 (.Data_In(Data_In), .Write_Enable(and_402_out), .Data_Out(gated_latch_130_data_out));
  and and_418 (and_418_out, and_386_out, Read_Enable);
  Gated_Latch gated_latch_131 (.Data_In(Data_In), .Write_Enable(and_403_out), .Data_Out(gated_latch_131_data_out));
  and and_419 (and_419_out, and_387_out, Read_Enable);
  Gated_Latch gated_latch_132 (.Data_In(Data_In), .Write_Enable(and_404_out), .Data_Out(gated_latch_132_data_out));
  and and_420 (and_420_out, and_388_out, Read_Enable);
  Gated_Latch gated_latch_133 (.Data_In(Data_In), .Write_Enable(and_405_out), .Data_Out(gated_latch_133_data_out));
  and and_421 (and_421_out, and_389_out, Read_Enable);
  Gated_Latch gated_latch_134 (.Data_In(Data_In), .Write_Enable(and_406_out), .Data_Out(gated_latch_134_data_out));
  and and_422 (and_422_out, and_390_out, Read_Enable);
  Gated_Latch gated_latch_135 (.Data_In(Data_In), .Write_Enable(and_407_out), .Data_Out(gated_latch_135_data_out));
  and and_423 (and_423_out, and_391_out, Read_Enable);
  Gated_Latch gated_latch_136 (.Data_In(Data_In), .Write_Enable(and_408_out), .Data_Out(gated_latch_136_data_out));
  and and_424 (and_424_out, and_392_out, Read_Enable);
  Gated_Latch gated_latch_137 (.Data_In(Data_In), .Write_Enable(and_409_out), .Data_Out(gated_latch_137_data_out));
  and and_425 (and_425_out, and_393_out, Read_Enable);
  Gated_Latch gated_latch_138 (.Data_In(Data_In), .Write_Enable(and_410_out), .Data_Out(gated_latch_138_data_out));
  and and_426 (and_426_out, and_394_out, Read_Enable);
  Gated_Latch gated_latch_139 (.Data_In(Data_In), .Write_Enable(and_411_out), .Data_Out(gated_latch_139_data_out));
  and and_427 (and_427_out, and_395_out, Read_Enable);
  Gated_Latch gated_latch_140 (.Data_In(Data_In), .Write_Enable(and_412_out), .Data_Out(gated_latch_140_data_out));
  and and_428 (and_428_out, and_396_out, Read_Enable);
  Gated_Latch gated_latch_141 (.Data_In(Data_In), .Write_Enable(and_413_out), .Data_Out(gated_latch_141_data_out));
  and and_429 (and_429_out, and_397_out, Read_Enable);
  Gated_Latch gated_latch_142 (.Data_In(Data_In), .Write_Enable(and_414_out), .Data_Out(gated_latch_142_data_out));
  and and_430 (and_430_out, and_398_out, Read_Enable);
  Gated_Latch gated_latch_143 (.Data_In(Data_In), .Write_Enable(and_415_out), .Data_Out(gated_latch_143_data_out));
  and and_431 (and_431_out, and_399_out, Read_Enable);
  Gated_Latch gated_latch_144 (.Data_In(Data_In), .Write_Enable(and_416_out), .Data_Out(gated_latch_144_data_out));
  and and_432 (and_432_out, and_400_out, Read_Enable);
  assign Data_Out = and_417_out ? gated_latch_129_data_out : 1'bz;  // Controlled_Buffer controlled_buffer_129
  assign Data_Out = and_418_out ? gated_latch_130_data_out : 1'bz;  // Controlled_Buffer controlled_buffer_130
  assign Data_Out = and_419_out ? gated_latch_131_data_out : 1'bz;  // Controlled_Buffer controlled_buffer_131
  assign Data_Out = and_420_out ? gated_latch_132_data_out : 1'bz;  // Controlled_Buffer controlled_buffer_132
  assign Data_Out = and_421_out ? gated_latch_133_data_out : 1'bz;  // Controlled_Buffer controlled_buffer_133
  assign Data_Out = and_422_out ? gated_latch_134_data_out : 1'bz;  // Controlled_Buffer controlled_buffer_134
  assign Data_Out = and_423_out ? gated_latch_135_data_out : 1'bz;  // Controlled_Buffer controlled_buffer_135
  assign Data_Out = and_424_out ? gated_latch_136_data_out : 1'bz;  // Controlled_Buffer controlled_buffer_136
  assign Data_Out = and_425_out ? gated_latch_137_data_out : 1'bz;  // Controlled_Buffer controlled_buffer_137
  assign Data_Out = and_426_out ? gated_latch_138_data_out : 1'bz;  // Controlled_Buffer controlled_buffer_138
  assign Data_Out = and_427_out ? gated_latch_139_data_out : 1'bz;  // Controlled_Buffer controlled_buffer_139
  assign Data_Out = and_428_out ? gated_latch_140_data_out : 1'bz;  // Controlled_Buffer controlled_buffer_140
  assign Data_Out = and_429_out ? gated_latch_141_data_out : 1'bz;  // Controlled_Buffer controlled_buffer_141
  assign Data_Out = and_430_out ? gated_latch_142_data_out : 1'bz;  // Controlled_Buffer controlled_buffer_142
  assign Data_Out = and_431_out ? gated_latch_143_data_out : 1'bz;  // Controlled_Buffer controlled_buffer_143
  assign Data_Out = and_432_out ? gated_latch_144_data_out : 1'bz;  // Controlled_Buffer controlled_buffer_144
  and and_433 (and_433_out, binary_decoder_4_to_16_2_1_out_11, binary_decoder_4_to_16_1_out_5);
  and and_434 (and_434_out, binary_decoder_4_to_16_2_1_out_11, binary_decoder_4_to_16_1_out_6);
  and and_435 (and_435_out, binary_decoder_4_to_16_2_1_out_11, binary_decoder_4_to_16_1_out_7);
  and and_436 (and_436_out, binary_decoder_4_to_16_2_1_out_11, binary_decoder_4_to_16_1_out_8);
  and and_437 (and_437_out, binary_decoder_4_to_16_2_1_out_11, binary_decoder_4_to_16_1_out_9);
  and and_438 (and_438_out, binary_decoder_4_to_16_2_1_out_11, binary_decoder_4_to_16_1_out_10);
  and and_439 (and_439_out, binary_decoder_4_to_16_2_1_out_11, binary_decoder_4_to_16_1_out_11);
  and and_440 (and_440_out, binary_decoder_4_to_16_2_1_out_11, binary_decoder_4_to_16_1_out_12);
  and and_441 (and_441_out, binary_decoder_4_to_16_2_1_out_11, binary_decoder_4_to_16_1_out_13);
  and and_442 (and_442_out, binary_decoder_4_to_16_2_1_out_11, binary_decoder_4_to_16_1_out_14);
  and and_443 (and_443_out, binary_decoder_4_to_16_2_1_out_11, binary_decoder_4_to_16_1_out_15);
  and and_444 (and_444_out, binary_decoder_4_to_16_2_1_out_11, binary_decoder_4_to_16_1_out_16);
  and and_445 (and_445_out, binary_decoder_4_to_16_2_1_out_11, binary_decoder_4_to_16_1_out_17);
  and and_446 (and_446_out, binary_decoder_4_to_16_2_1_out_11, binary_decoder_4_to_16_1_out_18);
  and and_447 (and_447_out, binary_decoder_4_to_16_2_1_out_11, binary_decoder_4_to_16_1_out_19);
  and and_448 (and_448_out, binary_decoder_4_to_16_2_1_out_11, binary_decoder_4_to_16_1_out_20);
  and and_449 (and_449_out, Write_Enable, and_433_out);
  and and_450 (and_450_out, Write_Enable, and_434_out);
  and and_451 (and_451_out, Write_Enable, and_435_out);
  and and_452 (and_452_out, Write_Enable, and_436_out);
  and and_453 (and_453_out, Write_Enable, and_437_out);
  and and_454 (and_454_out, Write_Enable, and_438_out);
  and and_455 (and_455_out, Write_Enable, and_439_out);
  and and_456 (and_456_out, Write_Enable, and_440_out);
  and and_457 (and_457_out, Write_Enable, and_441_out);
  and and_458 (and_458_out, Write_Enable, and_442_out);
  and and_459 (and_459_out, Write_Enable, and_443_out);
  and and_460 (and_460_out, Write_Enable, and_444_out);
  and and_461 (and_461_out, Write_Enable, and_445_out);
  and and_462 (and_462_out, Write_Enable, and_446_out);
  and and_463 (and_463_out, Write_Enable, and_447_out);
  and and_464 (and_464_out, Write_Enable, and_448_out);
  Gated_Latch gated_latch_145 (.Data_In(Data_In), .Write_Enable(and_449_out), .Data_Out(gated_latch_145_data_out));
  Gated_Latch gated_latch_146 (.Data_In(Data_In), .Write_Enable(and_450_out), .Data_Out(gated_latch_146_data_out));
  Gated_Latch gated_latch_147 (.Data_In(Data_In), .Write_Enable(and_451_out), .Data_Out(gated_latch_147_data_out));
  Gated_Latch gated_latch_148 (.Data_In(Data_In), .Write_Enable(and_452_out), .Data_Out(gated_latch_148_data_out));
  Gated_Latch gated_latch_149 (.Data_In(Data_In), .Write_Enable(and_453_out), .Data_Out(gated_latch_149_data_out));
  Gated_Latch gated_latch_150 (.Data_In(Data_In), .Write_Enable(and_454_out), .Data_Out(gated_latch_150_data_out));
  Gated_Latch gated_latch_151 (.Data_In(Data_In), .Write_Enable(and_455_out), .Data_Out(gated_latch_151_data_out));
  Gated_Latch gated_latch_152 (.Data_In(Data_In), .Write_Enable(and_456_out), .Data_Out(gated_latch_152_data_out));
  Gated_Latch gated_latch_153 (.Data_In(Data_In), .Write_Enable(and_457_out), .Data_Out(gated_latch_153_data_out));
  Gated_Latch gated_latch_154 (.Data_In(Data_In), .Write_Enable(and_458_out), .Data_Out(gated_latch_154_data_out));
  Gated_Latch gated_latch_155 (.Data_In(Data_In), .Write_Enable(and_459_out), .Data_Out(gated_latch_155_data_out));
  Gated_Latch gated_latch_156 (.Data_In(Data_In), .Write_Enable(and_460_out), .Data_Out(gated_latch_156_data_out));
  Gated_Latch gated_latch_157 (.Data_In(Data_In), .Write_Enable(and_461_out), .Data_Out(gated_latch_157_data_out));
  Gated_Latch gated_latch_158 (.Data_In(Data_In), .Write_Enable(and_462_out), .Data_Out(gated_latch_158_data_out));
  Gated_Latch gated_latch_159 (.Data_In(Data_In), .Write_Enable(and_463_out), .Data_Out(gated_latch_159_data_out));
  Gated_Latch gated_latch_160 (.Data_In(Data_In), .Write_Enable(and_464_out), .Data_Out(gated_latch_160_data_out));
  assign Data_Out = and_465_out ? gated_latch_145_data_out : 1'bz;  // Controlled_Buffer controlled_buffer_145
  and and_465 (and_465_out, and_433_out, Read_Enable);
  assign Data_Out = and_466_out ? gated_latch_146_data_out : 1'bz;  // Controlled_Buffer controlled_buffer_146
  and and_466 (and_466_out, and_434_out, Read_Enable);
  assign Data_Out = and_467_out ? gated_latch_147_data_out : 1'bz;  // Controlled_Buffer controlled_buffer_147
  and and_467 (and_467_out, and_435_out, Read_Enable);
  assign Data_Out = and_468_out ? gated_latch_148_data_out : 1'bz;  // Controlled_Buffer controlled_buffer_148
  and and_468 (and_468_out, and_436_out, Read_Enable);
  assign Data_Out = and_469_out ? gated_latch_149_data_out : 1'bz;  // Controlled_Buffer controlled_buffer_149
  and and_469 (and_469_out, and_437_out, Read_Enable);
  assign Data_Out = and_470_out ? gated_latch_150_data_out : 1'bz;  // Controlled_Buffer controlled_buffer_150
  and and_470 (and_470_out, and_438_out, Read_Enable);
  assign Data_Out = and_471_out ? gated_latch_151_data_out : 1'bz;  // Controlled_Buffer controlled_buffer_151
  and and_471 (and_471_out, and_439_out, Read_Enable);
  assign Data_Out = and_472_out ? gated_latch_152_data_out : 1'bz;  // Controlled_Buffer controlled_buffer_152
  and and_472 (and_472_out, and_440_out, Read_Enable);
  assign Data_Out = and_473_out ? gated_latch_153_data_out : 1'bz;  // Controlled_Buffer controlled_buffer_153
  and and_473 (and_473_out, and_441_out, Read_Enable);
  assign Data_Out = and_474_out ? gated_latch_154_data_out : 1'bz;  // Controlled_Buffer controlled_buffer_154
  and and_474 (and_474_out, and_442_out, Read_Enable);
  assign Data_Out = and_475_out ? gated_latch_155_data_out : 1'bz;  // Controlled_Buffer controlled_buffer_155
  and and_475 (and_475_out, and_443_out, Read_Enable);
  assign Data_Out = and_476_out ? gated_latch_156_data_out : 1'bz;  // Controlled_Buffer controlled_buffer_156
  and and_476 (and_476_out, and_444_out, Read_Enable);
  assign Data_Out = and_477_out ? gated_latch_157_data_out : 1'bz;  // Controlled_Buffer controlled_buffer_157
  and and_477 (and_477_out, and_445_out, Read_Enable);
  assign Data_Out = and_478_out ? gated_latch_158_data_out : 1'bz;  // Controlled_Buffer controlled_buffer_158
  and and_478 (and_478_out, and_446_out, Read_Enable);
  assign Data_Out = and_479_out ? gated_latch_159_data_out : 1'bz;  // Controlled_Buffer controlled_buffer_159
  and and_479 (and_479_out, and_447_out, Read_Enable);
  assign Data_Out = and_480_out ? gated_latch_160_data_out : 1'bz;  // Controlled_Buffer controlled_buffer_160
  and and_480 (and_480_out, and_448_out, Read_Enable);
  and and_481 (and_481_out, binary_decoder_4_to_16_2_1_out_10, binary_decoder_4_to_16_1_out_5);
  and and_482 (and_482_out, binary_decoder_4_to_16_2_1_out_10, binary_decoder_4_to_16_1_out_6);
  and and_483 (and_483_out, binary_decoder_4_to_16_2_1_out_10, binary_decoder_4_to_16_1_out_7);
  and and_484 (and_484_out, binary_decoder_4_to_16_2_1_out_10, binary_decoder_4_to_16_1_out_8);
  and and_485 (and_485_out, binary_decoder_4_to_16_2_1_out_10, binary_decoder_4_to_16_1_out_9);
  and and_486 (and_486_out, binary_decoder_4_to_16_2_1_out_10, binary_decoder_4_to_16_1_out_10);
  and and_487 (and_487_out, binary_decoder_4_to_16_2_1_out_10, binary_decoder_4_to_16_1_out_11);
  and and_488 (and_488_out, binary_decoder_4_to_16_2_1_out_10, binary_decoder_4_to_16_1_out_12);
  and and_489 (and_489_out, binary_decoder_4_to_16_2_1_out_10, binary_decoder_4_to_16_1_out_13);
  and and_490 (and_490_out, binary_decoder_4_to_16_2_1_out_10, binary_decoder_4_to_16_1_out_14);
  and and_491 (and_491_out, binary_decoder_4_to_16_2_1_out_10, binary_decoder_4_to_16_1_out_15);
  and and_492 (and_492_out, binary_decoder_4_to_16_2_1_out_10, binary_decoder_4_to_16_1_out_16);
  and and_493 (and_493_out, binary_decoder_4_to_16_2_1_out_10, binary_decoder_4_to_16_1_out_17);
  and and_494 (and_494_out, binary_decoder_4_to_16_2_1_out_10, binary_decoder_4_to_16_1_out_18);
  and and_495 (and_495_out, binary_decoder_4_to_16_2_1_out_10, binary_decoder_4_to_16_1_out_19);
  and and_496 (and_496_out, binary_decoder_4_to_16_2_1_out_10, binary_decoder_4_to_16_1_out_20);
  and and_497 (and_497_out, Write_Enable, and_481_out);
  and and_498 (and_498_out, Write_Enable, and_482_out);
  and and_499 (and_499_out, Write_Enable, and_483_out);
  and and_500 (and_500_out, Write_Enable, and_484_out);
  and and_501 (and_501_out, Write_Enable, and_485_out);
  and and_502 (and_502_out, Write_Enable, and_486_out);
  and and_503 (and_503_out, Write_Enable, and_487_out);
  and and_504 (and_504_out, Write_Enable, and_488_out);
  and and_505 (and_505_out, Write_Enable, and_489_out);
  and and_506 (and_506_out, Write_Enable, and_490_out);
  and and_507 (and_507_out, Write_Enable, and_491_out);
  and and_508 (and_508_out, Write_Enable, and_492_out);
  and and_509 (and_509_out, Write_Enable, and_493_out);
  and and_510 (and_510_out, Write_Enable, and_494_out);
  and and_511 (and_511_out, Write_Enable, and_495_out);
  and and_512 (and_512_out, Write_Enable, and_496_out);
  Gated_Latch gated_latch_161 (.Data_In(Data_In), .Write_Enable(and_497_out), .Data_Out(gated_latch_161_data_out));
  Gated_Latch gated_latch_162 (.Data_In(Data_In), .Write_Enable(and_498_out), .Data_Out(gated_latch_162_data_out));
  Gated_Latch gated_latch_163 (.Data_In(Data_In), .Write_Enable(and_499_out), .Data_Out(gated_latch_163_data_out));
  Gated_Latch gated_latch_164 (.Data_In(Data_In), .Write_Enable(and_500_out), .Data_Out(gated_latch_164_data_out));
  Gated_Latch gated_latch_165 (.Data_In(Data_In), .Write_Enable(and_501_out), .Data_Out(gated_latch_165_data_out));
  Gated_Latch gated_latch_166 (.Data_In(Data_In), .Write_Enable(and_502_out), .Data_Out(gated_latch_166_data_out));
  Gated_Latch gated_latch_167 (.Data_In(Data_In), .Write_Enable(and_503_out), .Data_Out(gated_latch_167_data_out));
  Gated_Latch gated_latch_168 (.Data_In(Data_In), .Write_Enable(and_504_out), .Data_Out(gated_latch_168_data_out));
  Gated_Latch gated_latch_169 (.Data_In(Data_In), .Write_Enable(and_505_out), .Data_Out(gated_latch_169_data_out));
  Gated_Latch gated_latch_170 (.Data_In(Data_In), .Write_Enable(and_506_out), .Data_Out(gated_latch_170_data_out));
  Gated_Latch gated_latch_171 (.Data_In(Data_In), .Write_Enable(and_507_out), .Data_Out(gated_latch_171_data_out));
  Gated_Latch gated_latch_172 (.Data_In(Data_In), .Write_Enable(and_508_out), .Data_Out(gated_latch_172_data_out));
  Gated_Latch gated_latch_173 (.Data_In(Data_In), .Write_Enable(and_509_out), .Data_Out(gated_latch_173_data_out));
  Gated_Latch gated_latch_174 (.Data_In(Data_In), .Write_Enable(and_510_out), .Data_Out(gated_latch_174_data_out));
  Gated_Latch gated_latch_175 (.Data_In(Data_In), .Write_Enable(and_511_out), .Data_Out(gated_latch_175_data_out));
  Gated_Latch gated_latch_176 (.Data_In(Data_In), .Write_Enable(and_512_out), .Data_Out(gated_latch_176_data_out));
  assign Data_Out = and_513_out ? gated_latch_161_data_out : 1'bz;  // Controlled_Buffer controlled_buffer_161
  and and_513 (and_513_out, and_481_out, Read_Enable);
  assign Data_Out = and_514_out ? gated_latch_162_data_out : 1'bz;  // Controlled_Buffer controlled_buffer_162
  and and_514 (and_514_out, and_482_out, Read_Enable);
  assign Data_Out = and_515_out ? gated_latch_163_data_out : 1'bz;  // Controlled_Buffer controlled_buffer_163
  and and_515 (and_515_out, and_483_out, Read_Enable);
  assign Data_Out = and_516_out ? gated_latch_164_data_out : 1'bz;  // Controlled_Buffer controlled_buffer_164
  and and_516 (and_516_out, and_484_out, Read_Enable);
  assign Data_Out = and_517_out ? gated_latch_165_data_out : 1'bz;  // Controlled_Buffer controlled_buffer_165
  and and_517 (and_517_out, and_485_out, Read_Enable);
  assign Data_Out = and_518_out ? gated_latch_166_data_out : 1'bz;  // Controlled_Buffer controlled_buffer_166
  and and_518 (and_518_out, and_486_out, Read_Enable);
  assign Data_Out = and_519_out ? gated_latch_167_data_out : 1'bz;  // Controlled_Buffer controlled_buffer_167
  and and_519 (and_519_out, and_487_out, Read_Enable);
  assign Data_Out = and_520_out ? gated_latch_168_data_out : 1'bz;  // Controlled_Buffer controlled_buffer_168
  and and_520 (and_520_out, and_488_out, Read_Enable);
  assign Data_Out = and_521_out ? gated_latch_169_data_out : 1'bz;  // Controlled_Buffer controlled_buffer_169
  and and_521 (and_521_out, and_489_out, Read_Enable);
  assign Data_Out = and_522_out ? gated_latch_170_data_out : 1'bz;  // Controlled_Buffer controlled_buffer_170
  and and_522 (and_522_out, and_490_out, Read_Enable);
  assign Data_Out = and_523_out ? gated_latch_171_data_out : 1'bz;  // Controlled_Buffer controlled_buffer_171
  and and_523 (and_523_out, and_491_out, Read_Enable);
  assign Data_Out = and_524_out ? gated_latch_172_data_out : 1'bz;  // Controlled_Buffer controlled_buffer_172
  and and_524 (and_524_out, and_492_out, Read_Enable);
  assign Data_Out = and_525_out ? gated_latch_173_data_out : 1'bz;  // Controlled_Buffer controlled_buffer_173
  and and_525 (and_525_out, and_493_out, Read_Enable);
  assign Data_Out = and_526_out ? gated_latch_174_data_out : 1'bz;  // Controlled_Buffer controlled_buffer_174
  and and_526 (and_526_out, and_494_out, Read_Enable);
  assign Data_Out = and_527_out ? gated_latch_175_data_out : 1'bz;  // Controlled_Buffer controlled_buffer_175
  and and_527 (and_527_out, and_495_out, Read_Enable);
  assign Data_Out = and_528_out ? gated_latch_176_data_out : 1'bz;  // Controlled_Buffer controlled_buffer_176
  and and_528 (and_528_out, and_496_out, Read_Enable);
  and and_529 (and_529_out, binary_decoder_4_to_16_2_1_out_9, binary_decoder_4_to_16_1_out_5);
  and and_530 (and_530_out, binary_decoder_4_to_16_2_1_out_9, binary_decoder_4_to_16_1_out_6);
  and and_531 (and_531_out, binary_decoder_4_to_16_2_1_out_9, binary_decoder_4_to_16_1_out_7);
  and and_532 (and_532_out, binary_decoder_4_to_16_2_1_out_9, binary_decoder_4_to_16_1_out_8);
  and and_533 (and_533_out, binary_decoder_4_to_16_2_1_out_9, binary_decoder_4_to_16_1_out_9);
  and and_534 (and_534_out, binary_decoder_4_to_16_2_1_out_9, binary_decoder_4_to_16_1_out_10);
  and and_535 (and_535_out, binary_decoder_4_to_16_2_1_out_9, binary_decoder_4_to_16_1_out_11);
  and and_536 (and_536_out, binary_decoder_4_to_16_2_1_out_9, binary_decoder_4_to_16_1_out_12);
  and and_537 (and_537_out, binary_decoder_4_to_16_2_1_out_9, binary_decoder_4_to_16_1_out_13);
  and and_538 (and_538_out, binary_decoder_4_to_16_2_1_out_9, binary_decoder_4_to_16_1_out_14);
  and and_539 (and_539_out, binary_decoder_4_to_16_2_1_out_9, binary_decoder_4_to_16_1_out_15);
  and and_540 (and_540_out, binary_decoder_4_to_16_2_1_out_9, binary_decoder_4_to_16_1_out_16);
  and and_541 (and_541_out, binary_decoder_4_to_16_2_1_out_9, binary_decoder_4_to_16_1_out_17);
  and and_542 (and_542_out, binary_decoder_4_to_16_2_1_out_9, binary_decoder_4_to_16_1_out_18);
  and and_543 (and_543_out, binary_decoder_4_to_16_2_1_out_9, binary_decoder_4_to_16_1_out_19);
  and and_544 (and_544_out, binary_decoder_4_to_16_2_1_out_9, binary_decoder_4_to_16_1_out_20);
  and and_545 (and_545_out, Write_Enable, and_529_out);
  and and_546 (and_546_out, Write_Enable, and_530_out);
  and and_547 (and_547_out, Write_Enable, and_531_out);
  and and_548 (and_548_out, Write_Enable, and_532_out);
  and and_549 (and_549_out, Write_Enable, and_533_out);
  and and_550 (and_550_out, Write_Enable, and_534_out);
  and and_551 (and_551_out, Write_Enable, and_535_out);
  and and_552 (and_552_out, Write_Enable, and_536_out);
  and and_553 (and_553_out, Write_Enable, and_537_out);
  and and_554 (and_554_out, Write_Enable, and_538_out);
  and and_555 (and_555_out, Write_Enable, and_539_out);
  and and_556 (and_556_out, Write_Enable, and_540_out);
  and and_557 (and_557_out, Write_Enable, and_541_out);
  and and_558 (and_558_out, Write_Enable, and_542_out);
  and and_559 (and_559_out, Write_Enable, and_543_out);
  and and_560 (and_560_out, Write_Enable, and_544_out);
  assign Data_Out = and_561_out ? gated_latch_177_data_out : 1'bz;  // Controlled_Buffer controlled_buffer_177
  Gated_Latch gated_latch_177 (.Data_In(Data_In), .Write_Enable(and_545_out), .Data_Out(gated_latch_177_data_out));
  and and_561 (and_561_out, and_529_out, Read_Enable);
  assign Data_Out = and_562_out ? gated_latch_178_data_out : 1'bz;  // Controlled_Buffer controlled_buffer_178
  Gated_Latch gated_latch_178 (.Data_In(Data_In), .Write_Enable(and_546_out), .Data_Out(gated_latch_178_data_out));
  and and_562 (and_562_out, and_530_out, Read_Enable);
  assign Data_Out = and_563_out ? gated_latch_179_data_out : 1'bz;  // Controlled_Buffer controlled_buffer_179
  Gated_Latch gated_latch_179 (.Data_In(Data_In), .Write_Enable(and_547_out), .Data_Out(gated_latch_179_data_out));
  and and_563 (and_563_out, and_531_out, Read_Enable);
  assign Data_Out = and_564_out ? gated_latch_180_data_out : 1'bz;  // Controlled_Buffer controlled_buffer_180
  Gated_Latch gated_latch_180 (.Data_In(Data_In), .Write_Enable(and_548_out), .Data_Out(gated_latch_180_data_out));
  and and_564 (and_564_out, and_532_out, Read_Enable);
  assign Data_Out = and_565_out ? gated_latch_181_data_out : 1'bz;  // Controlled_Buffer controlled_buffer_181
  Gated_Latch gated_latch_181 (.Data_In(Data_In), .Write_Enable(and_549_out), .Data_Out(gated_latch_181_data_out));
  and and_565 (and_565_out, and_533_out, Read_Enable);
  assign Data_Out = and_566_out ? gated_latch_182_data_out : 1'bz;  // Controlled_Buffer controlled_buffer_182
  Gated_Latch gated_latch_182 (.Data_In(Data_In), .Write_Enable(and_550_out), .Data_Out(gated_latch_182_data_out));
  and and_566 (and_566_out, and_534_out, Read_Enable);
  assign Data_Out = and_567_out ? gated_latch_183_data_out : 1'bz;  // Controlled_Buffer controlled_buffer_183
  Gated_Latch gated_latch_183 (.Data_In(Data_In), .Write_Enable(and_551_out), .Data_Out(gated_latch_183_data_out));
  and and_567 (and_567_out, and_535_out, Read_Enable);
  assign Data_Out = and_568_out ? gated_latch_184_data_out : 1'bz;  // Controlled_Buffer controlled_buffer_184
  Gated_Latch gated_latch_184 (.Data_In(Data_In), .Write_Enable(and_552_out), .Data_Out(gated_latch_184_data_out));
  and and_568 (and_568_out, and_536_out, Read_Enable);
  assign Data_Out = and_569_out ? gated_latch_185_data_out : 1'bz;  // Controlled_Buffer controlled_buffer_185
  Gated_Latch gated_latch_185 (.Data_In(Data_In), .Write_Enable(and_553_out), .Data_Out(gated_latch_185_data_out));
  and and_569 (and_569_out, and_537_out, Read_Enable);
  assign Data_Out = and_570_out ? gated_latch_186_data_out : 1'bz;  // Controlled_Buffer controlled_buffer_186
  Gated_Latch gated_latch_186 (.Data_In(Data_In), .Write_Enable(and_554_out), .Data_Out(gated_latch_186_data_out));
  and and_570 (and_570_out, and_538_out, Read_Enable);
  assign Data_Out = and_571_out ? gated_latch_187_data_out : 1'bz;  // Controlled_Buffer controlled_buffer_187
  Gated_Latch gated_latch_187 (.Data_In(Data_In), .Write_Enable(and_555_out), .Data_Out(gated_latch_187_data_out));
  and and_571 (and_571_out, and_539_out, Read_Enable);
  assign Data_Out = and_572_out ? gated_latch_188_data_out : 1'bz;  // Controlled_Buffer controlled_buffer_188
  Gated_Latch gated_latch_188 (.Data_In(Data_In), .Write_Enable(and_556_out), .Data_Out(gated_latch_188_data_out));
  and and_572 (and_572_out, and_540_out, Read_Enable);
  assign Data_Out = and_573_out ? gated_latch_189_data_out : 1'bz;  // Controlled_Buffer controlled_buffer_189
  Gated_Latch gated_latch_189 (.Data_In(Data_In), .Write_Enable(and_557_out), .Data_Out(gated_latch_189_data_out));
  and and_573 (and_573_out, and_541_out, Read_Enable);
  assign Data_Out = and_574_out ? gated_latch_190_data_out : 1'bz;  // Controlled_Buffer controlled_buffer_190
  Gated_Latch gated_latch_190 (.Data_In(Data_In), .Write_Enable(and_558_out), .Data_Out(gated_latch_190_data_out));
  and and_574 (and_574_out, and_542_out, Read_Enable);
  assign Data_Out = and_575_out ? gated_latch_191_data_out : 1'bz;  // Controlled_Buffer controlled_buffer_191
  Gated_Latch gated_latch_191 (.Data_In(Data_In), .Write_Enable(and_559_out), .Data_Out(gated_latch_191_data_out));
  and and_575 (and_575_out, and_543_out, Read_Enable);
  assign Data_Out = and_576_out ? gated_latch_192_data_out : 1'bz;  // Controlled_Buffer controlled_buffer_192
  Gated_Latch gated_latch_192 (.Data_In(Data_In), .Write_Enable(and_560_out), .Data_Out(gated_latch_192_data_out));
  and and_576 (and_576_out, and_544_out, Read_Enable);
  and and_577 (and_577_out, binary_decoder_4_to_16_2_1_out_8, binary_decoder_4_to_16_1_out_5);
  and and_578 (and_578_out, binary_decoder_4_to_16_2_1_out_8, binary_decoder_4_to_16_1_out_6);
  and and_579 (and_579_out, binary_decoder_4_to_16_2_1_out_8, binary_decoder_4_to_16_1_out_7);
  and and_580 (and_580_out, binary_decoder_4_to_16_2_1_out_8, binary_decoder_4_to_16_1_out_8);
  and and_581 (and_581_out, binary_decoder_4_to_16_2_1_out_8, binary_decoder_4_to_16_1_out_9);
  and and_582 (and_582_out, binary_decoder_4_to_16_2_1_out_8, binary_decoder_4_to_16_1_out_10);
  and and_583 (and_583_out, binary_decoder_4_to_16_2_1_out_8, binary_decoder_4_to_16_1_out_11);
  and and_584 (and_584_out, binary_decoder_4_to_16_2_1_out_8, binary_decoder_4_to_16_1_out_12);
  and and_585 (and_585_out, binary_decoder_4_to_16_2_1_out_8, binary_decoder_4_to_16_1_out_13);
  and and_586 (and_586_out, binary_decoder_4_to_16_2_1_out_8, binary_decoder_4_to_16_1_out_14);
  and and_587 (and_587_out, binary_decoder_4_to_16_2_1_out_8, binary_decoder_4_to_16_1_out_15);
  and and_588 (and_588_out, binary_decoder_4_to_16_2_1_out_8, binary_decoder_4_to_16_1_out_16);
  and and_589 (and_589_out, binary_decoder_4_to_16_2_1_out_8, binary_decoder_4_to_16_1_out_17);
  and and_590 (and_590_out, binary_decoder_4_to_16_2_1_out_8, binary_decoder_4_to_16_1_out_18);
  and and_591 (and_591_out, binary_decoder_4_to_16_2_1_out_8, binary_decoder_4_to_16_1_out_19);
  and and_592 (and_592_out, binary_decoder_4_to_16_2_1_out_8, binary_decoder_4_to_16_1_out_20);
  and and_593 (and_593_out, Write_Enable, and_577_out);
  and and_594 (and_594_out, Write_Enable, and_578_out);
  and and_595 (and_595_out, Write_Enable, and_579_out);
  and and_596 (and_596_out, Write_Enable, and_580_out);
  and and_597 (and_597_out, Write_Enable, and_581_out);
  and and_598 (and_598_out, Write_Enable, and_582_out);
  and and_599 (and_599_out, Write_Enable, and_583_out);
  and and_600 (and_600_out, Write_Enable, and_584_out);
  and and_601 (and_601_out, Write_Enable, and_585_out);
  and and_602 (and_602_out, Write_Enable, and_586_out);
  and and_603 (and_603_out, Write_Enable, and_587_out);
  and and_604 (and_604_out, Write_Enable, and_588_out);
  and and_605 (and_605_out, Write_Enable, and_589_out);
  and and_606 (and_606_out, Write_Enable, and_590_out);
  and and_607 (and_607_out, Write_Enable, and_591_out);
  and and_608 (and_608_out, Write_Enable, and_592_out);
  assign Data_Out = and_609_out ? gated_latch_193_data_out : 1'bz;  // Controlled_Buffer controlled_buffer_193
  Gated_Latch gated_latch_193 (.Data_In(Data_In), .Write_Enable(and_593_out), .Data_Out(gated_latch_193_data_out));
  and and_609 (and_609_out, and_577_out, Read_Enable);
  assign Data_Out = and_610_out ? gated_latch_194_data_out : 1'bz;  // Controlled_Buffer controlled_buffer_194
  Gated_Latch gated_latch_194 (.Data_In(Data_In), .Write_Enable(and_594_out), .Data_Out(gated_latch_194_data_out));
  and and_610 (and_610_out, and_578_out, Read_Enable);
  assign Data_Out = and_611_out ? gated_latch_195_data_out : 1'bz;  // Controlled_Buffer controlled_buffer_195
  Gated_Latch gated_latch_195 (.Data_In(Data_In), .Write_Enable(and_595_out), .Data_Out(gated_latch_195_data_out));
  and and_611 (and_611_out, and_579_out, Read_Enable);
  assign Data_Out = and_612_out ? gated_latch_196_data_out : 1'bz;  // Controlled_Buffer controlled_buffer_196
  Gated_Latch gated_latch_196 (.Data_In(Data_In), .Write_Enable(and_596_out), .Data_Out(gated_latch_196_data_out));
  and and_612 (and_612_out, and_580_out, Read_Enable);
  assign Data_Out = and_613_out ? gated_latch_197_data_out : 1'bz;  // Controlled_Buffer controlled_buffer_197
  Gated_Latch gated_latch_197 (.Data_In(Data_In), .Write_Enable(and_597_out), .Data_Out(gated_latch_197_data_out));
  and and_613 (and_613_out, and_581_out, Read_Enable);
  assign Data_Out = and_614_out ? gated_latch_198_data_out : 1'bz;  // Controlled_Buffer controlled_buffer_198
  Gated_Latch gated_latch_198 (.Data_In(Data_In), .Write_Enable(and_598_out), .Data_Out(gated_latch_198_data_out));
  and and_614 (and_614_out, and_582_out, Read_Enable);
  assign Data_Out = and_615_out ? gated_latch_199_data_out : 1'bz;  // Controlled_Buffer controlled_buffer_199
  Gated_Latch gated_latch_199 (.Data_In(Data_In), .Write_Enable(and_599_out), .Data_Out(gated_latch_199_data_out));
  and and_615 (and_615_out, and_583_out, Read_Enable);
  assign Data_Out = and_616_out ? gated_latch_200_data_out : 1'bz;  // Controlled_Buffer controlled_buffer_200
  Gated_Latch gated_latch_200 (.Data_In(Data_In), .Write_Enable(and_600_out), .Data_Out(gated_latch_200_data_out));
  and and_616 (and_616_out, and_584_out, Read_Enable);
  assign Data_Out = and_617_out ? gated_latch_201_data_out : 1'bz;  // Controlled_Buffer controlled_buffer_201
  Gated_Latch gated_latch_201 (.Data_In(Data_In), .Write_Enable(and_601_out), .Data_Out(gated_latch_201_data_out));
  and and_617 (and_617_out, and_585_out, Read_Enable);
  assign Data_Out = and_618_out ? gated_latch_202_data_out : 1'bz;  // Controlled_Buffer controlled_buffer_202
  Gated_Latch gated_latch_202 (.Data_In(Data_In), .Write_Enable(and_602_out), .Data_Out(gated_latch_202_data_out));
  and and_618 (and_618_out, and_586_out, Read_Enable);
  assign Data_Out = and_619_out ? gated_latch_203_data_out : 1'bz;  // Controlled_Buffer controlled_buffer_203
  Gated_Latch gated_latch_203 (.Data_In(Data_In), .Write_Enable(and_603_out), .Data_Out(gated_latch_203_data_out));
  and and_619 (and_619_out, and_587_out, Read_Enable);
  assign Data_Out = and_620_out ? gated_latch_204_data_out : 1'bz;  // Controlled_Buffer controlled_buffer_204
  Gated_Latch gated_latch_204 (.Data_In(Data_In), .Write_Enable(and_604_out), .Data_Out(gated_latch_204_data_out));
  and and_620 (and_620_out, and_588_out, Read_Enable);
  assign Data_Out = and_621_out ? gated_latch_205_data_out : 1'bz;  // Controlled_Buffer controlled_buffer_205
  Gated_Latch gated_latch_205 (.Data_In(Data_In), .Write_Enable(and_605_out), .Data_Out(gated_latch_205_data_out));
  and and_621 (and_621_out, and_589_out, Read_Enable);
  assign Data_Out = and_622_out ? gated_latch_206_data_out : 1'bz;  // Controlled_Buffer controlled_buffer_206
  Gated_Latch gated_latch_206 (.Data_In(Data_In), .Write_Enable(and_606_out), .Data_Out(gated_latch_206_data_out));
  and and_622 (and_622_out, and_590_out, Read_Enable);
  assign Data_Out = and_623_out ? gated_latch_207_data_out : 1'bz;  // Controlled_Buffer controlled_buffer_207
  Gated_Latch gated_latch_207 (.Data_In(Data_In), .Write_Enable(and_607_out), .Data_Out(gated_latch_207_data_out));
  and and_623 (and_623_out, and_591_out, Read_Enable);
  assign Data_Out = and_624_out ? gated_latch_208_data_out : 1'bz;  // Controlled_Buffer controlled_buffer_208
  Gated_Latch gated_latch_208 (.Data_In(Data_In), .Write_Enable(and_608_out), .Data_Out(gated_latch_208_data_out));
  and and_624 (and_624_out, and_592_out, Read_Enable);
  and and_625 (and_625_out, binary_decoder_4_to_16_2_1_out_7, binary_decoder_4_to_16_1_out_5);
  and and_626 (and_626_out, Write_Enable, and_625_out);
  and and_627 (and_627_out, binary_decoder_4_to_16_2_1_out_7, binary_decoder_4_to_16_1_out_6);
  and and_628 (and_628_out, Write_Enable, and_627_out);
  and and_629 (and_629_out, binary_decoder_4_to_16_2_1_out_7, binary_decoder_4_to_16_1_out_7);
  and and_630 (and_630_out, Write_Enable, and_629_out);
  and and_631 (and_631_out, binary_decoder_4_to_16_2_1_out_7, binary_decoder_4_to_16_1_out_8);
  and and_632 (and_632_out, Write_Enable, and_631_out);
  and and_633 (and_633_out, binary_decoder_4_to_16_2_1_out_7, binary_decoder_4_to_16_1_out_9);
  and and_634 (and_634_out, Write_Enable, and_633_out);
  and and_635 (and_635_out, binary_decoder_4_to_16_2_1_out_7, binary_decoder_4_to_16_1_out_10);
  and and_636 (and_636_out, Write_Enable, and_635_out);
  and and_637 (and_637_out, binary_decoder_4_to_16_2_1_out_7, binary_decoder_4_to_16_1_out_11);
  and and_638 (and_638_out, Write_Enable, and_637_out);
  and and_639 (and_639_out, binary_decoder_4_to_16_2_1_out_7, binary_decoder_4_to_16_1_out_12);
  and and_640 (and_640_out, Write_Enable, and_639_out);
  and and_641 (and_641_out, binary_decoder_4_to_16_2_1_out_7, binary_decoder_4_to_16_1_out_13);
  and and_642 (and_642_out, Write_Enable, and_641_out);
  and and_643 (and_643_out, binary_decoder_4_to_16_2_1_out_7, binary_decoder_4_to_16_1_out_14);
  and and_644 (and_644_out, Write_Enable, and_643_out);
  and and_645 (and_645_out, binary_decoder_4_to_16_2_1_out_7, binary_decoder_4_to_16_1_out_15);
  and and_646 (and_646_out, Write_Enable, and_645_out);
  and and_647 (and_647_out, binary_decoder_4_to_16_2_1_out_7, binary_decoder_4_to_16_1_out_16);
  and and_648 (and_648_out, Write_Enable, and_647_out);
  and and_649 (and_649_out, binary_decoder_4_to_16_2_1_out_7, binary_decoder_4_to_16_1_out_17);
  and and_650 (and_650_out, Write_Enable, and_649_out);
  and and_651 (and_651_out, binary_decoder_4_to_16_2_1_out_7, binary_decoder_4_to_16_1_out_18);
  and and_652 (and_652_out, Write_Enable, and_651_out);
  and and_653 (and_653_out, binary_decoder_4_to_16_2_1_out_7, binary_decoder_4_to_16_1_out_19);
  and and_654 (and_654_out, Write_Enable, and_653_out);
  and and_655 (and_655_out, binary_decoder_4_to_16_2_1_out_7, binary_decoder_4_to_16_1_out_20);
  and and_656 (and_656_out, Write_Enable, and_655_out);
  assign Data_Out = and_657_out ? gated_latch_209_data_out : 1'bz;  // Controlled_Buffer controlled_buffer_209
  Gated_Latch gated_latch_209 (.Data_In(Data_In), .Write_Enable(and_626_out), .Data_Out(gated_latch_209_data_out));
  and and_657 (and_657_out, and_625_out, Read_Enable);
  assign Data_Out = and_658_out ? gated_latch_210_data_out : 1'bz;  // Controlled_Buffer controlled_buffer_210
  Gated_Latch gated_latch_210 (.Data_In(Data_In), .Write_Enable(and_628_out), .Data_Out(gated_latch_210_data_out));
  and and_658 (and_658_out, and_627_out, Read_Enable);
  assign Data_Out = and_659_out ? gated_latch_211_data_out : 1'bz;  // Controlled_Buffer controlled_buffer_211
  Gated_Latch gated_latch_211 (.Data_In(Data_In), .Write_Enable(and_630_out), .Data_Out(gated_latch_211_data_out));
  and and_659 (and_659_out, and_629_out, Read_Enable);
  assign Data_Out = and_660_out ? gated_latch_212_data_out : 1'bz;  // Controlled_Buffer controlled_buffer_212
  Gated_Latch gated_latch_212 (.Data_In(Data_In), .Write_Enable(and_632_out), .Data_Out(gated_latch_212_data_out));
  and and_660 (and_660_out, and_631_out, Read_Enable);
  assign Data_Out = and_661_out ? gated_latch_213_data_out : 1'bz;  // Controlled_Buffer controlled_buffer_213
  Gated_Latch gated_latch_213 (.Data_In(Data_In), .Write_Enable(and_634_out), .Data_Out(gated_latch_213_data_out));
  and and_661 (and_661_out, and_633_out, Read_Enable);
  assign Data_Out = and_662_out ? gated_latch_214_data_out : 1'bz;  // Controlled_Buffer controlled_buffer_214
  Gated_Latch gated_latch_214 (.Data_In(Data_In), .Write_Enable(and_636_out), .Data_Out(gated_latch_214_data_out));
  and and_662 (and_662_out, and_635_out, Read_Enable);
  assign Data_Out = and_663_out ? gated_latch_215_data_out : 1'bz;  // Controlled_Buffer controlled_buffer_215
  Gated_Latch gated_latch_215 (.Data_In(Data_In), .Write_Enable(and_638_out), .Data_Out(gated_latch_215_data_out));
  and and_663 (and_663_out, and_637_out, Read_Enable);
  assign Data_Out = and_664_out ? gated_latch_216_data_out : 1'bz;  // Controlled_Buffer controlled_buffer_216
  Gated_Latch gated_latch_216 (.Data_In(Data_In), .Write_Enable(and_640_out), .Data_Out(gated_latch_216_data_out));
  and and_664 (and_664_out, and_639_out, Read_Enable);
  assign Data_Out = and_665_out ? gated_latch_217_data_out : 1'bz;  // Controlled_Buffer controlled_buffer_217
  Gated_Latch gated_latch_217 (.Data_In(Data_In), .Write_Enable(and_642_out), .Data_Out(gated_latch_217_data_out));
  and and_665 (and_665_out, and_641_out, Read_Enable);
  assign Data_Out = and_666_out ? gated_latch_218_data_out : 1'bz;  // Controlled_Buffer controlled_buffer_218
  Gated_Latch gated_latch_218 (.Data_In(Data_In), .Write_Enable(and_644_out), .Data_Out(gated_latch_218_data_out));
  and and_666 (and_666_out, and_643_out, Read_Enable);
  assign Data_Out = and_667_out ? gated_latch_219_data_out : 1'bz;  // Controlled_Buffer controlled_buffer_219
  Gated_Latch gated_latch_219 (.Data_In(Data_In), .Write_Enable(and_646_out), .Data_Out(gated_latch_219_data_out));
  and and_667 (and_667_out, and_645_out, Read_Enable);
  assign Data_Out = and_668_out ? gated_latch_220_data_out : 1'bz;  // Controlled_Buffer controlled_buffer_220
  Gated_Latch gated_latch_220 (.Data_In(Data_In), .Write_Enable(and_648_out), .Data_Out(gated_latch_220_data_out));
  and and_668 (and_668_out, and_647_out, Read_Enable);
  assign Data_Out = and_669_out ? gated_latch_221_data_out : 1'bz;  // Controlled_Buffer controlled_buffer_221
  Gated_Latch gated_latch_221 (.Data_In(Data_In), .Write_Enable(and_650_out), .Data_Out(gated_latch_221_data_out));
  and and_669 (and_669_out, and_649_out, Read_Enable);
  assign Data_Out = and_670_out ? gated_latch_222_data_out : 1'bz;  // Controlled_Buffer controlled_buffer_222
  Gated_Latch gated_latch_222 (.Data_In(Data_In), .Write_Enable(and_652_out), .Data_Out(gated_latch_222_data_out));
  and and_670 (and_670_out, and_651_out, Read_Enable);
  assign Data_Out = and_671_out ? gated_latch_223_data_out : 1'bz;  // Controlled_Buffer controlled_buffer_223
  Gated_Latch gated_latch_223 (.Data_In(Data_In), .Write_Enable(and_654_out), .Data_Out(gated_latch_223_data_out));
  and and_671 (and_671_out, and_653_out, Read_Enable);
  assign Data_Out = and_672_out ? gated_latch_224_data_out : 1'bz;  // Controlled_Buffer controlled_buffer_224
  Gated_Latch gated_latch_224 (.Data_In(Data_In), .Write_Enable(and_656_out), .Data_Out(gated_latch_224_data_out));
  and and_672 (and_672_out, and_655_out, Read_Enable);
  and and_673 (and_673_out, binary_decoder_4_to_16_2_1_out_6, binary_decoder_4_to_16_1_out_5);
  and and_674 (and_674_out, Write_Enable, and_673_out);
  and and_675 (and_675_out, binary_decoder_4_to_16_2_1_out_6, binary_decoder_4_to_16_1_out_6);
  and and_676 (and_676_out, Write_Enable, and_675_out);
  and and_677 (and_677_out, binary_decoder_4_to_16_2_1_out_6, binary_decoder_4_to_16_1_out_7);
  and and_678 (and_678_out, Write_Enable, and_677_out);
  and and_679 (and_679_out, binary_decoder_4_to_16_2_1_out_6, binary_decoder_4_to_16_1_out_8);
  and and_680 (and_680_out, Write_Enable, and_679_out);
  and and_681 (and_681_out, binary_decoder_4_to_16_2_1_out_6, binary_decoder_4_to_16_1_out_9);
  and and_682 (and_682_out, Write_Enable, and_681_out);
  and and_683 (and_683_out, binary_decoder_4_to_16_2_1_out_6, binary_decoder_4_to_16_1_out_10);
  and and_684 (and_684_out, Write_Enable, and_683_out);
  and and_685 (and_685_out, binary_decoder_4_to_16_2_1_out_6, binary_decoder_4_to_16_1_out_11);
  and and_686 (and_686_out, Write_Enable, and_685_out);
  and and_687 (and_687_out, binary_decoder_4_to_16_2_1_out_6, binary_decoder_4_to_16_1_out_12);
  and and_688 (and_688_out, Write_Enable, and_687_out);
  and and_689 (and_689_out, binary_decoder_4_to_16_2_1_out_6, binary_decoder_4_to_16_1_out_13);
  and and_690 (and_690_out, Write_Enable, and_689_out);
  and and_691 (and_691_out, binary_decoder_4_to_16_2_1_out_6, binary_decoder_4_to_16_1_out_14);
  and and_692 (and_692_out, Write_Enable, and_691_out);
  and and_693 (and_693_out, binary_decoder_4_to_16_2_1_out_6, binary_decoder_4_to_16_1_out_15);
  and and_694 (and_694_out, Write_Enable, and_693_out);
  and and_695 (and_695_out, binary_decoder_4_to_16_2_1_out_6, binary_decoder_4_to_16_1_out_16);
  and and_696 (and_696_out, Write_Enable, and_695_out);
  and and_697 (and_697_out, binary_decoder_4_to_16_2_1_out_6, binary_decoder_4_to_16_1_out_17);
  and and_698 (and_698_out, Write_Enable, and_697_out);
  and and_699 (and_699_out, binary_decoder_4_to_16_2_1_out_6, binary_decoder_4_to_16_1_out_18);
  and and_700 (and_700_out, Write_Enable, and_699_out);
  and and_701 (and_701_out, binary_decoder_4_to_16_2_1_out_6, binary_decoder_4_to_16_1_out_19);
  and and_702 (and_702_out, Write_Enable, and_701_out);
  and and_703 (and_703_out, binary_decoder_4_to_16_2_1_out_6, binary_decoder_4_to_16_1_out_20);
  and and_704 (and_704_out, Write_Enable, and_703_out);
  assign Data_Out = and_705_out ? gated_latch_225_data_out : 1'bz;  // Controlled_Buffer controlled_buffer_225
  Gated_Latch gated_latch_225 (.Data_In(Data_In), .Write_Enable(and_674_out), .Data_Out(gated_latch_225_data_out));
  and and_705 (and_705_out, and_673_out, Read_Enable);
  assign Data_Out = and_706_out ? gated_latch_226_data_out : 1'bz;  // Controlled_Buffer controlled_buffer_226
  Gated_Latch gated_latch_226 (.Data_In(Data_In), .Write_Enable(and_676_out), .Data_Out(gated_latch_226_data_out));
  and and_706 (and_706_out, and_675_out, Read_Enable);
  assign Data_Out = and_707_out ? gated_latch_227_data_out : 1'bz;  // Controlled_Buffer controlled_buffer_227
  Gated_Latch gated_latch_227 (.Data_In(Data_In), .Write_Enable(and_678_out), .Data_Out(gated_latch_227_data_out));
  and and_707 (and_707_out, and_677_out, Read_Enable);
  assign Data_Out = and_708_out ? gated_latch_228_data_out : 1'bz;  // Controlled_Buffer controlled_buffer_228
  Gated_Latch gated_latch_228 (.Data_In(Data_In), .Write_Enable(and_680_out), .Data_Out(gated_latch_228_data_out));
  and and_708 (and_708_out, and_679_out, Read_Enable);
  assign Data_Out = and_709_out ? gated_latch_229_data_out : 1'bz;  // Controlled_Buffer controlled_buffer_229
  Gated_Latch gated_latch_229 (.Data_In(Data_In), .Write_Enable(and_682_out), .Data_Out(gated_latch_229_data_out));
  and and_709 (and_709_out, and_681_out, Read_Enable);
  assign Data_Out = and_710_out ? gated_latch_230_data_out : 1'bz;  // Controlled_Buffer controlled_buffer_230
  Gated_Latch gated_latch_230 (.Data_In(Data_In), .Write_Enable(and_684_out), .Data_Out(gated_latch_230_data_out));
  and and_710 (and_710_out, and_683_out, Read_Enable);
  assign Data_Out = and_711_out ? gated_latch_231_data_out : 1'bz;  // Controlled_Buffer controlled_buffer_231
  Gated_Latch gated_latch_231 (.Data_In(Data_In), .Write_Enable(and_686_out), .Data_Out(gated_latch_231_data_out));
  and and_711 (and_711_out, and_685_out, Read_Enable);
  assign Data_Out = and_712_out ? gated_latch_232_data_out : 1'bz;  // Controlled_Buffer controlled_buffer_232
  Gated_Latch gated_latch_232 (.Data_In(Data_In), .Write_Enable(and_688_out), .Data_Out(gated_latch_232_data_out));
  and and_712 (and_712_out, and_687_out, Read_Enable);
  assign Data_Out = and_713_out ? gated_latch_233_data_out : 1'bz;  // Controlled_Buffer controlled_buffer_233
  Gated_Latch gated_latch_233 (.Data_In(Data_In), .Write_Enable(and_690_out), .Data_Out(gated_latch_233_data_out));
  and and_713 (and_713_out, and_689_out, Read_Enable);
  assign Data_Out = and_714_out ? gated_latch_234_data_out : 1'bz;  // Controlled_Buffer controlled_buffer_234
  Gated_Latch gated_latch_234 (.Data_In(Data_In), .Write_Enable(and_692_out), .Data_Out(gated_latch_234_data_out));
  and and_714 (and_714_out, and_691_out, Read_Enable);
  assign Data_Out = and_715_out ? gated_latch_235_data_out : 1'bz;  // Controlled_Buffer controlled_buffer_235
  Gated_Latch gated_latch_235 (.Data_In(Data_In), .Write_Enable(and_694_out), .Data_Out(gated_latch_235_data_out));
  and and_715 (and_715_out, and_693_out, Read_Enable);
  assign Data_Out = and_716_out ? gated_latch_236_data_out : 1'bz;  // Controlled_Buffer controlled_buffer_236
  Gated_Latch gated_latch_236 (.Data_In(Data_In), .Write_Enable(and_696_out), .Data_Out(gated_latch_236_data_out));
  and and_716 (and_716_out, and_695_out, Read_Enable);
  assign Data_Out = and_717_out ? gated_latch_237_data_out : 1'bz;  // Controlled_Buffer controlled_buffer_237
  Gated_Latch gated_latch_237 (.Data_In(Data_In), .Write_Enable(and_698_out), .Data_Out(gated_latch_237_data_out));
  and and_717 (and_717_out, and_697_out, Read_Enable);
  assign Data_Out = and_718_out ? gated_latch_238_data_out : 1'bz;  // Controlled_Buffer controlled_buffer_238
  Gated_Latch gated_latch_238 (.Data_In(Data_In), .Write_Enable(and_700_out), .Data_Out(gated_latch_238_data_out));
  and and_718 (and_718_out, and_699_out, Read_Enable);
  assign Data_Out = and_719_out ? gated_latch_239_data_out : 1'bz;  // Controlled_Buffer controlled_buffer_239
  Gated_Latch gated_latch_239 (.Data_In(Data_In), .Write_Enable(and_702_out), .Data_Out(gated_latch_239_data_out));
  and and_719 (and_719_out, and_701_out, Read_Enable);
  assign Data_Out = and_720_out ? gated_latch_240_data_out : 1'bz;  // Controlled_Buffer controlled_buffer_240
  Gated_Latch gated_latch_240 (.Data_In(Data_In), .Write_Enable(and_704_out), .Data_Out(gated_latch_240_data_out));
  and and_720 (and_720_out, and_703_out, Read_Enable);
  and and_721 (and_721_out, binary_decoder_4_to_16_2_1_out_5, binary_decoder_4_to_16_1_out_5);
  and and_722 (and_722_out, Write_Enable, and_721_out);
  and and_723 (and_723_out, binary_decoder_4_to_16_2_1_out_5, binary_decoder_4_to_16_1_out_6);
  and and_724 (and_724_out, Write_Enable, and_723_out);
  and and_725 (and_725_out, binary_decoder_4_to_16_2_1_out_5, binary_decoder_4_to_16_1_out_7);
  and and_726 (and_726_out, Write_Enable, and_725_out);
  and and_727 (and_727_out, binary_decoder_4_to_16_2_1_out_5, binary_decoder_4_to_16_1_out_8);
  and and_728 (and_728_out, Write_Enable, and_727_out);
  and and_729 (and_729_out, binary_decoder_4_to_16_2_1_out_5, binary_decoder_4_to_16_1_out_9);
  and and_730 (and_730_out, Write_Enable, and_729_out);
  and and_731 (and_731_out, binary_decoder_4_to_16_2_1_out_5, binary_decoder_4_to_16_1_out_10);
  and and_732 (and_732_out, Write_Enable, and_731_out);
  and and_733 (and_733_out, binary_decoder_4_to_16_2_1_out_5, binary_decoder_4_to_16_1_out_11);
  and and_734 (and_734_out, Write_Enable, and_733_out);
  and and_735 (and_735_out, binary_decoder_4_to_16_2_1_out_5, binary_decoder_4_to_16_1_out_12);
  and and_736 (and_736_out, Write_Enable, and_735_out);
  and and_737 (and_737_out, binary_decoder_4_to_16_2_1_out_5, binary_decoder_4_to_16_1_out_13);
  and and_738 (and_738_out, Write_Enable, and_737_out);
  and and_739 (and_739_out, binary_decoder_4_to_16_2_1_out_5, binary_decoder_4_to_16_1_out_14);
  and and_740 (and_740_out, Write_Enable, and_739_out);
  and and_741 (and_741_out, binary_decoder_4_to_16_2_1_out_5, binary_decoder_4_to_16_1_out_15);
  and and_742 (and_742_out, Write_Enable, and_741_out);
  and and_743 (and_743_out, binary_decoder_4_to_16_2_1_out_5, binary_decoder_4_to_16_1_out_16);
  and and_744 (and_744_out, Write_Enable, and_743_out);
  and and_745 (and_745_out, binary_decoder_4_to_16_2_1_out_5, binary_decoder_4_to_16_1_out_17);
  and and_746 (and_746_out, Write_Enable, and_745_out);
  and and_747 (and_747_out, binary_decoder_4_to_16_2_1_out_5, binary_decoder_4_to_16_1_out_18);
  and and_748 (and_748_out, Write_Enable, and_747_out);
  and and_749 (and_749_out, binary_decoder_4_to_16_2_1_out_5, binary_decoder_4_to_16_1_out_19);
  and and_750 (and_750_out, Write_Enable, and_749_out);
  and and_751 (and_751_out, binary_decoder_4_to_16_2_1_out_5, binary_decoder_4_to_16_1_out_20);
  and and_752 (and_752_out, Write_Enable, and_751_out);
  assign Data_Out = and_753_out ? gated_latch_241_data_out : 1'bz;  // Controlled_Buffer controlled_buffer_241
  Gated_Latch gated_latch_241 (.Data_In(Data_In), .Write_Enable(and_722_out), .Data_Out(gated_latch_241_data_out));
  and and_753 (and_753_out, and_721_out, Read_Enable);
  assign Data_Out = and_754_out ? gated_latch_242_data_out : 1'bz;  // Controlled_Buffer controlled_buffer_242
  Gated_Latch gated_latch_242 (.Data_In(Data_In), .Write_Enable(and_724_out), .Data_Out(gated_latch_242_data_out));
  and and_754 (and_754_out, and_723_out, Read_Enable);
  assign Data_Out = and_755_out ? gated_latch_243_data_out : 1'bz;  // Controlled_Buffer controlled_buffer_243
  Gated_Latch gated_latch_243 (.Data_In(Data_In), .Write_Enable(and_726_out), .Data_Out(gated_latch_243_data_out));
  and and_755 (and_755_out, and_725_out, Read_Enable);
  assign Data_Out = and_756_out ? gated_latch_244_data_out : 1'bz;  // Controlled_Buffer controlled_buffer_244
  Gated_Latch gated_latch_244 (.Data_In(Data_In), .Write_Enable(and_728_out), .Data_Out(gated_latch_244_data_out));
  and and_756 (and_756_out, and_727_out, Read_Enable);
  assign Data_Out = and_757_out ? gated_latch_245_data_out : 1'bz;  // Controlled_Buffer controlled_buffer_245
  Gated_Latch gated_latch_245 (.Data_In(Data_In), .Write_Enable(and_730_out), .Data_Out(gated_latch_245_data_out));
  and and_757 (and_757_out, and_729_out, Read_Enable);
  assign Data_Out = and_758_out ? gated_latch_246_data_out : 1'bz;  // Controlled_Buffer controlled_buffer_246
  Gated_Latch gated_latch_246 (.Data_In(Data_In), .Write_Enable(and_732_out), .Data_Out(gated_latch_246_data_out));
  and and_758 (and_758_out, and_731_out, Read_Enable);
  assign Data_Out = and_759_out ? gated_latch_247_data_out : 1'bz;  // Controlled_Buffer controlled_buffer_247
  Gated_Latch gated_latch_247 (.Data_In(Data_In), .Write_Enable(and_734_out), .Data_Out(gated_latch_247_data_out));
  and and_759 (and_759_out, and_733_out, Read_Enable);
  assign Data_Out = and_760_out ? gated_latch_248_data_out : 1'bz;  // Controlled_Buffer controlled_buffer_248
  Gated_Latch gated_latch_248 (.Data_In(Data_In), .Write_Enable(and_736_out), .Data_Out(gated_latch_248_data_out));
  and and_760 (and_760_out, and_735_out, Read_Enable);
  assign Data_Out = and_761_out ? gated_latch_249_data_out : 1'bz;  // Controlled_Buffer controlled_buffer_249
  Gated_Latch gated_latch_249 (.Data_In(Data_In), .Write_Enable(and_738_out), .Data_Out(gated_latch_249_data_out));
  and and_761 (and_761_out, and_737_out, Read_Enable);
  assign Data_Out = and_762_out ? gated_latch_250_data_out : 1'bz;  // Controlled_Buffer controlled_buffer_250
  Gated_Latch gated_latch_250 (.Data_In(Data_In), .Write_Enable(and_740_out), .Data_Out(gated_latch_250_data_out));
  and and_762 (and_762_out, and_739_out, Read_Enable);
  assign Data_Out = and_763_out ? gated_latch_251_data_out : 1'bz;  // Controlled_Buffer controlled_buffer_251
  Gated_Latch gated_latch_251 (.Data_In(Data_In), .Write_Enable(and_742_out), .Data_Out(gated_latch_251_data_out));
  and and_763 (and_763_out, and_741_out, Read_Enable);
  assign Data_Out = and_764_out ? gated_latch_252_data_out : 1'bz;  // Controlled_Buffer controlled_buffer_252
  Gated_Latch gated_latch_252 (.Data_In(Data_In), .Write_Enable(and_744_out), .Data_Out(gated_latch_252_data_out));
  and and_764 (and_764_out, and_743_out, Read_Enable);
  assign Data_Out = and_765_out ? gated_latch_253_data_out : 1'bz;  // Controlled_Buffer controlled_buffer_253
  Gated_Latch gated_latch_253 (.Data_In(Data_In), .Write_Enable(and_746_out), .Data_Out(gated_latch_253_data_out));
  and and_765 (and_765_out, and_745_out, Read_Enable);
  assign Data_Out = and_766_out ? gated_latch_254_data_out : 1'bz;  // Controlled_Buffer controlled_buffer_254
  Gated_Latch gated_latch_254 (.Data_In(Data_In), .Write_Enable(and_748_out), .Data_Out(gated_latch_254_data_out));
  and and_766 (and_766_out, and_747_out, Read_Enable);
  assign Data_Out = and_767_out ? gated_latch_255_data_out : 1'bz;  // Controlled_Buffer controlled_buffer_255
  Gated_Latch gated_latch_255 (.Data_In(Data_In), .Write_Enable(and_750_out), .Data_Out(gated_latch_255_data_out));
  and and_767 (and_767_out, and_749_out, Read_Enable);
  assign Data_Out = and_768_out ? gated_latch_256_data_out : 1'bz;  // Controlled_Buffer controlled_buffer_256
  Gated_Latch gated_latch_256 (.Data_In(Data_In), .Write_Enable(and_752_out), .Data_Out(gated_latch_256_data_out));
  and and_768 (and_768_out, and_751_out, Read_Enable);
endmodule

module Binary_Decoder_4_to_16_2 (
  input  in_1,
  input  in_2,
  input  in_3,
  input  in_4,
  output out_5,
  output out_6,
  output out_7,
  output out_8,
  output out_9,
  output out_10,
  output out_11,
  output out_12,
  output out_13,
  output out_14,
  output out_15,
  output out_16,
  output out_17,
  output out_18,
  output out_19,
  output out_20
);

  wire not_1_out, not_2_out, not_3_out, not_4_out;

  not not_1 (not_1_out, in_4);
  not not_2 (not_2_out, in_3);
  not not_3 (not_3_out, in_2);
  not not_4 (not_4_out, in_1);
  and and_1 (out_5, in_4, in_3, in_2, in_1);
  and and_2 (out_6, in_4, in_3, in_2, not_4_out);
  and and_3 (out_7, in_4, in_3, not_3_out, in_1);
  and and_4 (out_8, in_4, in_3, not_3_out, not_4_out);
  and and_5 (out_9, in_4, not_2_out, in_2, in_1);
  and and_6 (out_10, in_4, not_2_out, in_2, not_4_out);
  and and_7 (out_11, in_4, not_2_out, not_3_out, in_1);
  and and_8 (out_12, in_4, not_2_out, not_3_out, not_4_out);
  and and_9 (out_13, not_1_out, in_3, in_2, in_1);
  and and_10 (out_14, not_1_out, in_3, in_2, not_4_out);
  and and_11 (out_15, not_1_out, in_3, not_3_out, in_1);
  and and_12 (out_16, not_1_out, in_3, not_3_out, not_4_out);
  and and_13 (out_17, not_1_out, not_2_out, in_2, in_1);
  and and_14 (out_18, not_1_out, not_2_out, in_2, not_4_out);
  and and_15 (out_19, not_1_out, not_2_out, not_3_out, in_1);
  and and_16 (out_20, not_1_out, not_2_out, not_3_out, not_4_out);
endmodule

module Full_Adder (
  input  A,
  input  B,
  input  C_in,
  output S,
  output C_Out
);

  wire and_1_out, and_2_out, xor_1_out;

  xor xor_1 (xor_1_out, A, B);
  and and_1 (and_1_out, A, B);
  and and_2 (and_2_out, C_in, xor_1_out);
  xor xor_2 (S, xor_1_out, C_in);
  or or_1 (C_Out, and_2_out, and_1_out);
endmodule

module Full_Subtractor (
  input  A,
  input  B,
  input  B_in,
  output D,
  output B_Out
);

  wire and_1_out, and_2_out, not_1_out, not_2_out, xor_1_out;

  not not_1 (not_1_out, A);
  xor xor_1 (xor_1_out, A, B);
  and and_1 (and_1_out, not_1_out, B);
  and and_2 (and_2_out, B_in, not_2_out);
  not not_2 (not_2_out, xor_1_out);
  xor xor_2 (D, xor_1_out, B_in);
  or or_1 (B_Out, and_2_out, and_1_out);
endmodule

module Eight_Bit_Adder (
  input  A7,
  input  A6,
  input  A5,
  input  A4,
  input  A3,
  input  A2,
  input  A1,
  input  A0,
  input  B7,
  input  B6,
  input  B5,
  input  B4,
  input  B3,
  input  B2,
  input  B1,
  input  B0,
  output Carry_Out,
  output S7,
  output S6,
  output S5,
  output S4,
  output S3,
  output S2,
  output S1,
  output S0
);

  wire full_adder_2_c_out, full_adder_3_c_out, full_adder_4_c_out, full_adder_5_c_out, full_adder_6_c_out,
       full_adder_7_c_out, full_adder_8_c_out;

  Full_Adder full_adder_1 (.A(A7), .B(B7), .C_in(full_adder_2_c_out), .S(S7), .C_Out(Carry_Out));
  Full_Adder full_adder_2 (.A(A6), .B(B6), .C_in(full_adder_3_c_out), .S(S6), .C_Out(full_adder_2_c_out));
  Full_Adder full_adder_3 (.A(A5), .B(B5), .C_in(full_adder_4_c_out), .S(S5), .C_Out(full_adder_3_c_out));
  Full_Adder full_adder_4 (.A(A4), .B(B4), .C_in(full_adder_5_c_out), .S(S4), .C_Out(full_adder_4_c_out));
  Full_Adder full_adder_5 (.A(A3), .B(B3), .C_in(full_adder_6_c_out), .S(S3), .C_Out(full_adder_5_c_out));
  Full_Adder full_adder_6 (.A(A2), .B(B2), .C_in(full_adder_7_c_out), .S(S2), .C_Out(full_adder_6_c_out));
  Full_Adder full_adder_7 (.A(A1), .B(B1), .C_in(full_adder_8_c_out), .S(S1), .C_Out(full_adder_7_c_out));
  Full_Adder full_adder_8 (.A(A0), .B(B0), .C_in(1'b0), .S(S0), .C_Out(full_adder_8_c_out));
endmodule

module Eight_Bit_Subtractor (
  input  A7,
  input  A6,
  input  A5,
  input  A4,
  input  A3,
  input  A2,
  input  A1,
  input  A0,
  input  B7,
  input  B6,
  input  B5,
  input  B4,
  input  B3,
  input  B2,
  input  B1,
  input  B0,
  output Borrow_Out,
  output D7,
  output D6,
  output D5,
  output D4,
  output D3,
  output D2,
  output D1,
  output D0
);

  wire full_subtractor_2_b_out, full_subtractor_3_b_out, full_subtractor_4_b_out, full_subtractor_5_b_out,
       full_subtractor_6_b_out, full_subtractor_7_b_out, full_subtractor_8_b_out;

  Full_Subtractor full_subtractor_1 (.A(A7), .B(B7), .B_in(full_subtractor_2_b_out), .D(D7), .B_Out(Borrow_Out));
  Full_Subtractor full_subtractor_2 (
    .A(A6), .B(B6), .B_in(full_subtractor_3_b_out), .D(D6), .B_Out(full_subtractor_2_b_out));
  Full_Subtractor full_subtractor_3 (
    .A(A5), .B(B5), .B_in(full_subtractor_4_b_out), .D(D5), .B_Out(full_subtractor_3_b_out));
  Full_Subtractor full_subtractor_4 (
    .A(A4), .B(B4), .B_in(full_subtractor_5_b_out), .D(D4), .B_Out(full_subtractor_4_b_out));
  Full_Subtractor full_subtractor_5 (
    .A(A3), .B(B3), .B_in(full_subtractor_6_b_out), .D(D3), .B_Out(full_subtractor_5_b_out));
  Full_Subtractor full_subtractor_6 (
    .A(A2), .B(B2), .B_in(full_subtractor_7_b_out), .D(D2), .B_Out(full_subtractor_6_b_out));
  Full_Subtractor full_subtractor_7 (
    .A(A1), .B(B1), .B_in(full_subtractor_8_b_out), .D(D1), .B_Out(full_subtractor_7_b_out));
  Full_Subtractor full_subtractor_8 (.A(A0), .B(B0), .B_in(1'b0), .D(D0), .B_Out(full_subtractor_8_b_out));
endmodule

module ALU (
  input  O2,
  input  O1,
  input  O0,
  input  B7,
  input  B6,
  input  B5,
  input  B4,
  input  B3,
  input  B2,
  input  B1,
  input  B0,
  input  A7,
  input  A6,
  input  A5,
  input  A4,
  input  A3,
  input  A2,
  input  A1,
  input  A0,
  output Overflow,
  output R7,
  output R6,
  output R5,
  output R4,
  output R3,
  output R2,
  output R1,
  output R0
);

  wire and_1_out, and_2_out, and_3_out, and_4_out, and_5_out, and_6_out, and_7_out, and_8_out, and_9_out,
       and_10_out, and_11_out, and_12_out, and_13_out, and_14_out, and_15_out, and_16_out, and_17_out,
       and_18_out, and_19_out, and_20_out, and_21_out, and_22_out, and_23_out, and_24_out, and_25_out,
       and_26_out, and_27_out, and_28_out, and_29_out, and_30_out, and_31_out, and_32_out, and_33_out,
       and_34_out, and_35_out, and_36_out, binary_decoder_3_to_8_1_out_4, binary_decoder_3_to_8_1_out_5,
       binary_decoder_3_to_8_1_out_6, binary_decoder_3_to_8_1_out_7, eight_bit_adder_1_carry_out,
       eight_bit_adder_1_s0, eight_bit_adder_1_s1, eight_bit_adder_1_s2, eight_bit_adder_1_s3,
       eight_bit_adder_1_s4, eight_bit_adder_1_s5, eight_bit_adder_1_s6, eight_bit_adder_1_s7,
       eight_bit_decrementor_1_borrow_out, eight_bit_decrementor_1_d0, eight_bit_decrementor_1_d1,
       eight_bit_decrementor_1_d2, eight_bit_decrementor_1_d3, eight_bit_decrementor_1_d4,
       eight_bit_decrementor_1_d5, eight_bit_decrementor_1_d6, eight_bit_decrementor_1_d7,
       eight_bit_incrementor_1_carry_out, eight_bit_incrementor_1_s0, eight_bit_incrementor_1_s1,
       eight_bit_incrementor_1_s2, eight_bit_incrementor_1_s3, eight_bit_incrementor_1_s4,
       eight_bit_incrementor_1_s5, eight_bit_incrementor_1_s6, eight_bit_incrementor_1_s7,
       eight_bit_subtractor_1_borrow_out, eight_bit_subtractor_1_d0, eight_bit_subtractor_1_d1,
       eight_bit_subtractor_1_d2, eight_bit_subtractor_1_d3, eight_bit_subtractor_1_d4,
       eight_bit_subtractor_1_d5, eight_bit_subtractor_1_d6, eight_bit_subtractor_1_d7;

  Eight_Bit_Adder eight_bit_adder_1 (
    .A4(A4), .A3(A3), .A2(A2), .A1(A1), .A0(A0), .A7(A7), .A6(A6), .B7(B7), .B6(B6), .B5(B5), .A5(A5),
    .B4(B4), .B3(B3), .B2(B2), .B1(B1), .B0(B0), .S0(eight_bit_adder_1_s0), .S7(eight_bit_adder_1_s7),
    .S6(eight_bit_adder_1_s6), .S5(eight_bit_adder_1_s5), .S4(eight_bit_adder_1_s4),
    .S3(eight_bit_adder_1_s3), .S2(eight_bit_adder_1_s2), .Carry_Out(eight_bit_adder_1_carry_out),
    .S1(eight_bit_adder_1_s1));
  Eight_Bit_Subtractor eight_bit_subtractor_1 (
    .A7(A7), .A6(A6), .A5(A5), .A4(A4), .A3(A3), .A2(A2), .A1(A1), .A0(A0), .B7(B7), .B6(B6), .B5(B5),
    .B4(B4), .B3(B3), .B2(B2), .B1(B1), .B0(B0), .D2(eight_bit_subtractor_1_d2),
    .D1(eight_bit_subtractor_1_d1), .D0(eight_bit_subtractor_1_d0),
    .Borrow_Out(eight_bit_subtractor_1_borrow_out), .D7(eight_bit_subtractor_1_d7),
    .D6(eight_bit_subtractor_1_d6), .D5(eight_bit_subtractor_1_d5), .D4(eight_bit_subtractor_1_d4),
    .D3(eight_bit_subtractor_1_d3));
  Eight_Bit_Incrementor eight_bit_incrementor_1 (
    .A5(A5), .A4(A4), .A3(A3), .A2(A2), .A1(A1), .A0(A0), .A7(A7), .A6(A6),
    .Carry_Out(eight_bit_incrementor_1_carry_out), .S0(eight_bit_incrementor_1_s0),
    .S7(eight_bit_incrementor_1_s7), .S6(eight_bit_incrementor_1_s6), .S5(eight_bit_incrementor_1_s5),
    .S4(eight_bit_incrementor_1_s4), .S3(eight_bit_incrementor_1_s3), .S2(eight_bit_incrementor_1_s2),
    .S1(eight_bit_incrementor_1_s1));
  Eight_Bit_Decrementor eight_bit_decrementor_1 (
    .A7(A7), .A6(A6), .A5(A5), .A4(A4), .A3(A3), .A2(A2), .A1(A1), .A0(A0), .D0(eight_bit_decrementor_1_d0),
    .Borrow_Out(eight_bit_decrementor_1_borrow_out), .D7(eight_bit_decrementor_1_d7),
    .D6(eight_bit_decrementor_1_d6), .D5(eight_bit_decrementor_1_d5), .D4(eight_bit_decrementor_1_d4),
    .D3(eight_bit_decrementor_1_d3), .D2(eight_bit_decrementor_1_d2), .D1(eight_bit_decrementor_1_d1));
  and and_1 (and_1_out, binary_decoder_3_to_8_1_out_4, eight_bit_adder_1_carry_out);
  and and_2 (and_2_out, binary_decoder_3_to_8_1_out_4, eight_bit_adder_1_s7);
  and and_3 (and_3_out, binary_decoder_3_to_8_1_out_4, eight_bit_adder_1_s6);
  and and_4 (and_4_out, binary_decoder_3_to_8_1_out_4, eight_bit_adder_1_s5);
  and and_5 (and_5_out, binary_decoder_3_to_8_1_out_4, eight_bit_adder_1_s4);
  and and_6 (and_6_out, binary_decoder_3_to_8_1_out_4, eight_bit_adder_1_s3);
  and and_7 (and_7_out, binary_decoder_3_to_8_1_out_4, eight_bit_adder_1_s2);
  and and_8 (and_8_out, binary_decoder_3_to_8_1_out_4, eight_bit_adder_1_s1);
  and and_9 (and_9_out, binary_decoder_3_to_8_1_out_4, eight_bit_adder_1_s0);
  and and_10 (and_10_out, binary_decoder_3_to_8_1_out_5, eight_bit_subtractor_1_borrow_out);
  and and_11 (and_11_out, binary_decoder_3_to_8_1_out_5, eight_bit_subtractor_1_d7);
  and and_12 (and_12_out, binary_decoder_3_to_8_1_out_5, eight_bit_subtractor_1_d6);
  and and_13 (and_13_out, binary_decoder_3_to_8_1_out_5, eight_bit_subtractor_1_d5);
  and and_14 (and_14_out, binary_decoder_3_to_8_1_out_5, eight_bit_subtractor_1_d4);
  and and_15 (and_15_out, binary_decoder_3_to_8_1_out_5, eight_bit_subtractor_1_d3);
  and and_16 (and_16_out, binary_decoder_3_to_8_1_out_5, eight_bit_subtractor_1_d2);
  and and_17 (and_17_out, binary_decoder_3_to_8_1_out_5, eight_bit_subtractor_1_d1);
  and and_18 (and_18_out, binary_decoder_3_to_8_1_out_5, eight_bit_subtractor_1_d0);
  and and_19 (and_19_out, binary_decoder_3_to_8_1_out_6, eight_bit_incrementor_1_carry_out);
  and and_20 (and_20_out, binary_decoder_3_to_8_1_out_6, eight_bit_incrementor_1_s7);
  and and_21 (and_21_out, binary_decoder_3_to_8_1_out_6, eight_bit_incrementor_1_s6);
  and and_22 (and_22_out, binary_decoder_3_to_8_1_out_6, eight_bit_incrementor_1_s5);
  and and_23 (and_23_out, binary_decoder_3_to_8_1_out_6, eight_bit_incrementor_1_s4);
  and and_24 (and_24_out, binary_decoder_3_to_8_1_out_6, eight_bit_incrementor_1_s3);
  and and_25 (and_25_out, binary_decoder_3_to_8_1_out_6, eight_bit_incrementor_1_s2);
  and and_26 (and_26_out, binary_decoder_3_to_8_1_out_6, eight_bit_incrementor_1_s1);
  and and_27 (and_27_out, binary_decoder_3_to_8_1_out_6, eight_bit_incrementor_1_s0);
  and and_28 (and_28_out, binary_decoder_3_to_8_1_out_7, eight_bit_decrementor_1_borrow_out);
  and and_29 (and_29_out, binary_decoder_3_to_8_1_out_7, eight_bit_decrementor_1_d7);
  and and_30 (and_30_out, binary_decoder_3_to_8_1_out_7, eight_bit_decrementor_1_d6);
  and and_31 (and_31_out, binary_decoder_3_to_8_1_out_7, eight_bit_decrementor_1_d5);
  and and_32 (and_32_out, binary_decoder_3_to_8_1_out_7, eight_bit_decrementor_1_d4);
  and and_33 (and_33_out, binary_decoder_3_to_8_1_out_7, eight_bit_decrementor_1_d3);
  and and_34 (and_34_out, binary_decoder_3_to_8_1_out_7, eight_bit_decrementor_1_d2);
  and and_35 (and_35_out, binary_decoder_3_to_8_1_out_7, eight_bit_decrementor_1_d1);
  and and_36 (and_36_out, binary_decoder_3_to_8_1_out_7, eight_bit_decrementor_1_d0);
  Binary_Decoder_3_to_8 binary_decoder_3_to_8_1 (
    .in_1(O0), .in_2(O1), .in_3(O2), .out_4(binary_decoder_3_to_8_1_out_4),
    .out_5(binary_decoder_3_to_8_1_out_5), .out_6(binary_decoder_3_to_8_1_out_6),
    .out_7(binary_decoder_3_to_8_1_out_7));  // open: out_8, out_9, out_10, out_11
  or or_1 (Overflow, and_1_out, and_10_out, and_19_out, and_28_out);
  or or_2 (R7, and_2_out, and_11_out, and_20_out, and_29_out);
  or or_3 (R6, and_3_out, and_12_out, and_21_out, and_30_out);
  or or_4 (R5, and_4_out, and_13_out, and_22_out, and_31_out);
  or or_5 (R4, and_5_out, and_14_out, and_23_out, and_32_out);
  or or_6 (R3, and_6_out, and_15_out, and_24_out, and_33_out);
  or or_7 (R2, and_7_out, and_16_out, and_25_out, and_34_out);
  or or_8 (R1, and_8_out, and_17_out, and_26_out, and_35_out);
  or or_9 (R0, and_9_out, and_18_out, and_27_out, and_36_out);
endmodule

module Eight_Bit_Decrementor (
  input  A7,
  input  A6,
  input  A5,
  input  A4,
  input  A3,
  input  A2,
  input  A1,
  input  A0,
  output Borrow_Out,
  output D7,
  output D6,
  output D5,
  output D4,
  output D3,
  output D2,
  output D1,
  output D0
);

  wire full_subtractor_2_b_out, full_subtractor_3_b_out, full_subtractor_4_b_out, full_subtractor_5_b_out,
       full_subtractor_6_b_out, full_subtractor_7_b_out, full_subtractor_8_b_out;

  Full_Subtractor full_subtractor_1 (.A(A7), .B(1'b0), .B_in(full_subtractor_2_b_out), .D(D7), .B_Out(Borrow_Out));
  Full_Subtractor full_subtractor_2 (
    .A(A6), .B(1'b0), .B_in(full_subtractor_3_b_out), .D(D6), .B_Out(full_subtractor_2_b_out));
  Full_Subtractor full_subtractor_3 (
    .A(A5), .B(1'b0), .B_in(full_subtractor_4_b_out), .D(D5), .B_Out(full_subtractor_3_b_out));
  Full_Subtractor full_subtractor_4 (
    .A(A4), .B(1'b0), .B_in(full_subtractor_5_b_out), .D(D4), .B_Out(full_subtractor_4_b_out));
  Full_Subtractor full_subtractor_5 (
    .A(A3), .B(1'b0), .B_in(full_subtractor_6_b_out), .D(D3), .B_Out(full_subtractor_5_b_out));
  Full_Subtractor full_subtractor_6 (
    .A(A2), .B(1'b0), .B_in(full_subtractor_7_b_out), .D(D2), .B_Out(full_subtractor_6_b_out));
  Full_Subtractor full_subtractor_7 (
    .A(A1), .B(1'b0), .B_in(full_subtractor_8_b_out), .D(D1), .B_Out(full_subtractor_7_b_out));
  Full_Subtractor full_subtractor_8 (.A(A0), .B(1'b1), .B_in(1'b0), .D(D0), .B_Out(full_subtractor_8_b_out));
endmodule

module Eight_Bit_Incrementor (
  input  A7,
  input  A6,
  input  A5,
  input  A4,
  input  A3,
  input  A2,
  input  A1,
  input  A0,
  output Carry_Out,
  output S7,
  output S6,
  output S5,
  output S4,
  output S3,
  output S2,
  output S1,
  output S0
);

  wire full_adder_2_c_out, full_adder_3_c_out, full_adder_4_c_out, full_adder_5_c_out, full_adder_6_c_out,
       full_adder_7_c_out, full_adder_8_c_out;

  Full_Adder full_adder_1 (.A(A7), .B(1'b0), .C_in(full_adder_2_c_out), .S(S7), .C_Out(Carry_Out));
  Full_Adder full_adder_2 (.A(A6), .B(1'b0), .C_in(full_adder_3_c_out), .S(S6), .C_Out(full_adder_2_c_out));
  Full_Adder full_adder_3 (.A(A5), .B(1'b0), .C_in(full_adder_4_c_out), .S(S5), .C_Out(full_adder_3_c_out));
  Full_Adder full_adder_4 (.A(A4), .B(1'b0), .C_in(full_adder_5_c_out), .S(S4), .C_Out(full_adder_4_c_out));
  Full_Adder full_adder_5 (.A(A3), .B(1'b0), .C_in(full_adder_6_c_out), .S(S3), .C_Out(full_adder_5_c_out));
  Full_Adder full_adder_6 (.A(A2), .B(1'b0), .C_in(full_adder_7_c_out), .S(S2), .C_Out(full_adder_6_c_out));
  Full_Adder full_adder_7 (.A(A1), .B(1'b0), .C_in(full_adder_8_c_out), .S(S1), .C_Out(full_adder_7_c_out));
  Full_Adder full_adder_8 (.A(A0), .B(1'b1), .C_in(1'b0), .S(S0), .C_Out(full_adder_8_c_out));
endmodule

module Binary_Decoder_3_to_8 (
  input  in_1,
  input  in_2,
  input  in_3,
  output out_4,
  output out_5,
  output out_6,
  output out_7,
  output out_8,
  output out_9,
  output out_10,
  output out_11
);

  wire not_1_out, not_2_out, not_3_out;

  not not_1 (not_1_out, in_3);
  not not_2 (not_2_out, in_2);
  not not_3 (not_3_out, in_1);
  and and_1 (out_4, not_1_out, not_2_out, not_3_out);
  and and_2 (out_5, not_1_out, not_2_out, in_1);
  and and_3 (out_6, not_1_out, in_2, not_3_out);
  and and_4 (out_7, not_1_out, in_2, in_1);
  and and_5 (out_8, in_3, not_2_out, not_3_out);
  and and_6 (out_9, in_3, not_2_out, in_1);
  and and_7 (out_10, in_3, in_2, not_3_out);
  and and_8 (out_11, in_3, in_2, in_1);
endmodule

module Eight_Bit_Register (
  input  Write_Enable,
  input  Read_Enable,
  input  DI0,
  input  DI1,
  input  DI2,
  input  DI3,
  input  DI4,
  input  DI5,
  input  DI6,
  input  DI7,
  output DO0,
  output DO1,
  output DO2,
  output DO3,
  output DO4,
  output DO5,
  output DO6,
  output DO7
);

  wire gated_latch_1_data_out, gated_latch_2_data_out, gated_latch_3_data_out, gated_latch_4_data_out,
       gated_latch_5_data_out, gated_latch_6_data_out, gated_latch_7_data_out, gated_latch_8_data_out;

  Gated_Latch gated_latch_1 (.Data_In(DI0), .Write_Enable(Write_Enable), .Data_Out(gated_latch_1_data_out));
  Gated_Latch gated_latch_2 (.Data_In(DI1), .Write_Enable(Write_Enable), .Data_Out(gated_latch_2_data_out));
  Gated_Latch gated_latch_3 (.Data_In(DI2), .Write_Enable(Write_Enable), .Data_Out(gated_latch_3_data_out));
  Gated_Latch gated_latch_4 (.Data_In(DI3), .Write_Enable(Write_Enable), .Data_Out(gated_latch_4_data_out));
  Gated_Latch gated_latch_5 (.Data_In(DI4), .Write_Enable(Write_Enable), .Data_Out(gated_latch_5_data_out));
  Gated_Latch gated_latch_6 (.Data_In(DI5), .Write_Enable(Write_Enable), .Data_Out(gated_latch_6_data_out));
  Gated_Latch gated_latch_7 (.Data_In(DI6), .Write_Enable(Write_Enable), .Data_Out(gated_latch_7_data_out));
  Gated_Latch gated_latch_8 (.Data_In(DI7), .Write_Enable(Write_Enable), .Data_Out(gated_latch_8_data_out));
  and and_1 (DO0, gated_latch_1_data_out, Read_Enable);
  and and_2 (DO1, gated_latch_2_data_out, Read_Enable);
  and and_3 (DO2, gated_latch_3_data_out, Read_Enable);
  and and_4 (DO3, gated_latch_4_data_out, Read_Enable);
  and and_5 (DO4, gated_latch_5_data_out, Read_Enable);
  and and_6 (DO5, gated_latch_6_data_out, Read_Enable);
  and and_7 (DO6, gated_latch_7_data_out, Read_Enable);
  and and_8 (DO7, gated_latch_8_data_out, Read_Enable);
endmodule

module Eight_Bit_to_BCD (
  input  B7,
  input  B6,
  input  B5,
  input  B4,
  input  B3,
  input  B2,
  input  B1,
  input  B0,
  output H1,
  output H0,
  output T3,
  output T2,
  output T1,
  output T0,
  output O3,
  output O2,
  output O1,
  output O0
);

  wire and_1_out, and_2_out, and_3_out, and_4_out, and_5_out, and_6_out, and_7_out, and_8_out, and_9_out,
       and_10_out, and_11_out, and_12_out, and_13_out, and_14_out, and_15_out, and_16_out, and_17_out,
       and_18_out, and_19_out, and_20_out, and_21_out, and_22_out, and_23_out, and_24_out, and_25_out,
       and_26_out, and_27_out, and_28_out, and_29_out, and_30_out, and_31_out, and_32_out, and_33_out,
       and_34_out, and_35_out, and_36_out, and_37_out, and_38_out, and_39_out, and_40_out, and_41_out,
       and_42_out, and_43_out, and_44_out, and_45_out, and_46_out, and_47_out, and_48_out, and_49_out,
       and_50_out, and_51_out, and_52_out, and_53_out, and_54_out, and_55_out, and_56_out, and_57_out,
       and_58_out, and_59_out, and_60_out, and_61_out, and_62_out, and_63_out, not_1_out, not_2_out,
       not_3_out, not_4_out, not_5_out, not_6_out, not_7_out, not_8_out, not_9_out, not_10_out, not_11_out,
       not_12_out, not_13_out, not_14_out, not_15_out, not_16_out, not_17_out, not_18_out, not_19_out,
       not_20_out, not_21_out, not_22_out, not_23_out, not_24_out, not_25_out, not_26_out, not_27_out,
       not_28_out, or_2_out, or_3_out, or_4_out, or_6_out, or_7_out, or_9_out, or_10_out, or_12_out,
       or_13_out, or_15_out, or_16_out, or_17_out, or_18_out, or_19_out, or_20_out, or_21_out, or_22_out,
       or_24_out, or_26_out;

  and and_1 (and_1_out, 1'b0, not_2_out, not_4_out, or_15_out);
  and and_2 (and_2_out, 1'b0, not_2_out, not_4_out, not_7_out);
  and and_3 (and_3_out, 1'b0, not_5_out, not_8_out, B5);
  or or_1 (H1, and_1_out, and_2_out, and_4_out, and_7_out, and_10_out);
  and and_4 (and_4_out, not_1_out, or_2_out, or_7_out, or_15_out);
  and and_5 (and_5_out, 1'b0, not_5_out, not_8_out, not_11_out);
  and and_6 (and_6_out, or_3_out, not_9_out, not_12_out, or_19_out);
  and and_7 (and_7_out, not_1_out, or_2_out, or_7_out, not_7_out);
  or or_2 (or_2_out, and_3_out, and_5_out, and_8_out, and_12_out, and_17_out);
  and and_8 (and_8_out, not_3_out, B7, B6, B5);
  and and_9 (and_9_out, or_3_out, not_9_out, not_12_out, not_15_out);
  or or_3 (or_3_out, and_1_out, and_14_out);
  and and_10 (and_10_out, not_1_out, or_2_out, not_4_out, or_15_out);
  not not_1 (not_1_out, 1'b0);
  not not_2 (not_2_out, or_2_out);
  and and_11 (and_11_out, or_4_out, not_13_out, not_14_out, B4);
  or or_4 (or_4_out, and_3_out, and_23_out);
  and and_12 (and_12_out, not_3_out, B7, B6, not_11_out);
  not not_3 (not_3_out, 1'b0);
  or or_5 (H0, and_6_out, and_9_out, and_13_out, and_18_out, and_19_out);
  and and_13 (and_13_out, not_6_out, or_6_out, or_9_out, or_19_out);
  or or_6 (or_6_out, and_2_out, and_4_out, and_20_out, and_25_out);
  and and_14 (and_14_out, not_1_out, or_2_out, not_4_out, not_7_out);
  not not_4 (not_4_out, or_7_out);
  or or_7 (or_7_out, and_11_out, and_15_out, and_16_out, and_22_out, and_27_out);
  and and_15 (and_15_out, or_4_out, not_13_out, not_14_out, not_17_out);
  and and_16 (and_16_out, not_10_out, or_10_out, or_13_out, B4);
  and and_17 (and_17_out, not_3_out, B7, not_8_out, B5);
  not not_5 (not_5_out, B7);
  or or_8 (T3, and_6_out, and_24_out);
  and and_18 (and_18_out, not_6_out, or_6_out, or_9_out, not_15_out);
  and and_19 (and_19_out, not_6_out, or_6_out, not_12_out, or_19_out);
  not not_6 (not_6_out, or_3_out);
  or or_9 (or_9_out, and_2_out, and_7_out, and_20_out, and_31_out);
  and and_20 (and_20_out, not_1_out, not_2_out, or_7_out, or_15_out);
  not not_7 (not_7_out, or_15_out);
  and and_21 (and_21_out, or_12_out, not_18_out, not_20_out, B3);
  and and_22 (and_22_out, not_10_out, or_10_out, or_13_out, not_17_out);
  or or_10 (or_10_out, and_5_out, and_8_out, and_28_out, and_29_out);
  and and_23 (and_23_out, not_3_out, B7, not_8_out, not_11_out);
  not not_8 (not_8_out, B6);
  or or_11 (T2, and_9_out, and_13_out, and_30_out, and_36_out);
  and and_24 (and_24_out, not_6_out, or_6_out, not_12_out, not_15_out);
  not not_9 (not_9_out, or_6_out);
  and and_25 (and_25_out, not_1_out, not_2_out, or_7_out, not_7_out);
  and and_26 (and_26_out, or_12_out, not_18_out, not_20_out, not_22_out);
  or or_12 (or_12_out, and_11_out, and_34_out);
  and and_27 (and_27_out, not_10_out, or_10_out, not_14_out, B4);
  not not_10 (not_10_out, or_4_out);
  or or_13 (or_13_out, and_5_out, and_12_out, and_28_out, and_35_out);
  and and_28 (and_28_out, not_3_out, not_5_out, B6, B5);
  and and_29 (and_29_out, not_3_out, not_5_out, B6, not_11_out);
  not not_11 (not_11_out, B5);
  or or_14 (T1, and_9_out, and_18_out, and_30_out, and_40_out);
  and and_30 (and_30_out, not_6_out, not_9_out, or_9_out, or_19_out);
  not not_12 (not_12_out, or_9_out);
  and and_31 (and_31_out, not_1_out, not_2_out, not_4_out, or_15_out);
  and and_32 (and_32_out, or_17_out, not_21_out, not_23_out, B2);
  or or_15 (or_15_out, and_21_out, and_26_out, and_33_out, and_38_out, and_42_out);
  and and_33 (and_33_out, not_16_out, or_16_out, or_18_out, B3);
  or or_16 (or_16_out, and_15_out, and_16_out, and_39_out, and_44_out);
  and and_34 (and_34_out, not_10_out, or_10_out, not_14_out, not_17_out);
  not not_13 (not_13_out, or_10_out);
  not not_14 (not_14_out, or_13_out);
  and and_35 (and_35_out, not_3_out, not_5_out, not_8_out, B5);
  and and_36 (and_36_out, not_6_out, not_9_out, or_9_out, not_15_out);
  not not_15 (not_15_out, or_19_out);
  and and_37 (and_37_out, or_17_out, not_21_out, not_23_out, not_25_out);
  or or_17 (or_17_out, and_21_out, and_43_out);
  and and_38 (and_38_out, not_16_out, or_16_out, or_18_out, not_22_out);
  not not_16 (not_16_out, or_12_out);
  or or_18 (or_18_out, and_15_out, and_22_out, and_39_out, and_48_out);
  and and_39 (and_39_out, not_10_out, not_13_out, or_13_out, B4);
  not not_17 (not_17_out, B4);
  and and_40 (and_40_out, not_6_out, not_9_out, not_12_out, or_19_out);
  or or_19 (or_19_out, and_32_out, and_37_out, and_41_out, and_46_out, and_50_out);
  and and_41 (and_41_out, not_19_out, or_20_out, or_22_out, B2);
  or or_20 (or_20_out, and_26_out, and_33_out, and_47_out, and_51_out);
  and and_42 (and_42_out, not_16_out, or_16_out, not_20_out, B3);
  and and_43 (and_43_out, not_16_out, or_16_out, not_20_out, not_22_out);
  not not_18 (not_18_out, or_16_out);
  and and_44 (and_44_out, not_10_out, not_13_out, or_13_out, not_17_out);
  and and_45 (and_45_out, or_21_out, not_26_out, not_27_out, B1);
  or or_21 (or_21_out, and_32_out, and_54_out);
  and and_46 (and_46_out, not_19_out, or_20_out, or_22_out, not_25_out);
  not not_19 (not_19_out, or_17_out);
  and and_47 (and_47_out, not_16_out, not_18_out, or_18_out, B3);
  not not_20 (not_20_out, or_18_out);
  and and_48 (and_48_out, not_10_out, not_13_out, not_14_out, B4);
  and and_49 (and_49_out, or_21_out, not_26_out, not_27_out, not_28_out);
  and and_50 (and_50_out, not_19_out, or_20_out, not_23_out, B2);
  not not_21 (not_21_out, or_20_out);
  or or_22 (or_22_out, and_26_out, and_38_out, and_47_out, and_55_out);
  and and_51 (and_51_out, not_16_out, not_18_out, or_18_out, not_22_out);
  not not_22 (not_22_out, B3);
  or or_23 (T0, and_45_out, and_49_out, and_52_out, and_53_out, and_56_out);
  and and_52 (and_52_out, not_24_out, or_24_out, or_26_out, B1);
  and and_53 (and_53_out, not_24_out, or_24_out, or_26_out, not_28_out);
  or or_24 (or_24_out, and_37_out, and_41_out, and_57_out, and_59_out);
  and and_54 (and_54_out, not_19_out, or_20_out, not_23_out, not_25_out);
  not not_23 (not_23_out, or_22_out);
  and and_55 (and_55_out, not_16_out, not_18_out, not_20_out, B3);
  or or_25 (O3, and_45_out, and_58_out);
  and and_56 (and_56_out, not_24_out, or_24_out, not_27_out, B1);
  not not_24 (not_24_out, or_21_out);
  or or_26 (or_26_out, and_37_out, and_46_out, and_57_out, and_60_out);
  and and_57 (and_57_out, not_19_out, not_21_out, or_22_out, B2);
  not not_25 (not_25_out, B2);
  or or_27 (O2, and_49_out, and_52_out, and_61_out, and_62_out);
  and and_58 (and_58_out, not_24_out, or_24_out, not_27_out, not_28_out);
  not not_26 (not_26_out, or_24_out);
  and and_59 (and_59_out, not_19_out, not_21_out, or_22_out, not_25_out);
  and and_60 (and_60_out, not_19_out, not_21_out, not_23_out, B2);
  or or_28 (O1, and_49_out, and_53_out, and_61_out, and_63_out);
  and and_61 (and_61_out, not_24_out, not_26_out, or_26_out, B1);
  not not_27 (not_27_out, or_26_out);
  not not_28 (not_28_out, B1);
  and and_62 (and_62_out, not_24_out, not_26_out, or_26_out, not_28_out);
  and and_63 (and_63_out, not_24_out, not_26_out, not_27_out, B1);

  assign O0 = B0;
endmodule

module BCD_To_Seven_Segment_Display (
  input  B3_A,
  input  B2_B,
  input  B1_C,
  input  B0_D,
  output g,
  output f,
  output e,
  output d,
  output c,
  output b,
  output a
);

  wire and_1_out, and_2_out, and_3_out, and_4_out, and_5_out, and_6_out, and_7_out, and_8_out, and_9_out,
       and_10_out, not_1_out, not_2_out, not_3_out, xnor_1_out, xnor_2_out, xor_1_out;

  and and_1 (and_1_out, B1_C, not_3_out);
  or or_1 (g, B3_A, and_1_out, xor_1_out);
  xor xor_1 (xor_1_out, B1_C, B2_B);
  or or_2 (f, B3_A, and_2_out, and_3_out, and_4_out);
  and and_2 (and_2_out, not_2_out, B2_B);
  and and_3 (and_3_out, not_2_out, not_3_out);
  and and_4 (and_4_out, B2_B, not_3_out);
  or or_3 (e, and_5_out, and_6_out);
  and and_5 (and_5_out, B1_C, not_3_out);
  and and_6 (and_6_out, not_1_out, not_3_out);
  and and_7 (and_7_out, B0_D, not_2_out, B2_B);
  and and_8 (and_8_out, B1_C, not_1_out);
  and and_9 (and_9_out, B1_C, not_3_out);
  and and_10 (and_10_out, not_3_out, not_1_out);
  or or_4 (d, and_7_out, and_8_out, and_9_out, and_10_out, B3_A);
  or or_5 (c, B2_B, B0_D, not_2_out);
  or or_6 (b, not_1_out, xnor_1_out);
  xnor xnor_1 (xnor_1_out, B1_C, B0_D);
  not not_1 (not_1_out, B2_B);
  not not_2 (not_2_out, B1_C);
  or or_7 (a, B3_A, B1_C, xnor_2_out);
  xnor xnor_2 (xnor_2_out, B2_B, B0_D);
  not not_3 (not_3_out, B0_D);
endmodule
